// Digital circuit CPU.dig as structural Verilog
module CPU (
);

  cpu_ram_256__dbg cpu_ram_256__dbg_1 ();  // open: address, sa, reset, e, s, i, o, reg, reg_2, reg_3, reg_4, reg_5, reg_6, reg_7, reg_8, reg_9, reg_10, reg_11, reg_12, reg_13, reg_14, reg_15, reg_16, reg_17, reg_18, reg_19, reg_20, reg_21, reg_22, reg_23, reg_24, reg_25, reg_26, reg_27, reg_28, reg_29, reg_30, reg_31, reg_32, reg_33, reg_34, reg_35, reg_36, reg_37, reg_38, reg_39, reg_40, reg_41, reg_42, reg_43, reg_44, reg_45, reg_46, reg_47, reg_48, reg_49, reg_50, reg_51, reg_52, reg_53, reg_54, reg_55, reg_56, reg_57, reg_58, reg_59, reg_60, reg_61, reg_62, reg_63, reg_64, reg_65, reg_66, reg_67, reg_68, reg_69, reg_70, reg_71, reg_72, reg_73, reg_74, reg_75, reg_76, reg_77, reg_78, reg_79, reg_80, reg_81, reg_82, reg_83, reg_84, reg_85, reg_86, reg_87, reg_88, reg_89, reg_90, reg_91, reg_92, reg_93, reg_94, reg_95, reg_96, reg_97, reg_98, reg_99, reg_100, reg_101, reg_102, reg_103, reg_104, reg_105, reg_106, reg_107, reg_108, reg_109, reg_110, reg_111, reg_112, reg_113, reg_114, reg_115, reg_116, reg_117, reg_118, reg_119, reg_120, reg_121, reg_122, reg_123, reg_124, reg_125, reg_126, reg_127, reg_128, reg_129, reg_130, reg_131, reg_132, reg_133, reg_134, reg_135, reg_136, reg_137, reg_138, reg_139, reg_140, reg_141, reg_142, reg_143, reg_144, reg_145, reg_146, reg_147, reg_148, reg_149, reg_150, reg_151, reg_152, reg_153, reg_154, reg_155, reg_156, reg_157, reg_158, reg_159, reg_160, reg_161, reg_162, reg_163, reg_164, reg_165, reg_166, reg_167, reg_168, reg_169, reg_170, reg_171, reg_172, reg_173, reg_174, reg_175, reg_176, reg_177, reg_178, reg_179, reg_180, reg_181, reg_182, reg_183, reg_184, reg_185, reg_186, reg_187, reg_188, reg_189, reg_190, reg_191, reg_192, reg_193, reg_194, reg_195, reg_196, reg_197, reg_198, reg_199, reg_200, reg_201, reg_202, reg_203, reg_204, reg_205, reg_206, reg_207, reg_208, reg_209, reg_210, reg_211, reg_212, reg_213, reg_214, reg_215, reg_216, reg_217, reg_218, reg_219, reg_220, reg_221, reg_222, reg_223, reg_224, reg_225, reg_226, reg_227, reg_228, reg_229, reg_230, reg_231, reg_232, reg_233, reg_234, reg_235, reg_236, reg_237, reg_238, reg_239, reg_240, reg_241, reg_242, reg_243, reg_244, reg_245, reg_246, reg_247, reg_248, reg_249, reg_250, reg_251, reg_252, reg_253, reg_254, reg_255, reg_256
endmodule
