// Digital circuit CPU_LEO.dig as structural Verilog
module CPU_LEO (
  input  [7:0] in_1,
  input  [7:0] in_2,
  input  in_3,
  input  in_4,
  input  in_5,
  input  in_6,
  input  in_7,
  output [7:0] out_8,
  output [7:0] out_9,
  output [7:0] out_10,
  output [7:0] out_11
);

  wire cpu_clk_1_p2, cpu_clk_1_p3, cpu_clk_1_p4, undriven_2, undriven_3, undriven_4;
  wire [7:0] undriven;

  cpu_temp cpu_temp_1 (.I(out_8), .S(undriven_2));  // open: O
  cpu_bus cpu_bus_1 (.Bus1(in_4), .\Ì (undriven));  // open: O
  cpu_alu cpu_alu_1 ();
  // cpu_clk cpu_clk_1: pin names not known; wires that end beside it: in_3, cpu_clk_1_p2, cpu_clk_1_p3, cpu_clk_1_p4
  cpu_reg_8 Reg_0 (.I(in_1), .E(1'b1));  // open: S, O
  cpu_reg_8 Reg_1 (.I(in_2), .E(1'b1));  // open: S, O
  Control control_1 ();
  cpu_reg_8 Reg_2 (.I(out_8), .E(undriven_3));  // open: S, O
  cpu_reg_8 Reg_3 (.I(out_8), .E(undriven_4));  // open: S, O
endmodule
