// Digital circuit Control.dig as structural Verilog
module Control (
  input  Clk_e,
  input  Clk_s,
  input  Clk,
  output R0_s,
  output R1_s,
  output R2_s,
  output R3_s,
  output Acc_s,
  output Temp_s,
  output Mar_s,
  output Ram_s,
  output R0_e,
  output R1_e,
  output R2_e,
  output R3_e,
  output Acc_e,
  output Ram_e
);

  wire undriven, undriven_2, undriven_3;

  and and_1 (Ram_e, 1'b0, Clk_e);
  and and_2 (Acc_e, undriven_3, Clk_e);
  and and_3 (R0_e, undriven_2, Clk_e);
  and and_4 (R1_e, undriven, Clk_e);
  and and_5 (R2_e, 1'b0, Clk_e);
  and and_6 (R3_e, 1'b0, Clk_e);
  cpu_stepper cpu_stepper_1 ();
  and and_7 (Mar_s, Clk_s, 1'b0);
  and and_8 (Acc_s, Clk_s, undriven_2);
  and and_9 (Ram_s, Clk_s, 1'b0);
  and and_10 (Temp_s, Clk_s, undriven);
  and and_11 (R0_s, Clk_s, 1'b0);
  and and_12 (R1_s, Clk_s, 1'b0);
  and and_13 (R2_s, Clk_s, 1'b0);
  and and_14 (R3_s, Clk_s, undriven_3);

  // Notes on the sheet:
  //   1
  //   2
  //   3
  //   4
  //   5
  //   6
endmodule
