// Digital circuit cpu_adder.dig as structural Verilog
module cpu_adder (
  input  a,
  input  b,
  input  cin,
  output o,
  output cout
);

  wire and_1_out, and_2_out, xor_1_out;

  xor xor_1 (xor_1_out, a, b);
  and and_1 (and_1_out, cin, xor_1_out);
  and and_2 (and_2_out, a, b);
  xor xor_2 (o, xor_1_out, cin);
  or or_1 (cout, and_1_out, and_2_out);
endmodule
