// Digital circuit cpu_adder_8.dig as structural Verilog
module cpu_adder_8 (
  input  Cin,
  input  [7:0] A,
  input  [7:0] B,
  output Cout,
  output [7:0] O
);

  cpu_adder cpu_adder_1 ();
  cpu_adder cpu_adder_2 ();
  cpu_adder cpu_adder_3 ();
  cpu_adder cpu_adder_4 ();
  cpu_adder cpu_adder_5 ();
  cpu_adder cpu_adder_6 ();
  cpu_adder cpu_adder_7 ();
  cpu_adder cpu_adder_8 ();
endmodule
