// Digital circuit cpu_alu.dig as structural Verilog
module cpu_alu (
  input  [7:0] A,
  input  [7:0] B,
  input  Cin,
  input  a_0,
  input  a_1,
  input  a_2,
  output A_gt,
  output Eq,
  output Z,
  output C_out,
  output [7:0] O
);

  wire and_1_out, and_2_out, and_3_out, undriven_8, undriven_9, undriven_10;
  wire [6:0] undriven_11;
  wire [7:0] undriven, undriven_2, undriven_3, undriven_4, undriven_5, undriven_6, undriven_7;

  cpu_xor_le_8 cpu_xor_le_8_1 ();
  cpu_or_8 cpu_or_8_1 (.A(A), .B(B));  // open: O
  cpu_and_8 cpu_and_8_1 (.A(A), .B(B));  // open: O
  cpu_not_8 cpu_not_8_1 (.I(A));  // open: O
  cpu_shl_8 cpu_shl_8_1 ();
  cpu_shr_8 cpu_shr_8_1 ();
  cpu_adder_8 cpu_adder_8_1 ();
  cpu_enable_8 cpu_enable_8_1 (.I(undriven), .E(undriven_11[6]));  // open: O
  cpu_enable_8 cpu_enable_8_2 (.I(undriven_2), .E(undriven_11[5]));  // open: O
  cpu_enable_8 cpu_enable_8_3 (.I(undriven_3), .E(undriven_11[4]));  // open: O
  cpu_enable_8 cpu_enable_8_4 (.I(undriven_4), .E(undriven_11[3]));  // open: O
  cpu_enable_8 cpu_enable_8_5 (.I(undriven_5), .E(undriven_11[2]));  // open: O
  cpu_enable_8 cpu_enable_8_6 (.I(undriven_6), .E(undriven_11[1]));  // open: O
  cpu_enable_8 cpu_enable_8_7 (.I(undriven_7), .E(undriven_11[0]));  // open: O
  cpu_decoder_3x8 cpu_decoder_3x8_1 (.A(a_0), .C(a_1));  // open: B, O
  and and_1 (and_1_out, undriven_8, undriven_11[2]);
  and and_2 (and_2_out, undriven_9, undriven_11[1]);
  and and_3 (and_3_out, undriven_10, undriven_11[0]);
  assign C_out = undriven_11[2] ? and_1_out : 1'bz;  // Driver driver_1
  assign C_out = undriven_11[1] ? and_2_out : 1'bz;  // Driver driver_2
  assign C_out = undriven_11[0] ? and_3_out : 1'bz;  // Driver driver_3
  cpu_z_8 cpu_z_8_1 (.I(O));  // open: O
endmodule
