// Digital circuit cpu_and_8.dig as structural Verilog
module cpu_and_8 (
  input  [7:0] A,
  input  [7:0] B,
  output [7:0] O
);

  and and_1 (O[7], A[7], B[7]);
  and and_2 (O[6], A[6], B[6]);
  and and_3 (O[5], A[5], B[5]);
  and and_4 (O[4], A[4], B[4]);
  and and_5 (O[3], A[3], B[3]);
  and and_6 (O[2], A[2], B[2]);
  and and_7 (O[1], A[1], B[1]);
  and and_8 (O[0], A[0], B[0]);
endmodule
