// Digital circuit cpu_bus.dig as structural Verilog
module cpu_bus (
  input  Bus1,
  input  [7:0] \Ì ,
  output [7:0] O
);

  wire not_1_out;

  not not_1 (not_1_out, Bus1);
  and and_1 (O[7], \Ì [7], not_1_out);
  and and_2 (O[6], \Ì [6], not_1_out);
  and and_3 (O[5], \Ì [5], not_1_out);
  and and_4 (O[4], \Ì [4], not_1_out);
  and and_5 (O[3], \Ì [3], not_1_out);
  and and_6 (O[2], \Ì [2], not_1_out);
  and and_7 (O[1], \Ì [1], not_1_out);
  or or_1 (O[0], \Ì [0], Bus1);
endmodule
