// Digital circuit cpu_clk.dig as structural Verilog
module cpu_clk (
  input  Clk,
  output Clk_2,
  output Clk_s,
  output Clk_e
);

  wire jk_ff_1_nq, nand_1_out;

  JK_FF jk_ff_1 (.J(1'b1), .C(Clk), .K(1'b1), .Q(Clk_2), .nQ(jk_ff_1_nq));
  nand nand_1 (nand_1_out, Clk, Clk_2);
  nand nand_2 (Clk_e, jk_ff_1_nq, Clk);
  not not_1 (Clk_s, nand_1_out);
endmodule
