// Digital circuit cpu_decoder_3x8.dig as structural Verilog
module cpu_decoder_3x8 (
  input  A,
  input  B,
  input  C,
  output [7:0] O
);

  wire not_1_out, not_2_out, not_3_out;

  not not_1 (not_1_out, C);
  not not_2 (not_2_out, B);
  not not_3 (not_3_out, A);
  and and_1 (O[0], not_3_out, not_2_out, not_1_out);
  and and_2 (O[1], not_1_out, not_2_out, A);
  and and_3 (O[2], not_3_out, B, not_1_out);
  and and_4 (O[3], not_1_out, B, A);
  and and_5 (O[4], C, not_2_out, not_3_out);
  and and_6 (O[5], C, not_2_out, A);
  and and_7 (O[6], C, B, not_3_out);
  and and_8 (O[7], C, B, A);
endmodule
