// Digital circuit cpu_decoder_4x16.dig as structural Verilog
module cpu_decoder_4x16 (
  input  A,
  input  B,
  input  C,
  input  D,
  output [15:0] O
);

  wire not_1_out, not_2_out, not_3_out, not_4_out;

  not not_1 (not_1_out, D);
  not not_2 (not_2_out, C);
  not not_3 (not_3_out, B);
  not not_4 (not_4_out, A);
  and and_1 (O[0], not_1_out, not_2_out, not_3_out, not_4_out);
  and and_2 (O[1], not_1_out, not_2_out, not_3_out, A);
  and and_3 (O[2], not_1_out, not_2_out, B, not_4_out);
  and and_4 (O[3], not_1_out, not_2_out, B, A);
  and and_5 (O[4], not_1_out, C, not_3_out, not_4_out);
  and and_6 (O[5], not_1_out, C, not_3_out, A);
  and and_7 (O[6], not_1_out, C, B, not_4_out);
  and and_8 (O[7], not_1_out, C, B, A);
  and and_9 (O[8], D, not_2_out, not_3_out, not_4_out);
  and and_10 (O[9], D, not_2_out, not_3_out, A);
  and and_11 (O[10], D, not_2_out, B, not_4_out);
  and and_12 (O[11], D, not_2_out, B, A);
  and and_13 (O[12], D, C, not_3_out, not_4_out);
  and and_14 (O[13], D, C, not_3_out, A);
  and and_15 (O[14], D, C, B, not_4_out);
  and and_16 (O[15], D, C, B, A);
endmodule
