// Digital circuit cpu_mem_1.dig as structural Verilog
module cpu_mem_1 (
  input  S,
  input  E,
  output O
);

  wire nand_1_out, nand_2_out, nand_4_out;

  nand nand_1 (nand_1_out, S, E);
  nand nand_2 (nand_2_out, nand_1_out, E);
  nand nand_3 (O, nand_1_out, nand_4_out);
  nand nand_4 (nand_4_out, O, nand_2_out);
endmodule
