// Digital circuit cpu_mem_8.dig as structural Verilog
module cpu_mem_8 (
  input  [7:0] I,
  input  S,
  output [7:0] O
);

  cpu_mem_1 cpu_mem_1_1 (.S(I[0]), .E(S));  // open: O
  cpu_mem_1 cpu_mem_1_2 (.S(I[1]), .E(S));  // open: O
  cpu_mem_1 cpu_mem_1_3 (.S(I[2]), .E(S));  // open: O
  cpu_mem_1 cpu_mem_1_4 (.S(I[3]), .E(S));  // open: O
  cpu_mem_1 cpu_mem_1_5 (.S(I[4]), .E(S));  // open: O
  cpu_mem_1 cpu_mem_1_6 (.S(I[5]), .E(S));  // open: O
  cpu_mem_1 cpu_mem_1_7 (.S(I[6]), .E(S));  // open: O
  cpu_mem_1 cpu_mem_1_8 (.S(I[7]), .E(S));  // open: O
endmodule
