// Digital circuit cpu_not_8.dig as structural Verilog
module cpu_not_8 (
  input  [7:0] I,
  output [7:0] O
);

  not not_1 (O[7], I[7]);
  not not_2 (O[6], I[6]);
  not not_3 (O[5], I[5]);
  not not_4 (O[4], I[4]);
  not not_5 (O[3], I[3]);
  not not_6 (O[2], I[2]);
  not not_7 (O[1], I[1]);
  not not_8 (O[0], I[0]);
endmodule
