// Digital circuit cpu_reg_8.dig as structural Verilog
module cpu_reg_8 (
  input  [7:0] I,
  input  S,
  input  E,
  output [7:0] O
);

  wire [7:0] undriven, undriven_2;

  cpu_mem_8 cpu_mem_8_1 (.I(I), .S(S));  // open: O
  cpu_enable cpu_enable_1 (.I(undriven), .E(E));  // open: O
  assign O = E ? undriven_2 : 8'bz;  // Driver driver_1
endmodule
