// Digital circuit cpu_reg_8_dbg.dig as structural Verilog
module cpu_reg_8_dbg (
  input  [7:0] I,
  input  S,
  input  E,
  output [7:0] O,
  output [7:0] \reg 
);

  wire [7:0] undriven;

  cpu_mem_8 cpu_mem_8_1 (.I(I), .S(S));  // open: O
  cpu_enable cpu_enable_1 (.I(\reg ), .E(E));  // open: O
  assign O = E ? undriven : 8'bz;  // Driver driver_1
endmodule
