// Digital circuit cpu_reg_byte.dig as structural Verilog
module cpu_reg_byte (
  input  Hor,
  input  Ver,
  input  [7:0] I,
  input  Set,
  input  En,
  input  Reset,
  output [7:0] O
);

  wire and_1_out, and_2_out, and_3_out, or_1_out;
  wire [7:0] undriven;

  and and_1 (and_1_out, Hor, Ver);
  and and_2 (and_2_out, and_1_out, Set);
  and and_3 (and_3_out, and_1_out, En);
  or or_1 (or_1_out, Reset, and_2_out);
  cpu_reg_8 cpu_reg_8_1 (.I(I), .E(or_1_out));  // open: S, O
  assign O = and_3_out ? undriven : 8'bz;  // Driver driver_1
endmodule
