// Digital circuit cpu_shl_8.dig as structural Verilog
module cpu_shl_8 (
  input  Shft_in,
  input  [7:0] I,
  output Shft_out,
  output [7:0] O
);

  wire [6:0] cpu_reg_8_1_o;

  cpu_reg_8 cpu_reg_8_1 (.I(I), .E(1'b1), .O({Shft_out, cpu_reg_8_1_o}));  // open: S
  cpu_reg_8 cpu_reg_8_2 (.I({cpu_reg_8_1_o, Shft_in}), .E(1'b1), .O(O));  // open: S
endmodule
