// Digital circuit cpu_shr_8.dig as structural Verilog
module cpu_shr_8 (
  input  Shft_in,
  input  [7:0] I,
  output Shft_out,
  output [7:0] O
);

  wire [7:1] cpu_reg_8_1_o;

  cpu_reg_8 cpu_reg_8_1 (.I(I), .E(1'b1), .O({cpu_reg_8_1_o, Shft_out}));  // open: S
  cpu_reg_8 cpu_reg_8_2 (.I({Shft_in, cpu_reg_8_1_o}), .E(1'b1), .O(O));  // open: S
endmodule
