// Digital circuit cpu_stepper.dig as structural Verilog
module cpu_stepper (
  input  Reset,
  input  Clk,
  output S_1,
  output S_2,
  output S_3,
  output S_4,
  output S_5,
  output S_6,
  output S_7
);

  wire not_1_out, not_2_out, not_3_out, not_4_out, not_5_out, not_6_out, not_7_out, not_8_out, or_1_out,
       or_2_out, undriven, undriven_2, undriven_3, undriven_4, undriven_5, undriven_6, undriven_7,
       undriven_8, undriven_9, undriven_10, undriven_11;

  not not_1 (not_1_out, Clk);
  not not_2 (not_2_out, Reset);
  or or_1 (or_1_out, Reset, Clk);
  or or_2 (or_2_out, Reset, not_1_out);
  or or_3 (S_1, Reset, not_3_out);
  cpu_mem_1 cpu_mem_1_1 (.S(not_2_out), .E(or_1_out));  // open: O
  cpu_mem_1 cpu_mem_1_2 (.S(undriven), .E(or_2_out));  // open: O
  not not_3 (not_3_out, undriven_2);
  cpu_mem_1 cpu_mem_1_3 (.S(undriven_2), .E(or_1_out));  // open: O
  and and_1 (S_2, undriven_2, not_4_out);
  cpu_mem_1 cpu_mem_1_4 (.S(undriven_3), .E(or_2_out));  // open: O
  not not_4 (not_4_out, undriven_4);
  and and_2 (S_3, undriven_4, not_5_out);
  cpu_mem_1 cpu_mem_1_5 (.S(undriven_4), .E(or_1_out));  // open: O
  cpu_mem_1 cpu_mem_1_6 (.S(undriven_5), .E(or_2_out));  // open: O
  not not_5 (not_5_out, undriven_6);
  and and_3 (S_4, undriven_6, not_6_out);
  cpu_mem_1 cpu_mem_1_7 (.S(undriven_6), .E(or_1_out));  // open: O
  cpu_mem_1 cpu_mem_1_8 (.S(undriven_7), .E(or_2_out));  // open: O
  not not_6 (not_6_out, undriven_8);
  and and_4 (S_5, undriven_8, not_7_out);
  cpu_mem_1 cpu_mem_1_9 (.S(undriven_8), .E(or_1_out));  // open: O
  cpu_mem_1 cpu_mem_1_10 (.S(undriven_9), .E(or_2_out));  // open: O
  not not_7 (not_7_out, undriven_10);
  and and_5 (S_6, undriven_10, not_8_out);
  cpu_mem_1 cpu_mem_1_11 (.S(undriven_10), .E(or_1_out));  // open: O
  cpu_mem_1 cpu_mem_1_12 (.S(undriven_11), .E(or_2_out));  // open: O
  not not_8 (not_8_out, Reset);

  assign S_7 = Reset;
endmodule
