// Digital circuit cpu_temp.dig as structural Verilog
module cpu_temp (
  input  [7:0] I,
  input  S,
  output [7:0] O
);

  wire [7:0] driver_1_out;

  assign driver_1_out = S ? I : 8'bz;  // Driver driver_1
  cpu_mem_8 cpu_mem_8_1 (.I(driver_1_out), .S(S));  // open: O
endmodule
