// Digital circuit cpu_xor_le_1.dig as structural Verilog
module cpu_xor_le_1 (
  input  A__gt_in,
  input  Eq_in,
  input  A,
  input  B,
  output O,
  output Eq,
  output A_gt
);

  wire and_2_out, not_1_out;

  xor xor_1 (O, A, B);
  not not_1 (not_1_out, O);
  and and_1 (Eq, Eq_in, not_1_out);
  and and_2 (and_2_out, Eq_in, A, O);
  or or_1 (A_gt, A__gt_in, and_2_out);
endmodule
