// Digital circuit cpu_xor_le_8.dig as structural Verilog
module cpu_xor_le_8 (
  input  [7:0] A,
  input  [7:0] B,
  output [7:0] O,
  output Eq,
  output A_gt
);

  wire not_1_out;

  cpu_xor_le_1 cpu_xor_le_1_1 ();
  not not_1 (not_1_out, 1'b1);
  cpu_xor_le_1 cpu_xor_le_1_2 ();
  cpu_xor_le_1 cpu_xor_le_1_3 ();
  cpu_xor_le_1 cpu_xor_le_1_4 ();
  cpu_xor_le_1 cpu_xor_le_1_5 ();
  cpu_xor_le_1 cpu_xor_le_1_6 ();
  cpu_xor_le_1 cpu_xor_le_1_7 ();
  cpu_xor_le_1 cpu_xor_le_1_8 ();
endmodule
