// Digital circuit cpu_z_8.dig as structural Verilog
module cpu_z_8 (
  input  [7:0] I,
  output O
);

  wire or_1_out;

  or or_1 (or_1_out, I[0], I[1], I[2], I[3], I[4], I[5], I[6], I[7]);
  not not_1 (O, or_1_out);
endmodule
