// Digital circuit debug.dig as structural Verilog
module debug (
  input  [7:0] IN,
  input  in_2,
  output [7:0] out_3
);

  wire and_1_out, cpu_clk_1_p2, cpu_clk_1_p3, cpu_clk_1_p4, undriven, undriven_2;
  wire [7:0] undriven_3;

  cpu_temp test (.I(undriven_3), .S(and_1_out));  // open: O
  // cpu_clk cpu_clk_1: pin names not known; wires that end beside it: in_2, cpu_clk_1_p2, cpu_clk_1_p3, cpu_clk_1_p4
  and and_1 (and_1_out, undriven_2, undriven);
  LED led_1 (.in(undriven_2));
  cpu_reg_8 REG1 (.I(IN), .E(1'b1));  // open: S, O
  LED led_2 (.in(undriven));
  Control control_1 ();
  LED led_3 (.in(undriven));
endmodule
