// Digital circuit cpu_ram_256_1vhresxhvsrio.dig as structural Verilog
module cpu_ram_256_1vhresxhvsrio (
  input  [7:0] address,
  input  sa,
  input  reset,
  input  e,
  input  s,
  input  [7:0] i,
  output o
);

  wire [3:0] cpu_mem_8_1_o, cpu_mem_8_1_o_2;
  wire [15:0] cpu_decoder_4x16_1_o, cpu_decoder_4x16_2_o;

  cpu_decoder_4x16 cpu_decoder_4x16_1 (
    .A(cpu_mem_8_1_o_2[3]), .B(cpu_mem_8_1_o_2[2]), .C(cpu_mem_8_1_o_2[1]), .D(cpu_mem_8_1_o_2[0]),
    .O(cpu_decoder_4x16_1_o));
  cpu_mem_8 cpu_mem_8_1 (.I(address), .S(sa), .O({cpu_mem_8_1_o_2, cpu_mem_8_1_o}));
  // cpu_reg_byte cpu_reg_byte_1: pin names not known; wires that end beside it: cpu_decoder_4x16_1_o[0], cpu_decoder_4x16_2_o[15], s, e, o, i, reset
  // cpu_reg_byte cpu_reg_byte_2: pin names not known; wires that end beside it: cpu_decoder_4x16_1_o[1], cpu_decoder_4x16_2_o[15], s, e, cpu_decoder_4x16_1_o[2], cpu_decoder_4x16_2_o[15], s, o, i, reset, o, i, reset
  cpu_reg_byte cpu_reg_byte_3 ();
  cpu_reg_byte cpu_reg_byte_4 ();
  cpu_reg_byte cpu_reg_byte_5 ();
  cpu_reg_byte cpu_reg_byte_6 ();
  cpu_reg_byte cpu_reg_byte_7 ();
  cpu_reg_byte cpu_reg_byte_8 ();
  cpu_reg_byte cpu_reg_byte_9 ();
  cpu_reg_byte cpu_reg_byte_10 ();
  cpu_reg_byte cpu_reg_byte_11 ();
  cpu_reg_byte cpu_reg_byte_12 ();
  cpu_reg_byte cpu_reg_byte_13 ();
  cpu_reg_byte cpu_reg_byte_14 ();
  cpu_reg_byte cpu_reg_byte_15 ();
  cpu_reg_byte cpu_reg_byte_16 ();
  // cpu_reg_byte cpu_reg_byte_17: pin names not known; wires that end beside it: cpu_decoder_4x16_1_o[0], cpu_decoder_4x16_2_o[14], s, e, o, i, reset
  // cpu_reg_byte cpu_reg_byte_18: pin names not known; wires that end beside it: cpu_decoder_4x16_1_o[1], cpu_decoder_4x16_2_o[14], s, e, cpu_decoder_4x16_1_o[2], cpu_decoder_4x16_2_o[14], s, o, i, reset, o, i, reset
  cpu_reg_byte cpu_reg_byte_19 ();
  cpu_reg_byte cpu_reg_byte_20 ();
  cpu_reg_byte cpu_reg_byte_21 ();
  cpu_reg_byte cpu_reg_byte_22 ();
  cpu_reg_byte cpu_reg_byte_23 ();
  cpu_reg_byte cpu_reg_byte_24 ();
  cpu_reg_byte cpu_reg_byte_25 ();
  cpu_reg_byte cpu_reg_byte_26 ();
  cpu_reg_byte cpu_reg_byte_27 ();
  cpu_reg_byte cpu_reg_byte_28 ();
  cpu_reg_byte cpu_reg_byte_29 ();
  cpu_reg_byte cpu_reg_byte_30 ();
  cpu_reg_byte cpu_reg_byte_31 ();
  cpu_reg_byte cpu_reg_byte_32 ();
  // cpu_reg_byte cpu_reg_byte_33: pin names not known; wires that end beside it: cpu_decoder_4x16_1_o[0], cpu_decoder_4x16_2_o[13], s, e, o, i, reset
  // cpu_reg_byte cpu_reg_byte_34: pin names not known; wires that end beside it: cpu_decoder_4x16_1_o[1], cpu_decoder_4x16_2_o[13], s, e, cpu_decoder_4x16_1_o[2], cpu_decoder_4x16_2_o[13], s, o, i, reset, o, i, reset
  cpu_reg_byte cpu_reg_byte_35 ();
  cpu_reg_byte cpu_reg_byte_36 ();
  cpu_reg_byte cpu_reg_byte_37 ();
  cpu_reg_byte cpu_reg_byte_38 ();
  cpu_reg_byte cpu_reg_byte_39 ();
  cpu_reg_byte cpu_reg_byte_40 ();
  cpu_reg_byte cpu_reg_byte_41 ();
  cpu_reg_byte cpu_reg_byte_42 ();
  cpu_reg_byte cpu_reg_byte_43 ();
  cpu_reg_byte cpu_reg_byte_44 ();
  cpu_reg_byte cpu_reg_byte_45 ();
  cpu_reg_byte cpu_reg_byte_46 ();
  cpu_reg_byte cpu_reg_byte_47 ();
  cpu_reg_byte cpu_reg_byte_48 ();
  // cpu_reg_byte cpu_reg_byte_49: pin names not known; wires that end beside it: cpu_decoder_4x16_1_o[0], cpu_decoder_4x16_2_o[12], s, e, o, i, reset
  // cpu_reg_byte cpu_reg_byte_50: pin names not known; wires that end beside it: cpu_decoder_4x16_1_o[1], cpu_decoder_4x16_2_o[12], s, e, cpu_decoder_4x16_1_o[2], cpu_decoder_4x16_2_o[12], s, o, i, reset, o, i, reset
  cpu_reg_byte cpu_reg_byte_51 ();
  cpu_reg_byte cpu_reg_byte_52 ();
  cpu_reg_byte cpu_reg_byte_53 ();
  cpu_reg_byte cpu_reg_byte_54 ();
  cpu_reg_byte cpu_reg_byte_55 ();
  cpu_reg_byte cpu_reg_byte_56 ();
  cpu_reg_byte cpu_reg_byte_57 ();
  cpu_reg_byte cpu_reg_byte_58 ();
  cpu_reg_byte cpu_reg_byte_59 ();
  cpu_reg_byte cpu_reg_byte_60 ();
  cpu_reg_byte cpu_reg_byte_61 ();
  cpu_reg_byte cpu_reg_byte_62 ();
  cpu_reg_byte cpu_reg_byte_63 ();
  cpu_reg_byte cpu_reg_byte_64 ();
  // cpu_reg_byte cpu_reg_byte_65: pin names not known; wires that end beside it: cpu_decoder_4x16_1_o[0], cpu_decoder_4x16_2_o[11], s, e, o, i, reset
  // cpu_reg_byte cpu_reg_byte_66: pin names not known; wires that end beside it: cpu_decoder_4x16_1_o[1], cpu_decoder_4x16_2_o[11], s, e, cpu_decoder_4x16_1_o[2], cpu_decoder_4x16_2_o[11], s, o, i, reset, o, i, reset
  cpu_reg_byte cpu_reg_byte_67 ();
  cpu_reg_byte cpu_reg_byte_68 ();
  cpu_reg_byte cpu_reg_byte_69 ();
  cpu_reg_byte cpu_reg_byte_70 ();
  cpu_reg_byte cpu_reg_byte_71 ();
  cpu_reg_byte cpu_reg_byte_72 ();
  cpu_reg_byte cpu_reg_byte_73 ();
  cpu_reg_byte cpu_reg_byte_74 ();
  cpu_reg_byte cpu_reg_byte_75 ();
  cpu_reg_byte cpu_reg_byte_76 ();
  cpu_reg_byte cpu_reg_byte_77 ();
  cpu_reg_byte cpu_reg_byte_78 ();
  cpu_reg_byte cpu_reg_byte_79 ();
  cpu_reg_byte cpu_reg_byte_80 ();
  // cpu_reg_byte cpu_reg_byte_81: pin names not known; wires that end beside it: cpu_decoder_4x16_1_o[0], cpu_decoder_4x16_2_o[10], s, e, o, i, reset
  // cpu_reg_byte cpu_reg_byte_82: pin names not known; wires that end beside it: cpu_decoder_4x16_1_o[1], cpu_decoder_4x16_2_o[10], s, e, cpu_decoder_4x16_1_o[2], cpu_decoder_4x16_2_o[10], s, o, i, reset, o, i, reset
  cpu_reg_byte cpu_reg_byte_83 ();
  cpu_reg_byte cpu_reg_byte_84 ();
  cpu_reg_byte cpu_reg_byte_85 ();
  cpu_reg_byte cpu_reg_byte_86 ();
  cpu_reg_byte cpu_reg_byte_87 ();
  cpu_reg_byte cpu_reg_byte_88 ();
  cpu_reg_byte cpu_reg_byte_89 ();
  cpu_reg_byte cpu_reg_byte_90 ();
  cpu_reg_byte cpu_reg_byte_91 ();
  cpu_reg_byte cpu_reg_byte_92 ();
  cpu_reg_byte cpu_reg_byte_93 ();
  cpu_reg_byte cpu_reg_byte_94 ();
  cpu_reg_byte cpu_reg_byte_95 ();
  cpu_reg_byte cpu_reg_byte_96 ();
  // cpu_reg_byte cpu_reg_byte_97: pin names not known; wires that end beside it: cpu_decoder_4x16_1_o[0], cpu_decoder_4x16_2_o[9], s, e, o, i, reset
  // cpu_reg_byte cpu_reg_byte_98: pin names not known; wires that end beside it: cpu_decoder_4x16_1_o[1], cpu_decoder_4x16_2_o[9], s, e, cpu_decoder_4x16_1_o[2], cpu_decoder_4x16_2_o[9], s, o, i, reset, o, i, reset
  cpu_reg_byte cpu_reg_byte_99 ();
  cpu_reg_byte cpu_reg_byte_100 ();
  cpu_reg_byte cpu_reg_byte_101 ();
  cpu_reg_byte cpu_reg_byte_102 ();
  cpu_reg_byte cpu_reg_byte_103 ();
  cpu_reg_byte cpu_reg_byte_104 ();
  cpu_reg_byte cpu_reg_byte_105 ();
  cpu_reg_byte cpu_reg_byte_106 ();
  cpu_reg_byte cpu_reg_byte_107 ();
  cpu_reg_byte cpu_reg_byte_108 ();
  cpu_reg_byte cpu_reg_byte_109 ();
  cpu_reg_byte cpu_reg_byte_110 ();
  cpu_reg_byte cpu_reg_byte_111 ();
  cpu_reg_byte cpu_reg_byte_112 ();
  // cpu_reg_byte cpu_reg_byte_113: pin names not known; wires that end beside it: cpu_decoder_4x16_1_o[0], cpu_decoder_4x16_2_o[8], s, e, o, i, reset
  // cpu_reg_byte cpu_reg_byte_114: pin names not known; wires that end beside it: cpu_decoder_4x16_1_o[1], cpu_decoder_4x16_2_o[8], s, e, cpu_decoder_4x16_1_o[2], cpu_decoder_4x16_2_o[8], s, o, i, reset, o, i, reset
  cpu_reg_byte cpu_reg_byte_115 ();
  cpu_reg_byte cpu_reg_byte_116 ();
  cpu_reg_byte cpu_reg_byte_117 ();
  cpu_reg_byte cpu_reg_byte_118 ();
  cpu_reg_byte cpu_reg_byte_119 ();
  cpu_reg_byte cpu_reg_byte_120 ();
  cpu_reg_byte cpu_reg_byte_121 ();
  cpu_reg_byte cpu_reg_byte_122 ();
  cpu_reg_byte cpu_reg_byte_123 ();
  cpu_reg_byte cpu_reg_byte_124 ();
  cpu_reg_byte cpu_reg_byte_125 ();
  cpu_reg_byte cpu_reg_byte_126 ();
  cpu_reg_byte cpu_reg_byte_127 ();
  cpu_reg_byte cpu_reg_byte_128 ();
  // cpu_reg_byte cpu_reg_byte_129: pin names not known; wires that end beside it: cpu_decoder_4x16_1_o[0], cpu_decoder_4x16_2_o[7], s, e, o, i, reset
  // cpu_reg_byte cpu_reg_byte_130: pin names not known; wires that end beside it: cpu_decoder_4x16_1_o[1], cpu_decoder_4x16_2_o[7], s, e, cpu_decoder_4x16_1_o[2], cpu_decoder_4x16_2_o[7], s, o, i, reset, o, i, reset
  cpu_reg_byte cpu_reg_byte_131 ();
  cpu_reg_byte cpu_reg_byte_132 ();
  cpu_reg_byte cpu_reg_byte_133 ();
  cpu_reg_byte cpu_reg_byte_134 ();
  cpu_reg_byte cpu_reg_byte_135 ();
  cpu_reg_byte cpu_reg_byte_136 ();
  cpu_reg_byte cpu_reg_byte_137 ();
  cpu_reg_byte cpu_reg_byte_138 ();
  cpu_reg_byte cpu_reg_byte_139 ();
  cpu_reg_byte cpu_reg_byte_140 ();
  cpu_reg_byte cpu_reg_byte_141 ();
  cpu_reg_byte cpu_reg_byte_142 ();
  cpu_reg_byte cpu_reg_byte_143 ();
  cpu_reg_byte cpu_reg_byte_144 ();
  cpu_decoder_4x16 cpu_decoder_4x16_2 (
    .A(cpu_mem_8_1_o[3]), .B(cpu_mem_8_1_o[2]), .C(cpu_mem_8_1_o[1]), .D(cpu_mem_8_1_o[0]),
    .O(cpu_decoder_4x16_2_o));
  // cpu_reg_byte cpu_reg_byte_145: pin names not known; wires that end beside it: cpu_decoder_4x16_1_o[0], cpu_decoder_4x16_2_o[6], s, e, o, i, reset
  // cpu_reg_byte cpu_reg_byte_146: pin names not known; wires that end beside it: cpu_decoder_4x16_1_o[1], cpu_decoder_4x16_2_o[6], s, e, cpu_decoder_4x16_1_o[2], cpu_decoder_4x16_2_o[6], s, o, i, reset, o, i, reset
  cpu_reg_byte cpu_reg_byte_147 ();
  cpu_reg_byte cpu_reg_byte_148 ();
  cpu_reg_byte cpu_reg_byte_149 ();
  cpu_reg_byte cpu_reg_byte_150 ();
  cpu_reg_byte cpu_reg_byte_151 ();
  cpu_reg_byte cpu_reg_byte_152 ();
  cpu_reg_byte cpu_reg_byte_153 ();
  cpu_reg_byte cpu_reg_byte_154 ();
  cpu_reg_byte cpu_reg_byte_155 ();
  cpu_reg_byte cpu_reg_byte_156 ();
  cpu_reg_byte cpu_reg_byte_157 ();
  cpu_reg_byte cpu_reg_byte_158 ();
  cpu_reg_byte cpu_reg_byte_159 ();
  cpu_reg_byte cpu_reg_byte_160 ();
  // cpu_reg_byte cpu_reg_byte_161: pin names not known; wires that end beside it: cpu_decoder_4x16_1_o[0], cpu_decoder_4x16_2_o[5], s, e, o, i, reset
  // cpu_reg_byte cpu_reg_byte_162: pin names not known; wires that end beside it: cpu_decoder_4x16_1_o[1], cpu_decoder_4x16_2_o[5], s, e, cpu_decoder_4x16_1_o[2], cpu_decoder_4x16_2_o[5], s, o, i, reset, o, i, reset
  cpu_reg_byte cpu_reg_byte_163 ();
  cpu_reg_byte cpu_reg_byte_164 ();
  cpu_reg_byte cpu_reg_byte_165 ();
  cpu_reg_byte cpu_reg_byte_166 ();
  cpu_reg_byte cpu_reg_byte_167 ();
  cpu_reg_byte cpu_reg_byte_168 ();
  cpu_reg_byte cpu_reg_byte_169 ();
  cpu_reg_byte cpu_reg_byte_170 ();
  cpu_reg_byte cpu_reg_byte_171 ();
  cpu_reg_byte cpu_reg_byte_172 ();
  cpu_reg_byte cpu_reg_byte_173 ();
  cpu_reg_byte cpu_reg_byte_174 ();
  cpu_reg_byte cpu_reg_byte_175 ();
  cpu_reg_byte cpu_reg_byte_176 ();
  // cpu_reg_byte cpu_reg_byte_177: pin names not known; wires that end beside it: cpu_decoder_4x16_1_o[0], cpu_decoder_4x16_2_o[4], s, e, o, i, reset
  // cpu_reg_byte cpu_reg_byte_178: pin names not known; wires that end beside it: cpu_decoder_4x16_1_o[1], cpu_decoder_4x16_2_o[4], s, e, cpu_decoder_4x16_1_o[2], cpu_decoder_4x16_2_o[4], s, o, i, reset, o, i, reset
  cpu_reg_byte cpu_reg_byte_179 ();
  cpu_reg_byte cpu_reg_byte_180 ();
  cpu_reg_byte cpu_reg_byte_181 ();
  cpu_reg_byte cpu_reg_byte_182 ();
  cpu_reg_byte cpu_reg_byte_183 ();
  cpu_reg_byte cpu_reg_byte_184 ();
  cpu_reg_byte cpu_reg_byte_185 ();
  cpu_reg_byte cpu_reg_byte_186 ();
  cpu_reg_byte cpu_reg_byte_187 ();
  cpu_reg_byte cpu_reg_byte_188 ();
  cpu_reg_byte cpu_reg_byte_189 ();
  cpu_reg_byte cpu_reg_byte_190 ();
  cpu_reg_byte cpu_reg_byte_191 ();
  cpu_reg_byte cpu_reg_byte_192 ();
  // cpu_reg_byte cpu_reg_byte_193: pin names not known; wires that end beside it: cpu_decoder_4x16_1_o[0], cpu_decoder_4x16_2_o[3], s, e, o, i, reset
  // cpu_reg_byte cpu_reg_byte_194: pin names not known; wires that end beside it: cpu_decoder_4x16_1_o[1], cpu_decoder_4x16_2_o[3], s, e, cpu_decoder_4x16_1_o[2], cpu_decoder_4x16_2_o[3], s, o, i, reset, o, i, reset
  cpu_reg_byte cpu_reg_byte_195 ();
  cpu_reg_byte cpu_reg_byte_196 ();
  cpu_reg_byte cpu_reg_byte_197 ();
  cpu_reg_byte cpu_reg_byte_198 ();
  cpu_reg_byte cpu_reg_byte_199 ();
  cpu_reg_byte cpu_reg_byte_200 ();
  cpu_reg_byte cpu_reg_byte_201 ();
  cpu_reg_byte cpu_reg_byte_202 ();
  cpu_reg_byte cpu_reg_byte_203 ();
  cpu_reg_byte cpu_reg_byte_204 ();
  cpu_reg_byte cpu_reg_byte_205 ();
  cpu_reg_byte cpu_reg_byte_206 ();
  cpu_reg_byte cpu_reg_byte_207 ();
  cpu_reg_byte cpu_reg_byte_208 ();
  // cpu_reg_byte cpu_reg_byte_209: pin names not known; wires that end beside it: cpu_decoder_4x16_1_o[0], cpu_decoder_4x16_2_o[2], s, e, o, i, reset
  // cpu_reg_byte cpu_reg_byte_210: pin names not known; wires that end beside it: cpu_decoder_4x16_1_o[1], cpu_decoder_4x16_2_o[2], s, e, cpu_decoder_4x16_1_o[2], cpu_decoder_4x16_2_o[2], s, o, i, reset, o, i, reset
  cpu_reg_byte cpu_reg_byte_211 ();
  cpu_reg_byte cpu_reg_byte_212 ();
  cpu_reg_byte cpu_reg_byte_213 ();
  cpu_reg_byte cpu_reg_byte_214 ();
  cpu_reg_byte cpu_reg_byte_215 ();
  cpu_reg_byte cpu_reg_byte_216 ();
  cpu_reg_byte cpu_reg_byte_217 ();
  cpu_reg_byte cpu_reg_byte_218 ();
  cpu_reg_byte cpu_reg_byte_219 ();
  cpu_reg_byte cpu_reg_byte_220 ();
  cpu_reg_byte cpu_reg_byte_221 ();
  cpu_reg_byte cpu_reg_byte_222 ();
  cpu_reg_byte cpu_reg_byte_223 ();
  cpu_reg_byte cpu_reg_byte_224 ();
  // cpu_reg_byte cpu_reg_byte_225: pin names not known; wires that end beside it: cpu_decoder_4x16_1_o[0], cpu_decoder_4x16_2_o[1], s, e, o, i, reset
  // cpu_reg_byte cpu_reg_byte_226: pin names not known; wires that end beside it: cpu_decoder_4x16_1_o[1], cpu_decoder_4x16_2_o[1], s, e, cpu_decoder_4x16_1_o[2], cpu_decoder_4x16_2_o[1], s, o, i, reset
  cpu_reg_byte cpu_reg_byte_227 ();
  cpu_reg_byte cpu_reg_byte_228 ();
  cpu_reg_byte cpu_reg_byte_229 ();
  cpu_reg_byte cpu_reg_byte_230 ();
  cpu_reg_byte cpu_reg_byte_231 ();
  cpu_reg_byte cpu_reg_byte_232 ();
  cpu_reg_byte cpu_reg_byte_233 ();
  cpu_reg_byte cpu_reg_byte_234 ();
  cpu_reg_byte cpu_reg_byte_235 ();
  cpu_reg_byte cpu_reg_byte_236 ();
  cpu_reg_byte cpu_reg_byte_237 ();
  cpu_reg_byte cpu_reg_byte_238 ();
  cpu_reg_byte cpu_reg_byte_239 ();
  cpu_reg_byte cpu_reg_byte_240 ();
  // cpu_reg_byte cpu_reg_byte_241: pin names not known; wires that end beside it: cpu_decoder_4x16_1_o[0], cpu_decoder_4x16_2_o[0], s, e, o, i, reset
  // cpu_reg_byte cpu_reg_byte_242: pin names not known; wires that end beside it: cpu_decoder_4x16_1_o[1], cpu_decoder_4x16_2_o[0], s, e, o, i, reset
  // cpu_reg_byte cpu_reg_byte_243: pin names not known; wires that end beside it: o, i, reset, cpu_decoder_4x16_1_o[2], cpu_decoder_4x16_2_o[0], s, e, o, i, reset
  // cpu_reg_byte cpu_reg_byte_244: pin names not known; wires that end beside it: cpu_decoder_4x16_1_o[3], cpu_decoder_4x16_2_o[1], s, o, i, reset, cpu_decoder_4x16_1_o[3], cpu_decoder_4x16_2_o[0], s, e, o, i, reset
  // cpu_reg_byte cpu_reg_byte_245: pin names not known; wires that end beside it: cpu_decoder_4x16_1_o[4], cpu_decoder_4x16_2_o[1], s, o, i, reset, cpu_decoder_4x16_1_o[4], cpu_decoder_4x16_2_o[0], s, e, o, i, reset
  // cpu_reg_byte cpu_reg_byte_246: pin names not known; wires that end beside it: cpu_decoder_4x16_1_o[5], cpu_decoder_4x16_2_o[1], s, o, i, reset, cpu_decoder_4x16_1_o[5], cpu_decoder_4x16_2_o[0], s, e, o, i, reset
  // cpu_reg_byte cpu_reg_byte_247: pin names not known; wires that end beside it: cpu_decoder_4x16_1_o[6], cpu_decoder_4x16_2_o[1], s, o, i, reset, cpu_decoder_4x16_1_o[6], cpu_decoder_4x16_2_o[0], s, e, o, i, reset
  // cpu_reg_byte cpu_reg_byte_248: pin names not known; wires that end beside it: cpu_decoder_4x16_1_o[7], cpu_decoder_4x16_2_o[1], s, o, i, reset, cpu_decoder_4x16_1_o[7], cpu_decoder_4x16_2_o[0], s, e, o, i, reset
  // cpu_reg_byte cpu_reg_byte_249: pin names not known; wires that end beside it: cpu_decoder_4x16_1_o[8], cpu_decoder_4x16_2_o[1], s, o, i, reset, cpu_decoder_4x16_1_o[8], cpu_decoder_4x16_2_o[0], s, e, o, i, reset
  // cpu_reg_byte cpu_reg_byte_250: pin names not known; wires that end beside it: cpu_decoder_4x16_1_o[9], cpu_decoder_4x16_2_o[1], s, o, i, reset, cpu_decoder_4x16_1_o[9], cpu_decoder_4x16_2_o[0], s, e, o, i, reset
  // cpu_reg_byte cpu_reg_byte_251: pin names not known; wires that end beside it: cpu_decoder_4x16_1_o[10], cpu_decoder_4x16_2_o[1], s, o, i, reset, cpu_decoder_4x16_1_o[10], cpu_decoder_4x16_2_o[0], s, e, o, i, reset
  // cpu_reg_byte cpu_reg_byte_252: pin names not known; wires that end beside it: cpu_decoder_4x16_1_o[11], cpu_decoder_4x16_2_o[1], s, o, i, reset, cpu_decoder_4x16_1_o[11], cpu_decoder_4x16_2_o[0], s, e, o, i, reset
  // cpu_reg_byte cpu_reg_byte_253: pin names not known; wires that end beside it: cpu_decoder_4x16_1_o[12], cpu_decoder_4x16_2_o[1], s, o, i, reset, cpu_decoder_4x16_1_o[12], cpu_decoder_4x16_2_o[0], s, e, o, i, reset
  // cpu_reg_byte cpu_reg_byte_254: pin names not known; wires that end beside it: cpu_decoder_4x16_1_o[13], cpu_decoder_4x16_2_o[1], s, o, i, reset, cpu_decoder_4x16_1_o[13], cpu_decoder_4x16_2_o[0], s, e, o, i, reset
  // cpu_reg_byte cpu_reg_byte_255: pin names not known; wires that end beside it: cpu_decoder_4x16_1_o[14], cpu_decoder_4x16_2_o[1], s, o, i, reset, cpu_decoder_4x16_1_o[14], cpu_decoder_4x16_2_o[0], s, e, o, i, reset
  // cpu_reg_byte cpu_reg_byte_256: pin names not known; wires that end beside it: cpu_decoder_4x16_1_o[15], cpu_decoder_4x16_2_o[1], s, o, i, reset, cpu_decoder_4x16_1_o[15], cpu_decoder_4x16_2_o[0], s, e, o, i, reset
endmodule
