// Digital circuit cpu_ram_256_1vhresxhvsrioregV.dig as structural Verilog
module cpu_ram_256_1vhresxhvsrioregV (
  input  [7:0] address,
  input  sa,
  input  reset,
  input  e,
  input  s,
  input  [7:0] i,
  output o,
  output \reg ,
  output reg_2,
  output reg_3,
  output reg_4,
  output reg_5,
  output reg_6,
  output reg_7,
  output reg_8,
  output reg_9,
  output reg_10,
  output reg_11,
  output reg_12,
  output reg_13,
  output reg_14,
  output reg_15,
  output reg_16,
  output reg_17,
  output reg_18,
  output reg_19,
  output reg_20,
  output reg_21,
  output reg_22,
  output reg_23,
  output reg_24,
  output reg_25,
  output reg_26,
  output reg_27,
  output reg_28,
  output reg_29,
  output reg_30,
  output reg_31,
  output reg_32,
  output reg_33,
  output reg_34,
  output reg_35,
  output reg_36,
  output reg_37,
  output reg_38,
  output reg_39,
  output reg_40,
  output reg_41,
  output reg_42,
  output reg_43,
  output reg_44,
  output reg_45,
  output reg_46,
  output reg_47,
  output reg_48,
  output reg_49,
  output reg_50,
  output reg_51,
  output reg_52,
  output reg_53,
  output reg_54,
  output reg_55,
  output reg_56,
  output reg_57,
  output reg_58,
  output reg_59,
  output reg_60,
  output reg_61,
  output reg_62,
  output reg_63,
  output reg_64,
  output reg_65,
  output reg_66,
  output reg_67,
  output reg_68,
  output reg_69,
  output reg_70,
  output reg_71,
  output reg_72,
  output reg_73,
  output reg_74,
  output reg_75,
  output reg_76,
  output reg_77,
  output reg_78,
  output reg_79,
  output reg_80,
  output reg_81,
  output reg_82,
  output reg_83,
  output reg_84,
  output reg_85,
  output reg_86,
  output reg_87,
  output reg_88,
  output reg_89,
  output reg_90,
  output reg_91,
  output reg_92,
  output reg_93,
  output reg_94,
  output reg_95,
  output reg_96,
  output reg_97,
  output reg_98,
  output reg_99,
  output reg_100,
  output reg_101,
  output reg_102,
  output reg_103,
  output reg_104,
  output reg_105,
  output reg_106,
  output reg_107,
  output reg_108,
  output reg_109,
  output reg_110,
  output reg_111,
  output reg_112,
  output reg_113,
  output reg_114,
  output reg_115,
  output reg_116,
  output reg_117,
  output reg_118,
  output reg_119,
  output reg_120,
  output reg_121,
  output reg_122,
  output reg_123,
  output reg_124,
  output reg_125,
  output reg_126,
  output reg_127,
  output reg_128,
  output reg_129,
  output reg_130,
  output reg_131,
  output reg_132,
  output reg_133,
  output reg_134,
  output reg_135,
  output reg_136,
  output reg_137,
  output reg_138,
  output reg_139,
  output reg_140,
  output reg_141,
  output reg_142,
  output reg_143,
  output reg_144,
  output reg_145,
  output reg_146,
  output reg_147,
  output reg_148,
  output reg_149,
  output reg_150,
  output reg_151,
  output reg_152,
  output reg_153,
  output reg_154,
  output reg_155,
  output reg_156,
  output reg_157,
  output reg_158,
  output reg_159,
  output reg_160,
  output reg_161,
  output reg_162,
  output reg_163,
  output reg_164,
  output reg_165,
  output reg_166,
  output reg_167,
  output reg_168,
  output reg_169,
  output reg_170,
  output reg_171,
  output reg_172,
  output reg_173,
  output reg_174,
  output reg_175,
  output reg_176,
  output reg_177,
  output reg_178,
  output reg_179,
  output reg_180,
  output reg_181,
  output reg_182,
  output reg_183,
  output reg_184,
  output reg_185,
  output reg_186,
  output reg_187,
  output reg_188,
  output reg_189,
  output reg_190,
  output reg_191,
  output reg_192,
  output reg_193,
  output reg_194,
  output reg_195,
  output reg_196,
  output reg_197,
  output reg_198,
  output reg_199,
  output reg_200,
  output reg_201,
  output reg_202,
  output reg_203,
  output reg_204,
  output reg_205,
  output reg_206,
  output reg_207,
  output reg_208,
  output reg_209,
  output reg_210,
  output reg_211,
  output reg_212,
  output reg_213,
  output reg_214,
  output reg_215,
  output reg_216,
  output reg_217,
  output reg_218,
  output reg_219,
  output reg_220,
  output reg_221,
  output reg_222,
  output reg_223,
  output reg_224,
  output reg_225,
  output reg_226,
  output reg_227,
  output reg_228,
  output reg_229,
  output reg_230,
  output reg_231,
  output reg_232,
  output reg_233,
  output reg_234,
  output reg_235,
  output reg_236,
  output reg_237,
  output reg_238,
  output reg_239,
  output reg_240,
  output reg_241,
  output reg_242,
  output reg_243,
  output reg_244,
  output reg_245,
  output reg_246,
  output reg_247,
  output reg_248,
  output reg_249,
  output reg_250,
  output reg_251,
  output reg_252,
  output reg_253,
  output reg_254,
  output reg_255,
  output reg_256
);

  wire [3:0] cpu_mem_8_1_o, cpu_mem_8_1_o_2;
  wire [15:0] cpu_decoder_4x16_1_o, cpu_decoder_4x16_2_o;

  cpu_decoder_4x16 cpu_decoder_4x16_1 (
    .A(cpu_mem_8_1_o_2[3]), .B(cpu_mem_8_1_o_2[2]), .C(cpu_mem_8_1_o_2[1]), .D(cpu_mem_8_1_o_2[0]),
    .O(cpu_decoder_4x16_1_o));
  cpu_mem_8 cpu_mem_8_1 (.I(address), .S(sa), .O({cpu_mem_8_1_o_2, cpu_mem_8_1_o}));
  // cpu_reg_byte cpu_reg_byte_1: pin names not known; wires that end beside it: cpu_decoder_4x16_1_o[0], cpu_decoder_4x16_2_o[15], s, e, o, \reg , i, reset
  // cpu_reg_byte cpu_reg_byte_2: pin names not known; wires that end beside it: cpu_decoder_4x16_1_o[1], cpu_decoder_4x16_2_o[15], s, e, cpu_decoder_4x16_1_o[2], cpu_decoder_4x16_2_o[15], s, o, reg_17, i, reset, o, reg_33, i, reset
  cpu_reg_byte cpu_reg_byte_3 ();
  cpu_reg_byte cpu_reg_byte_4 ();
  cpu_reg_byte cpu_reg_byte_5 ();
  cpu_reg_byte cpu_reg_byte_6 ();
  cpu_reg_byte cpu_reg_byte_7 ();
  cpu_reg_byte cpu_reg_byte_8 ();
  cpu_reg_byte cpu_reg_byte_9 ();
  cpu_reg_byte cpu_reg_byte_10 ();
  cpu_reg_byte cpu_reg_byte_11 ();
  cpu_reg_byte cpu_reg_byte_12 ();
  cpu_reg_byte cpu_reg_byte_13 ();
  cpu_reg_byte cpu_reg_byte_14 ();
  cpu_reg_byte cpu_reg_byte_15 ();
  cpu_reg_byte cpu_reg_byte_16 ();
  // cpu_reg_byte cpu_reg_byte_17: pin names not known; wires that end beside it: cpu_decoder_4x16_1_o[0], cpu_decoder_4x16_2_o[14], s, e, o, reg_2, i, reset
  // cpu_reg_byte cpu_reg_byte_18: pin names not known; wires that end beside it: cpu_decoder_4x16_1_o[1], cpu_decoder_4x16_2_o[14], s, e, cpu_decoder_4x16_1_o[2], cpu_decoder_4x16_2_o[14], s, o, reg_18, i, reset, o, reg_34, i, reset
  cpu_reg_byte cpu_reg_byte_19 ();
  cpu_reg_byte cpu_reg_byte_20 ();
  cpu_reg_byte cpu_reg_byte_21 ();
  cpu_reg_byte cpu_reg_byte_22 ();
  cpu_reg_byte cpu_reg_byte_23 ();
  cpu_reg_byte cpu_reg_byte_24 ();
  cpu_reg_byte cpu_reg_byte_25 ();
  cpu_reg_byte cpu_reg_byte_26 ();
  cpu_reg_byte cpu_reg_byte_27 ();
  cpu_reg_byte cpu_reg_byte_28 ();
  cpu_reg_byte cpu_reg_byte_29 ();
  cpu_reg_byte cpu_reg_byte_30 ();
  cpu_reg_byte cpu_reg_byte_31 ();
  cpu_reg_byte cpu_reg_byte_32 ();
  // cpu_reg_byte cpu_reg_byte_33: pin names not known; wires that end beside it: cpu_decoder_4x16_1_o[0], cpu_decoder_4x16_2_o[13], s, e, o, reg_3, i, reset
  // cpu_reg_byte cpu_reg_byte_34: pin names not known; wires that end beside it: cpu_decoder_4x16_1_o[1], cpu_decoder_4x16_2_o[13], s, e, cpu_decoder_4x16_1_o[2], cpu_decoder_4x16_2_o[13], s, o, reg_19, i, reset, o, reg_35, i, reset
  cpu_reg_byte cpu_reg_byte_35 ();
  cpu_reg_byte cpu_reg_byte_36 ();
  cpu_reg_byte cpu_reg_byte_37 ();
  cpu_reg_byte cpu_reg_byte_38 ();
  cpu_reg_byte cpu_reg_byte_39 ();
  cpu_reg_byte cpu_reg_byte_40 ();
  cpu_reg_byte cpu_reg_byte_41 ();
  cpu_reg_byte cpu_reg_byte_42 ();
  cpu_reg_byte cpu_reg_byte_43 ();
  cpu_reg_byte cpu_reg_byte_44 ();
  cpu_reg_byte cpu_reg_byte_45 ();
  cpu_reg_byte cpu_reg_byte_46 ();
  cpu_reg_byte cpu_reg_byte_47 ();
  cpu_reg_byte cpu_reg_byte_48 ();
  // cpu_reg_byte cpu_reg_byte_49: pin names not known; wires that end beside it: cpu_decoder_4x16_1_o[0], cpu_decoder_4x16_2_o[12], s, e, o, reg_4, i, reset
  // cpu_reg_byte cpu_reg_byte_50: pin names not known; wires that end beside it: cpu_decoder_4x16_1_o[1], cpu_decoder_4x16_2_o[12], s, e, cpu_decoder_4x16_1_o[2], cpu_decoder_4x16_2_o[12], s, o, reg_20, i, reset, o, reg_36, i, reset
  cpu_reg_byte cpu_reg_byte_51 ();
  cpu_reg_byte cpu_reg_byte_52 ();
  cpu_reg_byte cpu_reg_byte_53 ();
  cpu_reg_byte cpu_reg_byte_54 ();
  cpu_reg_byte cpu_reg_byte_55 ();
  cpu_reg_byte cpu_reg_byte_56 ();
  cpu_reg_byte cpu_reg_byte_57 ();
  cpu_reg_byte cpu_reg_byte_58 ();
  cpu_reg_byte cpu_reg_byte_59 ();
  cpu_reg_byte cpu_reg_byte_60 ();
  cpu_reg_byte cpu_reg_byte_61 ();
  cpu_reg_byte cpu_reg_byte_62 ();
  cpu_reg_byte cpu_reg_byte_63 ();
  cpu_reg_byte cpu_reg_byte_64 ();
  // cpu_reg_byte cpu_reg_byte_65: pin names not known; wires that end beside it: cpu_decoder_4x16_1_o[0], cpu_decoder_4x16_2_o[11], s, e, o, reg_5, i, reset
  // cpu_reg_byte cpu_reg_byte_66: pin names not known; wires that end beside it: cpu_decoder_4x16_1_o[1], cpu_decoder_4x16_2_o[11], s, e, cpu_decoder_4x16_1_o[2], cpu_decoder_4x16_2_o[11], s, o, reg_21, i, reset, o, reg_37, i, reset
  cpu_reg_byte cpu_reg_byte_67 ();
  cpu_reg_byte cpu_reg_byte_68 ();
  cpu_reg_byte cpu_reg_byte_69 ();
  cpu_reg_byte cpu_reg_byte_70 ();
  cpu_reg_byte cpu_reg_byte_71 ();
  cpu_reg_byte cpu_reg_byte_72 ();
  cpu_reg_byte cpu_reg_byte_73 ();
  cpu_reg_byte cpu_reg_byte_74 ();
  cpu_reg_byte cpu_reg_byte_75 ();
  cpu_reg_byte cpu_reg_byte_76 ();
  cpu_reg_byte cpu_reg_byte_77 ();
  cpu_reg_byte cpu_reg_byte_78 ();
  cpu_reg_byte cpu_reg_byte_79 ();
  cpu_reg_byte cpu_reg_byte_80 ();
  // cpu_reg_byte cpu_reg_byte_81: pin names not known; wires that end beside it: cpu_decoder_4x16_1_o[0], cpu_decoder_4x16_2_o[10], s, e, o, reg_6, i, reset
  // cpu_reg_byte cpu_reg_byte_82: pin names not known; wires that end beside it: cpu_decoder_4x16_1_o[1], cpu_decoder_4x16_2_o[10], s, e, cpu_decoder_4x16_1_o[2], cpu_decoder_4x16_2_o[10], s, o, reg_22, i, reset, o, reg_38, i, reset
  cpu_reg_byte cpu_reg_byte_83 ();
  cpu_reg_byte cpu_reg_byte_84 ();
  cpu_reg_byte cpu_reg_byte_85 ();
  cpu_reg_byte cpu_reg_byte_86 ();
  cpu_reg_byte cpu_reg_byte_87 ();
  cpu_reg_byte cpu_reg_byte_88 ();
  cpu_reg_byte cpu_reg_byte_89 ();
  cpu_reg_byte cpu_reg_byte_90 ();
  cpu_reg_byte cpu_reg_byte_91 ();
  cpu_reg_byte cpu_reg_byte_92 ();
  cpu_reg_byte cpu_reg_byte_93 ();
  cpu_reg_byte cpu_reg_byte_94 ();
  cpu_reg_byte cpu_reg_byte_95 ();
  cpu_reg_byte cpu_reg_byte_96 ();
  // cpu_reg_byte cpu_reg_byte_97: pin names not known; wires that end beside it: cpu_decoder_4x16_1_o[0], cpu_decoder_4x16_2_o[9], s, e, o, reg_7, i, reset
  // cpu_reg_byte cpu_reg_byte_98: pin names not known; wires that end beside it: cpu_decoder_4x16_1_o[1], cpu_decoder_4x16_2_o[9], s, e, cpu_decoder_4x16_1_o[2], cpu_decoder_4x16_2_o[9], s, o, reg_23, i, reset, o, reg_39, i, reset
  cpu_reg_byte cpu_reg_byte_99 ();
  cpu_reg_byte cpu_reg_byte_100 ();
  cpu_reg_byte cpu_reg_byte_101 ();
  cpu_reg_byte cpu_reg_byte_102 ();
  cpu_reg_byte cpu_reg_byte_103 ();
  cpu_reg_byte cpu_reg_byte_104 ();
  cpu_reg_byte cpu_reg_byte_105 ();
  cpu_reg_byte cpu_reg_byte_106 ();
  cpu_reg_byte cpu_reg_byte_107 ();
  cpu_reg_byte cpu_reg_byte_108 ();
  cpu_reg_byte cpu_reg_byte_109 ();
  cpu_reg_byte cpu_reg_byte_110 ();
  cpu_reg_byte cpu_reg_byte_111 ();
  cpu_reg_byte cpu_reg_byte_112 ();
  // cpu_reg_byte cpu_reg_byte_113: pin names not known; wires that end beside it: cpu_decoder_4x16_1_o[0], cpu_decoder_4x16_2_o[8], s, e, o, reg_8, i, reset
  // cpu_reg_byte cpu_reg_byte_114: pin names not known; wires that end beside it: cpu_decoder_4x16_1_o[1], cpu_decoder_4x16_2_o[8], s, e, cpu_decoder_4x16_1_o[2], cpu_decoder_4x16_2_o[8], s, o, reg_24, i, reset, o, reg_40, i, reset
  cpu_reg_byte cpu_reg_byte_115 ();
  cpu_reg_byte cpu_reg_byte_116 ();
  cpu_reg_byte cpu_reg_byte_117 ();
  cpu_reg_byte cpu_reg_byte_118 ();
  cpu_reg_byte cpu_reg_byte_119 ();
  cpu_reg_byte cpu_reg_byte_120 ();
  cpu_reg_byte cpu_reg_byte_121 ();
  cpu_reg_byte cpu_reg_byte_122 ();
  cpu_reg_byte cpu_reg_byte_123 ();
  cpu_reg_byte cpu_reg_byte_124 ();
  cpu_reg_byte cpu_reg_byte_125 ();
  cpu_reg_byte cpu_reg_byte_126 ();
  cpu_reg_byte cpu_reg_byte_127 ();
  cpu_reg_byte cpu_reg_byte_128 ();
  // cpu_reg_byte cpu_reg_byte_129: pin names not known; wires that end beside it: cpu_decoder_4x16_1_o[0], cpu_decoder_4x16_2_o[7], s, e, o, reg_9, i, reset
  // cpu_reg_byte cpu_reg_byte_130: pin names not known; wires that end beside it: cpu_decoder_4x16_1_o[1], cpu_decoder_4x16_2_o[7], s, e, cpu_decoder_4x16_1_o[2], cpu_decoder_4x16_2_o[7], s, o, reg_25, i, reset, o, reg_41, i, reset
  cpu_reg_byte cpu_reg_byte_131 ();
  cpu_reg_byte cpu_reg_byte_132 ();
  cpu_reg_byte cpu_reg_byte_133 ();
  cpu_reg_byte cpu_reg_byte_134 ();
  cpu_reg_byte cpu_reg_byte_135 ();
  cpu_reg_byte cpu_reg_byte_136 ();
  cpu_reg_byte cpu_reg_byte_137 ();
  cpu_reg_byte cpu_reg_byte_138 ();
  cpu_reg_byte cpu_reg_byte_139 ();
  cpu_reg_byte cpu_reg_byte_140 ();
  cpu_reg_byte cpu_reg_byte_141 ();
  cpu_reg_byte cpu_reg_byte_142 ();
  cpu_reg_byte cpu_reg_byte_143 ();
  cpu_reg_byte cpu_reg_byte_144 ();
  cpu_decoder_4x16 cpu_decoder_4x16_2 (
    .A(cpu_mem_8_1_o[3]), .B(cpu_mem_8_1_o[2]), .C(cpu_mem_8_1_o[1]), .D(cpu_mem_8_1_o[0]),
    .O(cpu_decoder_4x16_2_o));
  // cpu_reg_byte cpu_reg_byte_145: pin names not known; wires that end beside it: cpu_decoder_4x16_1_o[0], cpu_decoder_4x16_2_o[6], s, e, o, reg_10, i, reset
  // cpu_reg_byte cpu_reg_byte_146: pin names not known; wires that end beside it: cpu_decoder_4x16_1_o[1], cpu_decoder_4x16_2_o[6], s, e, cpu_decoder_4x16_1_o[2], cpu_decoder_4x16_2_o[6], s, o, reg_26, i, reset, o, reg_42, i, reset
  cpu_reg_byte cpu_reg_byte_147 ();
  cpu_reg_byte cpu_reg_byte_148 ();
  cpu_reg_byte cpu_reg_byte_149 ();
  cpu_reg_byte cpu_reg_byte_150 ();
  cpu_reg_byte cpu_reg_byte_151 ();
  cpu_reg_byte cpu_reg_byte_152 ();
  cpu_reg_byte cpu_reg_byte_153 ();
  cpu_reg_byte cpu_reg_byte_154 ();
  cpu_reg_byte cpu_reg_byte_155 ();
  cpu_reg_byte cpu_reg_byte_156 ();
  cpu_reg_byte cpu_reg_byte_157 ();
  cpu_reg_byte cpu_reg_byte_158 ();
  cpu_reg_byte cpu_reg_byte_159 ();
  cpu_reg_byte cpu_reg_byte_160 ();
  // cpu_reg_byte cpu_reg_byte_161: pin names not known; wires that end beside it: cpu_decoder_4x16_1_o[0], cpu_decoder_4x16_2_o[5], s, e, o, reg_11, i, reset
  // cpu_reg_byte cpu_reg_byte_162: pin names not known; wires that end beside it: cpu_decoder_4x16_1_o[1], cpu_decoder_4x16_2_o[5], s, e, cpu_decoder_4x16_1_o[2], cpu_decoder_4x16_2_o[5], s, o, reg_27, i, reset, o, reg_43, i, reset
  cpu_reg_byte cpu_reg_byte_163 ();
  cpu_reg_byte cpu_reg_byte_164 ();
  cpu_reg_byte cpu_reg_byte_165 ();
  cpu_reg_byte cpu_reg_byte_166 ();
  cpu_reg_byte cpu_reg_byte_167 ();
  cpu_reg_byte cpu_reg_byte_168 ();
  cpu_reg_byte cpu_reg_byte_169 ();
  cpu_reg_byte cpu_reg_byte_170 ();
  cpu_reg_byte cpu_reg_byte_171 ();
  cpu_reg_byte cpu_reg_byte_172 ();
  cpu_reg_byte cpu_reg_byte_173 ();
  cpu_reg_byte cpu_reg_byte_174 ();
  cpu_reg_byte cpu_reg_byte_175 ();
  cpu_reg_byte cpu_reg_byte_176 ();
  // cpu_reg_byte cpu_reg_byte_177: pin names not known; wires that end beside it: cpu_decoder_4x16_1_o[0], cpu_decoder_4x16_2_o[4], s, e, o, reg_12, i, reset
  // cpu_reg_byte cpu_reg_byte_178: pin names not known; wires that end beside it: cpu_decoder_4x16_1_o[1], cpu_decoder_4x16_2_o[4], s, e, cpu_decoder_4x16_1_o[2], cpu_decoder_4x16_2_o[4], s, o, reg_28, i, reset, o, reg_44, i, reset
  cpu_reg_byte cpu_reg_byte_179 ();
  cpu_reg_byte cpu_reg_byte_180 ();
  cpu_reg_byte cpu_reg_byte_181 ();
  cpu_reg_byte cpu_reg_byte_182 ();
  cpu_reg_byte cpu_reg_byte_183 ();
  cpu_reg_byte cpu_reg_byte_184 ();
  cpu_reg_byte cpu_reg_byte_185 ();
  cpu_reg_byte cpu_reg_byte_186 ();
  cpu_reg_byte cpu_reg_byte_187 ();
  cpu_reg_byte cpu_reg_byte_188 ();
  cpu_reg_byte cpu_reg_byte_189 ();
  cpu_reg_byte cpu_reg_byte_190 ();
  cpu_reg_byte cpu_reg_byte_191 ();
  cpu_reg_byte cpu_reg_byte_192 ();
  // cpu_reg_byte cpu_reg_byte_193: pin names not known; wires that end beside it: cpu_decoder_4x16_1_o[0], cpu_decoder_4x16_2_o[3], s, e, o, reg_13, i, reset
  // cpu_reg_byte cpu_reg_byte_194: pin names not known; wires that end beside it: cpu_decoder_4x16_1_o[1], cpu_decoder_4x16_2_o[3], s, e, cpu_decoder_4x16_1_o[2], cpu_decoder_4x16_2_o[3], s, o, reg_29, i, reset, o, reg_45, i, reset
  cpu_reg_byte cpu_reg_byte_195 ();
  cpu_reg_byte cpu_reg_byte_196 ();
  cpu_reg_byte cpu_reg_byte_197 ();
  cpu_reg_byte cpu_reg_byte_198 ();
  cpu_reg_byte cpu_reg_byte_199 ();
  cpu_reg_byte cpu_reg_byte_200 ();
  cpu_reg_byte cpu_reg_byte_201 ();
  cpu_reg_byte cpu_reg_byte_202 ();
  cpu_reg_byte cpu_reg_byte_203 ();
  cpu_reg_byte cpu_reg_byte_204 ();
  cpu_reg_byte cpu_reg_byte_205 ();
  cpu_reg_byte cpu_reg_byte_206 ();
  cpu_reg_byte cpu_reg_byte_207 ();
  cpu_reg_byte cpu_reg_byte_208 ();
  // cpu_reg_byte cpu_reg_byte_209: pin names not known; wires that end beside it: cpu_decoder_4x16_1_o[0], cpu_decoder_4x16_2_o[2], s, e, o, reg_14, i, reset
  // cpu_reg_byte cpu_reg_byte_210: pin names not known; wires that end beside it: cpu_decoder_4x16_1_o[1], cpu_decoder_4x16_2_o[2], s, e, cpu_decoder_4x16_1_o[2], cpu_decoder_4x16_2_o[2], s, o, reg_30, i, reset, o, reg_46, i, reset
  cpu_reg_byte cpu_reg_byte_211 ();
  cpu_reg_byte cpu_reg_byte_212 ();
  cpu_reg_byte cpu_reg_byte_213 ();
  cpu_reg_byte cpu_reg_byte_214 ();
  cpu_reg_byte cpu_reg_byte_215 ();
  cpu_reg_byte cpu_reg_byte_216 ();
  cpu_reg_byte cpu_reg_byte_217 ();
  cpu_reg_byte cpu_reg_byte_218 ();
  cpu_reg_byte cpu_reg_byte_219 ();
  cpu_reg_byte cpu_reg_byte_220 ();
  cpu_reg_byte cpu_reg_byte_221 ();
  cpu_reg_byte cpu_reg_byte_222 ();
  cpu_reg_byte cpu_reg_byte_223 ();
  cpu_reg_byte cpu_reg_byte_224 ();
  // cpu_reg_byte cpu_reg_byte_225: pin names not known; wires that end beside it: cpu_decoder_4x16_1_o[0], cpu_decoder_4x16_2_o[1], s, e, o, reg_15, i, reset
  // cpu_reg_byte cpu_reg_byte_226: pin names not known; wires that end beside it: cpu_decoder_4x16_1_o[1], cpu_decoder_4x16_2_o[1], s, e, cpu_decoder_4x16_1_o[2], cpu_decoder_4x16_2_o[1], s, o, reg_31, i, reset
  cpu_reg_byte cpu_reg_byte_227 ();
  cpu_reg_byte cpu_reg_byte_228 ();
  cpu_reg_byte cpu_reg_byte_229 ();
  cpu_reg_byte cpu_reg_byte_230 ();
  cpu_reg_byte cpu_reg_byte_231 ();
  cpu_reg_byte cpu_reg_byte_232 ();
  cpu_reg_byte cpu_reg_byte_233 ();
  cpu_reg_byte cpu_reg_byte_234 ();
  cpu_reg_byte cpu_reg_byte_235 ();
  cpu_reg_byte cpu_reg_byte_236 ();
  cpu_reg_byte cpu_reg_byte_237 ();
  cpu_reg_byte cpu_reg_byte_238 ();
  cpu_reg_byte cpu_reg_byte_239 ();
  cpu_reg_byte cpu_reg_byte_240 ();
  // cpu_reg_byte cpu_reg_byte_241: pin names not known; wires that end beside it: cpu_decoder_4x16_1_o[0], cpu_decoder_4x16_2_o[0], s, e, o, reg_16, i, reset
  // cpu_reg_byte cpu_reg_byte_242: pin names not known; wires that end beside it: cpu_decoder_4x16_1_o[1], cpu_decoder_4x16_2_o[0], s, e, o, reg_32, i, reset
  // cpu_reg_byte cpu_reg_byte_243: pin names not known; wires that end beside it: o, reg_47, i, reset, cpu_decoder_4x16_1_o[2], cpu_decoder_4x16_2_o[0], s, e, o, reg_48, i, reset
  // cpu_reg_byte cpu_reg_byte_244: pin names not known; wires that end beside it: cpu_decoder_4x16_1_o[3], cpu_decoder_4x16_2_o[1], s, o, reg_63, i, reset, cpu_decoder_4x16_1_o[3], cpu_decoder_4x16_2_o[0], s, e, o, reg_64, i, reset
  // cpu_reg_byte cpu_reg_byte_245: pin names not known; wires that end beside it: cpu_decoder_4x16_1_o[4], cpu_decoder_4x16_2_o[1], s, o, reg_79, i, reset, cpu_decoder_4x16_1_o[4], cpu_decoder_4x16_2_o[0], s, e, o, reg_80, i, reset
  // cpu_reg_byte cpu_reg_byte_246: pin names not known; wires that end beside it: cpu_decoder_4x16_1_o[5], cpu_decoder_4x16_2_o[1], s, o, reg_95, i, reset, cpu_decoder_4x16_1_o[5], cpu_decoder_4x16_2_o[0], s, e, o, reg_96, i, reset
  // cpu_reg_byte cpu_reg_byte_247: pin names not known; wires that end beside it: cpu_decoder_4x16_1_o[6], cpu_decoder_4x16_2_o[1], s, o, reg_111, i, reset, cpu_decoder_4x16_1_o[6], cpu_decoder_4x16_2_o[0], s, e, o, reg_112, i, reset
  // cpu_reg_byte cpu_reg_byte_248: pin names not known; wires that end beside it: cpu_decoder_4x16_1_o[7], cpu_decoder_4x16_2_o[1], s, o, reg_127, i, reset, cpu_decoder_4x16_1_o[7], cpu_decoder_4x16_2_o[0], s, e, o, reg_128, i, reset
  // cpu_reg_byte cpu_reg_byte_249: pin names not known; wires that end beside it: cpu_decoder_4x16_1_o[8], cpu_decoder_4x16_2_o[1], s, o, reg_143, i, reset, cpu_decoder_4x16_1_o[8], cpu_decoder_4x16_2_o[0], s, e, o, reg_144, i, reset
  // cpu_reg_byte cpu_reg_byte_250: pin names not known; wires that end beside it: cpu_decoder_4x16_1_o[9], cpu_decoder_4x16_2_o[1], s, o, reg_159, i, reset, cpu_decoder_4x16_1_o[9], cpu_decoder_4x16_2_o[0], s, e, o, reg_160, i, reset
  // cpu_reg_byte cpu_reg_byte_251: pin names not known; wires that end beside it: cpu_decoder_4x16_1_o[10], cpu_decoder_4x16_2_o[1], s, o, reg_175, i, reset, cpu_decoder_4x16_1_o[10], cpu_decoder_4x16_2_o[0], s, e, o, reg_176, i, reset
  // cpu_reg_byte cpu_reg_byte_252: pin names not known; wires that end beside it: cpu_decoder_4x16_1_o[11], cpu_decoder_4x16_2_o[1], s, o, reg_191, i, reset, cpu_decoder_4x16_1_o[11], cpu_decoder_4x16_2_o[0], s, e, o, reg_192, i, reset
  // cpu_reg_byte cpu_reg_byte_253: pin names not known; wires that end beside it: cpu_decoder_4x16_1_o[12], cpu_decoder_4x16_2_o[1], s, o, reg_207, i, reset, cpu_decoder_4x16_1_o[12], cpu_decoder_4x16_2_o[0], s, e, o, reg_208, i, reset
  // cpu_reg_byte cpu_reg_byte_254: pin names not known; wires that end beside it: cpu_decoder_4x16_1_o[13], cpu_decoder_4x16_2_o[1], s, o, reg_223, i, reset, cpu_decoder_4x16_1_o[13], cpu_decoder_4x16_2_o[0], s, e, o, reg_224, i, reset
  // cpu_reg_byte cpu_reg_byte_255: pin names not known; wires that end beside it: cpu_decoder_4x16_1_o[14], cpu_decoder_4x16_2_o[1], s, o, reg_239, i, reset, cpu_decoder_4x16_1_o[14], cpu_decoder_4x16_2_o[0], s, e, o, reg_240, i, reset
  // cpu_reg_byte cpu_reg_byte_256: pin names not known; wires that end beside it: cpu_decoder_4x16_1_o[15], cpu_decoder_4x16_2_o[1], s, o, reg_255, i, reset, cpu_decoder_4x16_1_o[15], cpu_decoder_4x16_2_o[0], s, e, o, reg_256, i, reset
endmodule
