// Digital circuit CPU_ADD2.dig as structural Verilog
module CPU_ADD2 (
  input  S,
  input  [7:0] I,
  input  [7:0] I_2,
  input  RES,
  input  R_0,
  input  R_1,
  input  R_2,
  input  clk,
  output [7:0] out_8,
  output [7:0] out_9,
  output [7:0] out_10,
  output [7:0] out_11
);

  wire cpu_accumulator_1_p4, cpu_accumulator_1_p5, cpu_accumulator_1_p7, cpu_accumulator_1_p8,
       cpu_ram_256_1_p1, cpu_ram_256_1_p7, R_0_p3, R_0_p5, R_0_p6, R_0_p8, R_1_p8, R_1_p11, R_2_p2, R_3_p3,
       TEMP_p2;
  wire [7:0] TEMP_p3;

  LED led_1 (.in(TEMP_p2));
  // CPU_MEM_8 TEMP: pin names not known; wires that end beside it: out_8, TEMP_p2, TEMP_p3, out_8, out_11, 1'b0, R_0, R_1, out_11
  CPU_ALU cpu_alu_1 ();
  CPU_BUS_1 cpu_bus_1_1 (.I(TEMP_p3), .S_1(S));  // open: O
  LED led_2 (.in(cpu_accumulator_1_p4));
  LED led_3 (.in(cpu_accumulator_1_p5));
  // CPU_ACCUMULATOR cpu_accumulator_1: pin names not known; wires that end beside it: R_2, out_9, out_9, cpu_accumulator_1_p4, cpu_accumulator_1_p5, out_8, cpu_accumulator_1_p7, cpu_accumulator_1_p8
  // CPU_REGISTER_8 R_0: pin names not known; wires that end beside it: I, 1'b1, R_0_p3, clk, R_0_p5, R_0_p6, out_8, R_0_p8
  LED led_4 (.in(R_0_p3));
  CPU_CLK cpu_clk_1 ();
  LED led_5 (.in(cpu_accumulator_1_p7));
  // CPU_REGISTER_8 R_1: pin names not known; wires that end beside it: I_2, 1'b1, cpu_accumulator_1_p7, R_0_p6, R_0_p8, R_0_p5, cpu_accumulator_1_p5, R_1_p8, R_0_p3, out_8, R_1_p11
  CPU_CONTROL cpu_control_1 ();
  // CPU_REGISTER_8 R_2: pin names not known; wires that end beside it: out_8, R_2_p2, cpu_accumulator_1_p8, out_8
  LED led_6 (.in(R_1_p11));
  // CPU_REGISTER_8 R_3: pin names not known; wires that end beside it: out_8, R_1_p11, R_3_p3, out_8
  LED led_7 (.in(R_3_p3));
  // CPU_RAM_256 cpu_ram_256_1: pin names not known; wires that end beside it: cpu_ram_256_1_p1, out_8, out_8, RES, out_8, R_1_p8, cpu_ram_256_1_p7

  assign out_10 = out_8;

  // Notes on the sheet:
  //   clk: Hz: 2147483647
endmodule
