// Digital circuit CPU_ADD2_DEBUG.dig as structural Verilog
module CPU_ADD2_DEBUG (
  input  [7:0] I,
  input  [7:0] I_2,
  input  RES,
  input  R_0,
  input  R_1,
  input  R_2,
  input  CLK,
  input  in_12,
  output [7:0] out_8,
  output [7:0] out_9,
  output [7:0] out_10,
  output [7:0] out_11
);

  wire cpu_accumulator_1_p3, cpu_accumulator_1_p4, cpu_accumulator_1_p6, cpu_accumulator_1_p7,
       cpu_ram_256_1_p1, cpu_ram_256_1_p7, R_0_p3, R_0_p5, R_0_p6, R_0_p8, R_1_p8, R_1_p11, R_2_p2, R_3_p3,
       TEMP_p2, undriven;

  LED led_1 (.in(TEMP_p2));
  // CPU_REGISTER_8 TEMP: pin names not known; wires that end beside it: out_8, TEMP_p2, in_12, out_8, {8{1'b1}}, 1'b0, R_0, R_1, R_2, out_11
  CPU_ALU cpu_alu_1 ();
  LED led_2 (.in(cpu_accumulator_1_p3));
  LED led_3 (.in(cpu_accumulator_1_p4));
  // CPU_ACCUMULATOR cpu_accumulator_1: pin names not known; wires that end beside it: out_9, out_9, cpu_accumulator_1_p3, cpu_accumulator_1_p4, out_8, cpu_accumulator_1_p6, cpu_accumulator_1_p7
  // CPU_REGISTER_8 R_0: pin names not known; wires that end beside it: I, 1'b1, R_0_p3, CLK, R_0_p5, R_0_p6, out_8, R_0_p8
  LED led_4 (.in(R_0_p3));
  and and_1 (TEMP_p2, cpu_accumulator_1_p6, undriven);
  CPU_CLK cpu_clk_1 ();
  LED led_5 (.in(cpu_accumulator_1_p6));
  // CPU_REGISTER_8 R_1: pin names not known; wires that end beside it: I_2, 1'b1, cpu_accumulator_1_p6, R_0_p6, R_0_p8, R_0_p5, cpu_accumulator_1_p4, R_1_p8, R_0_p3, out_8, R_1_p11
  CPU_CONTROL cpu_control_1 ();
  // CPU_REGISTER_8 R_2: pin names not known; wires that end beside it: out_8, R_2_p2, cpu_accumulator_1_p7, out_8
  LED led_6 (.in(R_1_p11));
  // CPU_REGISTER_8 R_3: pin names not known; wires that end beside it: out_8, R_1_p11, R_3_p3, out_8
  LED led_7 (.in(R_3_p3));
  // CPU_RAM_256 cpu_ram_256_1: pin names not known; wires that end beside it: cpu_ram_256_1_p1, out_8, out_8, RES, out_8, R_1_p8, cpu_ram_256_1_p7

  assign out_10 = out_8;
endmodule
