// Digital circuit CPU_CLK.dig as structural Verilog
module CPU_CLK (
  input  Clk_in,
  output Clk_s,
  output Clk_out,
  output Clk_e
);

  wire jk_ff_1_nq, nand_1_out, not_1_out, not_2_out;

  not not_1 (not_1_out, Clk_in);
  not not_2 (not_2_out, not_1_out);
  JK_FF jk_ff_1 (.J(1'b1), .C(Clk_in), .K(1'b1), .Q(Clk_out), .nQ(jk_ff_1_nq));
  nand nand_1 (nand_1_out, not_2_out, Clk_out);
  nand nand_2 (Clk_e, jk_ff_1_nq, Clk_in);
  not not_3 (Clk_s, nand_1_out);
endmodule
