// Digital circuit CPU_DECODER_4x16.dig as structural Verilog
module CPU_DECODER_4x16 (
  input  A_lsb,
  input  B,
  input  C,
  input  D_msb,
  output [15:0] O
);

  wire not_1_out, not_2_out, not_3_out, not_4_out;

  not not_1 (not_1_out, D_msb);
  not not_2 (not_2_out, C);
  not not_3 (not_3_out, B);
  not not_4 (not_4_out, A_lsb);
  and and_1 (O[0], not_1_out, not_2_out, not_3_out, not_4_out);
  and and_2 (O[1], not_1_out, not_2_out, not_3_out, A_lsb);
  and and_3 (O[2], not_1_out, not_2_out, B, not_4_out);
  and and_4 (O[3], not_1_out, not_2_out, B, A_lsb);
  and and_5 (O[4], not_1_out, C, not_3_out, not_4_out);
  and and_6 (O[5], not_1_out, C, not_3_out, A_lsb);
  and and_7 (O[6], not_1_out, C, B, not_4_out);
  and and_8 (O[7], not_1_out, C, B, A_lsb);
  and and_9 (O[8], D_msb, not_2_out, not_3_out, not_4_out);
  and and_10 (O[9], D_msb, not_2_out, not_3_out, A_lsb);
  and and_11 (O[10], D_msb, not_2_out, B, not_4_out);
  and and_12 (O[11], D_msb, not_2_out, B, A_lsb);
  and and_13 (O[12], D_msb, C, not_3_out, not_4_out);
  and and_14 (O[13], D_msb, C, not_3_out, A_lsb);
  and and_15 (O[14], D_msb, C, B, not_4_out);
  and and_16 (O[15], D_msb, C, B, A_lsb);
endmodule
