// Digital circuit CPU_ENABLE_8.dig as structural Verilog
module CPU_ENABLE_8 (
  input  [7:0] I,
  input  E,
  output [7:0] O
);

  wire and_1_out, and_2_out, and_3_out, and_4_out, and_5_out, and_6_out, and_7_out, and_8_out;

  and and_1 (and_1_out, I[0], E);
  and and_2 (and_2_out, I[1], E);
  and and_3 (and_3_out, I[2], E);
  and and_4 (and_4_out, I[3], E);
  and and_5 (and_5_out, I[4], E);
  and and_6 (and_6_out, I[5], E);
  and and_7 (and_7_out, I[6], E);
  and and_8 (and_8_out, I[7], E);
  assign O[0] = E ? and_1_out : 1'bz;  // Driver driver_1
  assign O[1] = E ? and_2_out : 1'bz;  // Driver driver_2
  assign O[2] = E ? and_3_out : 1'bz;  // Driver driver_3
  assign O[3] = E ? and_4_out : 1'bz;  // Driver driver_4
  assign O[4] = E ? and_5_out : 1'bz;  // Driver driver_5
  assign O[5] = E ? and_6_out : 1'bz;  // Driver driver_6
  assign O[6] = E ? and_7_out : 1'bz;  // Driver driver_7
  assign O[7] = E ? and_8_out : 1'bz;  // Driver driver_8
endmodule
