// Digital circuit CPU_MEM_8.dig as structural Verilog
module CPU_MEM_8 (
  input  [7:0] I,
  input  E,
  output [7:0] O
);

  CPU_MEM_1 cpu_mem_1_1 (.S(I[0]), .E(E));  // open: O
  CPU_MEM_1 cpu_mem_1_2 (.S(I[1]), .E(E));  // open: O
  CPU_MEM_1 cpu_mem_1_3 (.S(I[2]), .E(E));  // open: O
  CPU_MEM_1 cpu_mem_1_4 (.S(I[3]), .E(E));  // open: O
  CPU_MEM_1 cpu_mem_1_5 (.S(I[4]), .E(E));  // open: O
  CPU_MEM_1 cpu_mem_1_6 (.S(I[5]), .E(E));  // open: O
  CPU_MEM_1 cpu_mem_1_7 (.S(I[6]), .E(E));  // open: O
  CPU_MEM_1 cpu_mem_1_8 (.S(I[7]), .E(E));  // open: O
endmodule
