// Digital circuit CPU_OR.dig as structural Verilog
module CPU_OR (
  input  [7:0] A,
  input  [7:0] B,
  output [7:0] O
);

  or or_1 (O[0], A[0], B[0]);
  or or_2 (O[1], A[1], B[1]);
  or or_3 (O[2], A[2], B[2]);
  or or_4 (O[3], A[3], B[3]);
  or or_5 (O[4], A[4], B[4]);
  or or_6 (O[5], A[5], B[5]);
  or or_7 (O[6], A[6], B[6]);
  or or_8 (O[7], A[7], B[7]);
endmodule
