// Digital circuit CPU_SHR.dig as structural Verilog
module CPU_SHR (
  input  Shft_in,
  input  [7:0] I,
  output Shft_out,
  output [7:0] O
);

  wire [7:1] cpu_register_8_1_p4;

  // CPU_REGISTER_8 cpu_register_8_1: pin names not known; wires that end beside it: I, 1'b1, 1'b1, {cpu_register_8_1_p4, Shft_out}
  // CPU_REGISTER_8 cpu_register_8_2: pin names not known; wires that end beside it: {Shft_in, cpu_register_8_1_p4}, 1'b1, 1'b1, O
endmodule
