// Digital circuit CPU_TMP.dig as structural Verilog
module CPU_TMP (
  input  [7:0] I,
  input  S,
  output [7:0] O
);

  wire [7:0] driver_1_out;

  assign driver_1_out = S ? I : 8'bz;  // Driver driver_1
  // CPU_MEM_8 cpu_mem_8_1: pin names not known; wires that end beside it: driver_1_out, S, O
endmodule
