// Digital circuit OSCILL_SOLUTION.dig as structural Verilog
module OSCILL_SOLUTION (
  input  Clk_in,
  input  Clk_in_2,
  output O,
  output O_2
);

  wire jk_ff_1_q, jk_ff_2_q, nand_1_out, nand_2_out, nand_3_out, nand_4_out, nand_5_out, nand_6_out,
       nand_8_out, nand_10_out, not_1_out, not_2_out, not_3_out, not_4_out;

  not not_1 (not_1_out, Clk_in_2);
  JK_FF jk_ff_1 (.J(1'b1), .C(Clk_in), .K(1'b1), .Q(jk_ff_1_q));  // open: nQ
  not not_2 (not_2_out, not_1_out);
  JK_FF jk_ff_2 (.J(1'b1), .C(Clk_in_2), .K(1'b1), .Q(jk_ff_2_q));  // open: nQ
  nand nand_1 (nand_1_out, Clk_in, jk_ff_1_q);
  nand nand_2 (nand_2_out, not_2_out, jk_ff_2_q);
  not not_3 (not_3_out, nand_1_out);
  not not_4 (not_4_out, nand_2_out);
  nand nand_3 (nand_3_out, 1'b1, not_3_out);
  nand nand_4 (nand_4_out, 1'b1, not_4_out);
  nand nand_5 (nand_5_out, nand_3_out, not_3_out);
  nand nand_6 (nand_6_out, nand_4_out, not_4_out);
  nand nand_7 (O, nand_3_out, nand_8_out);
  nand nand_8 (nand_8_out, O, nand_5_out);
  nand nand_9 (O_2, nand_4_out, nand_10_out);
  nand nand_10 (nand_10_out, O_2, nand_6_out);
endmodule
