// Digital circuit CPU_ALU_INSTRUCTION_WITH_RESET.dig as structural Verilog
module CPU_ALU_INSTRUCTION_WITH_RESET (
  input  clk,
  input  [7:0] IR_in,
  input  [7:0] IN,
  input  [7:0] IN_2
);

  wire Acc_p1, Acc_p3, Acc_p4, IAR_p1, IAR_p3, IAR_p5, IR_p3, Memory_p1, Memory_p4, Memory_p6, Memory_p7,
       R_0_p2, R_0_p3, R_1_p2, R_1_p3, R_1_p5, R_2_p3, R_2_p5, R_3_p3, Reset_0_out, TEMP_p2, TEMP_p5,
       TEMP_p7, undriven, undriven_2;
  wire [7:0] TEMP_p1, TEMP_p3;

  // CPU_MEM_8 TEMP: pin names not known; wires that end beside it: TEMP_p1, TEMP_p2, TEMP_p3, TEMP_p1, TEMP_p5, 1'b0, TEMP_p7, TEMP_p5
  LED led_1 (.in(TEMP_p2));
  CPU_ALU ALU ();
  LED led_2 (.in(R_1_p5));
  CPU_BUS_1 Bus (.I(TEMP_p3), .S_1(R_1_p5));  // open: O
  LED led_3 (.in(Acc_p3));
  LED led_4 (.in(Acc_p4));
  // CPU_ACCUMULATOR Acc: pin names not known; wires that end beside it: Acc_p1, Acc_p1, Acc_p3, Acc_p4, TEMP_p1
  CPU_CLK Clock ();
  LED led_5 (.in(R_0_p2));
  LED led_6 (.in(R_0_p3));
  // CPU_REGISTER_8 R_0: pin names not known; wires that end beside it: TEMP_p1, R_0_p2, R_0_p3, TEMP_p1
  LED led_7 (.in(R_1_p2));
  LED led_8 (.in(R_1_p3));
  CPU_CONTROL Control ();
  // CPU_REGISTER_8 R_1: pin names not known; wires that end beside it: TEMP_p1, R_1_p2, R_1_p3, TEMP_p1, R_1_p5
  Button Reset_0 (.out(Reset_0_out));
  LED led_9 (.in(IAR_p1));
  LED led_10 (.in(undriven_2));
  RESET1 reset1_1 (.Set_1(Reset_0_out), .Line_in(undriven));  // open: Line_out
  LED led_11 (.in(IAR_p3));
  // CPU_REGISTER_8 IAR: pin names not known; wires that end beside it: IAR_p1, TEMP_p1, IAR_p3, IAR_p3, IAR_p5, IAR_p5
  // CPU_REGISTER_8 R_2: pin names not known; wires that end beside it: IN, 1'b1, R_2_p3, TEMP_p1, R_2_p5
  LED led_12 (.in(R_2_p3));
  RESET8 reset8_1 (.Reset_0(Reset_0_out), .Bus_in(TEMP_p1));  // open: Bus_out
  LED led_13 (.in(R_2_p5));
  // CPU_MEM_8 IR: pin names not known; wires that end beside it: IR_in, 1'b1, IR_p3
  // CPU_REGISTER_8 R_3: pin names not known; wires that end beside it: IN_2, 1'b1, R_3_p3, TEMP_p1
  LED led_14 (.in(R_3_p3));
  LED led_15 (.in(1'b1));
  // CPU_RAM_256 Memory: pin names not known; wires that end beside it: Memory_p1, TEMP_p1, TEMP_p1, Memory_p4, TEMP_p1, Memory_p6, Memory_p7
  Button button_1 (.out(Memory_p4));

  // Notes on the sheet:
  //   clk: Hz: 2147483647
endmodule
