// Digital circuit CPU_CONTROL.dig as structural Verilog
module CPU_CONTROL (
  input  CLK,
  input  CLK_E,
  input  CLK_S,
  input  [7:0] IR_IN,
  output ACC_S,
  output MAR_S,
  output RAM_S,
  output TMP_S,
  output R0_S,
  output R1_S,
  output R2_S,
  output R3_S,
  output BUS_1,
  output ACC_E,
  output RAM_E,
  output IAR_E,
  output IOCLK_E,
  output R0_E,
  output R1_E,
  output R2_E,
  output R3_E,
  output ALU_0,
  output ALU_1,
  output ALU_2,
  output IR_S,
  output IAR_S,
  output FLAGS_S,
  output IOCLK_S
);

  wire ACC_E_t, ACC_S_t, and_5_out, and_6_out, and_7_out, and_8_out, and_9_out, and_10_out, and_11_out,
       and_12_out, and_18_out, not_1_out, REGB_E, undriven, undriven_2, undriven_3, undriven_4, undriven_5,
       undriven_6, undriven_7, undriven_8, undriven_9, undriven_10, undriven_11, undriven_12, undriven_13,
       undriven_14, undriven_15;

  or or_1 (R0_E, and_9_out, and_5_out);
  or or_2 (R1_E, and_10_out, and_6_out);
  or or_3 (R2_E, and_11_out, and_7_out);
  or or_4 (R3_E, and_12_out, and_8_out);
  and and_1 (IAR_E, 1'b0, CLK_E);
  and and_2 (RAM_E, 1'b0, CLK_E);
  and and_3 (ACC_E, ACC_E_t, CLK_E);
  and and_4 (IOCLK_E, 1'b0, CLK_E);
  and and_5 (and_5_out, undriven, REGB_E, CLK_E);
  and and_6 (and_6_out, undriven_2, REGB_E, CLK_E);
  and and_7 (and_7_out, undriven_3, REGB_E, CLK_E);
  and and_8 (and_8_out, undriven_4, REGB_E, CLK_E);
  and and_9 (and_9_out, undriven_5, ACC_S_t, CLK_E);
  and and_10 (and_10_out, undriven_6, ACC_S_t, CLK_E);
  and and_11 (and_11_out, undriven_7, ACC_S_t, CLK_E);
  and and_12 (and_12_out, undriven_8, ACC_S_t, CLK_E);
  and and_13 (ALU_0, IR_IN[6], IR_IN[7], undriven_10);
  and and_14 (ALU_1, IR_IN[5], IR_IN[7], undriven_10);
  and and_15 (ALU_2, IR_IN[4], IR_IN[7], undriven_10);
  and and_16 (REGB_E, undriven_9, IR_IN[7]);
  CPU_DECODER_2x4 REG_B ();
  CPU_DECODER_2x4 REG_A ();
  and and_17 (ACC_S_t, undriven_10, IR_IN[7]);
  CPU_STEPPER cpu_stepper_1 ();
  and and_18 (and_18_out, IR_IN[6], IR_IN[5], IR_IN[4]);
  not not_1 (not_1_out, and_18_out);
  and and_19 (ACC_E_t, undriven_11, IR_IN[7], not_1_out);
  CPU_DECODER_2x4 cpu_decoder_2x4_1 ();
  and and_20 (IR_S, CLK_S, 1'b0);
  and and_21 (MAR_S, CLK_S, 1'b0);
  and and_22 (IAR_S, CLK_S, 1'b0);
  and and_23 (ACC_S, CLK_S, ACC_S_t);
  and and_24 (RAM_S, CLK_S, 1'b0);
  and and_25 (TMP_S, CLK_S, REGB_E);
  and and_26 (FLAGS_S, CLK_S, 1'b0);
  and and_27 (IOCLK_S, CLK_S, 1'b0);
  and and_28 (R0_S, CLK_S, ACC_E_t, undriven_12);
  and and_29 (R1_S, CLK_S, ACC_E_t, undriven_15);
  and and_30 (R2_S, CLK_S, ACC_E_t, undriven_14);
  and and_31 (R3_S, CLK_S, ACC_E_t, undriven_13);

  // Other names for the same wires on the sheet: REGA_E = ACC_S_t; REGB_S = ACC_E_t; TMP_S_t = REGB_E

  // Notes on the sheet:
  //   1
  //   2
  //   3
  //   4
  //   5
  //   6
endmodule
