// Digital circuit CPU_ALU.dig as structural Verilog
module CPU_ALU (
  input  [7:0] B,
  input  [7:0] A,
  input  C_in,
  input  A_2,
  input  B_2,
  input  C,
  output eq,
  output gt__A,
  output [7:0] O,
  output C_out,
  output Zero
);

  wire and_1_out, and_2_out, and_3_out, cpu_e_1_p2, cpu_e_2_p1, cpu_e_3_p1, cpu_e_4_p1, cpu_e_5_p1,
       cpu_e_6_p1, cpu_e_7_p1, undriven, undriven_2, undriven_3;
  wire [7:0] cpu_e_7_p2;

  CPU_XOR_LE_8 cpu_xor_le_8_1 ();
  CPU_OR cpu_or_1 (.A(A), .B(B));  // open: O
  CPU_AND cpu_and_1 (.A(A), .B(B));  // open: O
  CPU_NOT cpu_not_1 (.I(A));  // open: O
  CPU_SHL cpu_shl_1 ();
  CPU_SHR cpu_shr_1 ();
  CPU_ADDER_8 cpu_adder_8_1 ();
  CPU_DECODER_3x8 cpu_decoder_3x8_1 (.A_lsb(C), .C_msb(B_2));  // open: B, O
  // CPU_E cpu_e_1: pin names not known; wires that end beside it: eq, cpu_e_1_p2, cpu_e_7_p2[6], O
  // CPU_E cpu_e_2: pin names not known; wires that end beside it: cpu_e_2_p1, cpu_e_2_p1, cpu_e_7_p2[5], O
  // CPU_E cpu_e_3: pin names not known; wires that end beside it: cpu_e_3_p1, cpu_e_3_p1, cpu_e_7_p2[4], O
  // CPU_E cpu_e_4: pin names not known; wires that end beside it: cpu_e_4_p1, cpu_e_4_p1, cpu_e_7_p2[3], O
  // CPU_E cpu_e_5: pin names not known; wires that end beside it: cpu_e_5_p1, cpu_e_5_p1, cpu_e_7_p2[2], O
  // CPU_E cpu_e_6: pin names not known; wires that end beside it: cpu_e_6_p1, cpu_e_6_p1, cpu_e_7_p2[1], O
  // CPU_E cpu_e_7: pin names not known; wires that end beside it: cpu_e_7_p1, cpu_e_7_p2, A_2, cpu_e_7_p1, cpu_e_7_p2[0], O
  and and_1 (and_1_out, undriven, cpu_e_7_p2[2]);
  and and_2 (and_2_out, undriven_2, cpu_e_7_p2[1]);
  and and_3 (and_3_out, undriven_3, cpu_e_7_p2[0]);
  assign C_out = cpu_e_7_p2[2] ? and_1_out : 1'bz;  // Driver driver_1
  assign C_out = cpu_e_7_p2[1] ? and_2_out : 1'bz;  // Driver driver_2
  assign C_out = cpu_e_7_p2[0] ? and_3_out : 1'bz;  // Driver driver_3
  CPU_Z cpu_z_1 (.I(O));  // open: O
endmodule
