// Digital circuit CPU_BUS_1.dig as structural Verilog
module CPU_BUS_1 (
  input  [7:0] I,
  input  S_1,
  output [7:0] O
);

  wire not_1_out;

  and and_1 (O[7], not_1_out, I[7]);
  and and_2 (O[6], not_1_out, I[6]);
  and and_3 (O[5], not_1_out, I[5]);
  and and_4 (O[4], not_1_out, I[4]);
  and and_5 (O[3], not_1_out, I[3]);
  and and_6 (O[2], not_1_out, I[2]);
  and and_7 (O[1], not_1_out, I[1]);
  or or_1 (O[0], S_1, I[0]);
  not not_1 (not_1_out, S_1);
endmodule
