// Digital circuit CPU_CONTROL.dig as structural Verilog
module CPU_CONTROL (
  input  CLK,
  input  CLK_E,
  input  CLK_S,
  output ACC_E,
  output RAM_E,
  output R0_E,
  output R1_E,
  output R2_E,
  output R3_E,
  output ACC_S,
  output MAR_S,
  output RAM_S,
  output TMP_S,
  output R0_S,
  output R1_S,
  output R2_S,
  output R3_S
);

  wire undriven, undriven_2, undriven_3;

  and and_1 (RAM_E, 1'b0, CLK_E);
  and and_2 (ACC_E, undriven_3, CLK_E);
  and and_3 (R0_E, undriven_2, CLK_E);
  and and_4 (R1_E, undriven, CLK_E);
  and and_5 (R2_E, 1'b0, CLK_E);
  and and_6 (R3_E, 1'b0, CLK_E);
  CPU_STEPPER cpu_stepper_1 ();
  and and_7 (MAR_S, CLK_S, 1'b0);
  and and_8 (ACC_S, CLK_S, undriven_2);
  and and_9 (RAM_S, CLK_S, 1'b0);
  and and_10 (TMP_S, CLK_S, undriven);
  and and_11 (R0_S, CLK_S, 1'b0);
  and and_12 (R1_S, CLK_S, 1'b0);
  and and_13 (R2_S, CLK_S, 1'b0);
  and and_14 (R3_S, CLK_S, undriven_3);

  // Notes on the sheet:
  //   1
  //   2
  //   3
  //   4
  //   5
  //   6
endmodule
