// Digital circuit CPU_DECODER_3x8.dig as structural Verilog
module CPU_DECODER_3x8 (
  input  A_lsb,
  input  B,
  input  C_msb,
  output [7:0] O
);

  wire not_1_out, not_2_out, not_3_out;

  not not_1 (not_1_out, C_msb);
  not not_2 (not_2_out, B);
  not not_3 (not_3_out, A_lsb);
  and and_1 (O[0], not_1_out, not_2_out, not_3_out);
  and and_2 (O[1], not_1_out, not_2_out, A_lsb);
  and and_3 (O[2], not_1_out, B, not_3_out);
  and and_4 (O[3], not_1_out, B, A_lsb);
  and and_5 (O[4], C_msb, not_2_out, not_3_out);
  and and_6 (O[5], C_msb, not_2_out, A_lsb);
  and and_7 (O[6], C_msb, B, not_3_out);
  and and_8 (O[7], C_msb, B, A_lsb);
endmodule
