// Digital circuit CPU_DESIGN.dig as structural Verilog
module CPU_DESIGN (
  input  H,
  input  V,
  input  S,
  input  E,
  input  Reset,
  input  [7:0] I,
  output [7:0] O
);

  wire and_1_out, and_2_out, and_3_out, cpu_register_8_1_p4, or_1_out;

  and and_1 (and_1_out, H, V);
  and and_2 (and_2_out, and_1_out, S);
  and and_3 (and_3_out, and_1_out, E);
  or or_1 (or_1_out, Reset, and_2_out);
  // CPU_REGISTER_8 cpu_register_8_1: pin names not known; wires that end beside it: I, or_1_out, and_3_out, cpu_register_8_1_p4
  assign O[0] = and_3_out ? cpu_register_8_1_p4 : 1'bz;  // Driver driver_1
  // Pins of 1 and 8 bits meet at O
endmodule
