// Digital circuit CPU_CONTROL.dig as structural Verilog
module CPU_CONTROL (
  input  CLK,
  input  CLK_S,
  input  CLK_E,
  input  X,
  input  A,
  input  E,
  input  Z,
  input  RESET,
  input  MARS,
  input  LOAD,
  input  [7:0] IR_IN,
  output ALU_0,
  output ALU_1,
  output ALU_2,
  output C,
  output BUS_1,
  output TMP_S,
  output ACC_E,
  output ACC_S,
  output IOCLK_E,
  output IOCLK_S,
  output FLAGS_S,
  output R0_E,
  output R0_S,
  output R1_E,
  output R1_S,
  output R2_E,
  output R2_S,
  output R3_E,
  output R3_S,
  output IAR_E,
  output IAR_S,
  output RAM_E,
  output RAM_S,
  output MAR_S,
  output IR_S,
  output END,
  output IO,
  output DA,
  output LOAD_2
);

  wire and_5_out, and_6_out, and_7_out, and_8_out, and_9_out, and_10_out, and_11_out, and_12_out, and_16_out,
       and_18_out, and_19_out, and_20_out, and_21_out, and_29_out, and_30_out, and_52_out, and_53_out,
       and_54_out, and_55_out, and_56_out, and_57_out, and_58_out, and_60_out, and_61_out, and_62_out,
       and_63_out, and_64_out, not_1_out, not_2_out, not_3_out, not_4_out, not_5_out, not_6_out, not_7_out,
       not_8_out, not_9_out, not_10_out, not_11_out, not_14_out, or_5_out, or_6_out, or_7_out, or_8_out,
       or_9_out, or_11_out, or_12_out, or_13_out, or_14_out, or_15_out, or_16_out, undriven, undriven_2,
       undriven_3, undriven_4, undriven_5, undriven_6, undriven_7, undriven_8, undriven_9, undriven_10,
       undriven_11, undriven_12, undriven_13, undriven_14, undriven_15, undriven_16, undriven_17, undriven_18;

  or or_1 (R0_E, and_9_out, and_5_out);
  or or_2 (R1_E, and_10_out, and_6_out);
  or or_3 (R2_E, and_11_out, and_7_out);
  or or_4 (R3_E, and_12_out, and_8_out);
  and and_1 (IAR_E, or_5_out, CLK_E);
  and and_2 (RAM_E, or_6_out, CLK_E);
  and and_3 (ACC_E, or_7_out, CLK_E);
  buf and_4 (IOCLK_E, CLK_E);  // And open: In_1
  and and_5 (and_5_out, undriven, or_8_out, CLK_E);
  and and_6 (and_6_out, undriven_2, or_8_out, CLK_E);
  and and_7 (and_7_out, undriven_3, or_8_out, CLK_E);
  and and_8 (and_8_out, undriven_4, or_8_out, CLK_E);
  and and_9 (and_9_out, undriven_5, or_9_out, CLK_E);
  and and_10 (and_10_out, undriven_6, or_9_out, CLK_E);
  and and_11 (and_11_out, undriven_7, or_9_out, CLK_E);
  and and_12 (and_12_out, undriven_8, or_9_out, CLK_E);
  and and_13 (ALU_0, undriven_11, undriven_10, undriven_9);
  and and_14 (ALU_1, undriven_12, undriven_10, undriven_9);
  and and_15 (ALU_2, undriven_14, undriven_10, undriven_9);
  // Or or_5 has open pins: In_1=open, In_2=open, In_3=open, In_4=open, out=or_5_out
  // Or or_6 has open pins: In_1=open, In_2=open, In_3=open, In_4=open, out=or_6_out
  // Or or_7 has open pins: In_1=open, In_2=open, In_3=open, In_4=open, out=or_7_out
  // Or or_8 has open pins: In_1=open, In_2=open, In_3=open, In_4=open, out=or_8_out
  // Or or_9 has open pins: In_1=open, In_2=open, In_3=open, In_4=open, out=or_9_out
  not not_1 (not_1_out, LOAD);
  CPU_DECODER_2x4 REG_B ();
  CPU_DECODER_2x4 REG_A ();
  and and_16 (and_16_out, CLK, not_1_out);
  not not_2 (not_2_out, not_1_out);
  CPU_STEPPER cpu_stepper_1 ();
  // And and_17 has open pins: In_1=undriven_13, In_2=not_2_out, out=open
  // Not not_3 has open pins: in=open, out=not_3_out
  CPU_DECODER_3x8 cpu_decoder_3x8_1 ();
  buf and_18 (and_18_out, X);  // And open: In_2
  buf and_19 (and_19_out, A);  // And open: In_2
  buf and_20 (and_20_out, E);  // And open: In_2
  buf and_21 (and_21_out, Z);  // And open: In_2
  // And and_22 has open pins: In_1=not_3_out, In_2=open, out=open
  // And and_23 is placed but not wired
  // And and_24 is placed but not wired
  // And and_25 is placed but not wired
  // And and_26 is placed but not wired
  // And and_27 is placed but not wired
  // And and_28 is placed but not wired
  // And and_29 has open pins: In_1=open, In_2=open, out=and_29_out
  // Not not_4 has open pins: in=open, out=not_4_out
  // Not not_5 has open pins: in=open, out=not_5_out
  // Not not_6 has open pins: in=open, out=not_6_out
  // Not not_7 has open pins: in=open, out=not_7_out
  // Not not_8 has open pins: in=open, out=not_8_out
  // Not not_9 has open pins: in=open, out=not_9_out
  // Not not_10 has open pins: in=open, out=not_10_out
  // Not not_11 has open pins: in=open, out=not_11_out
  and and_30 (and_30_out, undriven_11, undriven_12, undriven_14);
  // Not not_12 is placed but not wired
  // Not not_13 is placed but not wired
  not not_14 (not_14_out, and_30_out);
  // Or or_10 has open pins: In_1=and_18_out, In_2=and_19_out, In_3=and_20_out, In_4=and_21_out, out=open
  and and_31 (LOAD, not_4_out, not_5_out, not_6_out, not_7_out, not_8_out, not_9_out, not_10_out, not_11_out);
  // And and_32 is placed but not wired
  // And and_33 is placed but not wired
  // And and_34 is placed but not wired
  // And and_35 is placed but not wired
  // And and_36 is placed but not wired
  // And and_37 is placed but not wired
  // And and_38 is placed but not wired
  // And and_39 is placed but not wired
  // And and_40 has open pins: In_1=open, In_2=and_29_out, In_3=open, out=open
  // And and_41 is placed but not wired
  // Not not_15 is placed but not wired
  // And and_42 is placed but not wired
  // And and_43 is placed but not wired
  // And and_44 is placed but not wired
  // And and_45 is placed but not wired
  // And and_46 is placed but not wired
  // And and_47 is placed but not wired
  // And and_48 is placed but not wired
  // And and_49 is placed but not wired
  // And and_50 is placed but not wired
  // And and_51 is placed but not wired
  // Or or_11 has open pins: In_1=open, In_2=open, In_3=open, In_4=open, In_5=open, In_6=open, out=or_11_out
  // Or or_12 has open pins: In_1=open, In_2=open, In_3=open, In_4=open, In_5=open, In_6=open, out=or_12_out
  // Or or_13 has open pins: In_1=open, In_2=open, In_3=open, In_4=open, out=or_13_out
  // Or or_14 has open pins: In_1=open, In_2=open, out=or_14_out
  // Or or_15 has open pins: In_1=open, In_2=open, In_3=open, In_4=open, out=or_15_out
  CPU_DECODER_2x4 cpu_decoder_2x4_1 ();
  buf and_52 (and_52_out, CLK_S);  // And open: In_2
  and and_53 (and_53_out, CLK_S, or_11_out);
  and and_54 (and_54_out, CLK_S, or_12_out);
  and and_55 (and_55_out, CLK_S, or_13_out);
  buf and_56 (and_56_out, CLK_S);  // And open: In_2
  buf and_57 (and_57_out, CLK_S);  // And open: In_2
  and and_58 (and_58_out, CLK_S, or_14_out);
  buf and_59 (IOCLK_S, CLK_S);  // And open: In_2
  and and_60 (and_60_out, CLK_S, or_15_out, undriven_15);
  and and_61 (and_61_out, CLK_S, or_15_out, undriven_18);
  and and_62 (and_62_out, CLK_S, or_15_out, undriven_17);
  and and_63 (and_63_out, CLK_S, or_15_out, undriven_16);
  or or_16 (or_16_out, MARS, RESET);
  and and_64 (and_64_out, LOAD, CLK_S);
  or or_17 (IR_S, RESET, and_52_out);
  or or_18 (MAR_S, or_16_out, and_53_out);
  or or_19 (IAR_S, RESET, and_54_out);
  or or_20 (ACC_S, RESET, and_55_out);
  or or_21 (RAM_S, and_64_out, and_56_out);
  or or_22 (TMP_S, RESET, and_57_out);
  or or_23 (FLAGS_S, RESET, and_58_out);
  or or_24 (R0_S, RESET, and_60_out);
  or or_25 (R1_S, RESET, and_61_out);
  or or_26 (R2_S, RESET, and_62_out);
  or or_27 (R3_S, RESET, and_63_out);

  assign LOAD_2 = LOAD;

  // Other names for the same wires on the sheet: CLKE = CLK_E

  // Notes on the sheet:
  //   REG B_E
  //   REG A_E
  //   REG B_S
endmodule
