// Digital circuit CPU_STEPPER.dig as structural Verilog
module CPU_STEPPER (
  input  RES,
  input  CLK,
  output O_1,
  output O_2,
  output O_3,
  output O_4,
  output O_5,
  output O_6,
  output O_7
);

  wire not_1_out, not_2_out, not_3_out, not_4_out, not_5_out, not_6_out, not_7_out, not_8_out, or_1_out,
       or_2_out, undriven, undriven_2, undriven_3, undriven_4, undriven_5, undriven_6, undriven_7,
       undriven_8, undriven_9, undriven_10, undriven_11;

  not not_1 (not_1_out, CLK);
  not not_2 (not_2_out, RES);
  or or_1 (or_1_out, RES, CLK);
  or or_2 (or_2_out, RES, not_1_out);
  or or_3 (O_1, RES, not_3_out);
  CPU_MEM_1 cpu_mem_1_1 (.S(not_2_out), .E(or_1_out));  // open: O
  not not_3 (not_3_out, undriven_2);
  CPU_MEM_1 cpu_mem_1_2 (.S(undriven), .E(or_2_out));  // open: O
  and and_1 (O_2, undriven_2, not_4_out);
  CPU_MEM_1 cpu_mem_1_3 (.S(undriven_2), .E(or_1_out));  // open: O
  not not_4 (not_4_out, undriven_4);
  CPU_MEM_1 cpu_mem_1_4 (.S(undriven_3), .E(or_2_out));  // open: O
  and and_2 (O_3, undriven_4, not_5_out);
  CPU_MEM_1 cpu_mem_1_5 (.S(undriven_4), .E(or_1_out));  // open: O
  not not_5 (not_5_out, undriven_6);
  CPU_MEM_1 cpu_mem_1_6 (.S(undriven_5), .E(or_2_out));  // open: O
  CPU_MEM_1 cpu_mem_1_7 (.S(undriven_6), .E(or_1_out));  // open: O
  and and_3 (O_4, undriven_6, not_6_out);
  not not_6 (not_6_out, undriven_8);
  CPU_MEM_1 cpu_mem_1_8 (.S(undriven_7), .E(or_2_out));  // open: O
  CPU_MEM_1 cpu_mem_1_9 (.S(undriven_8), .E(or_1_out));  // open: O
  and and_4 (O_5, undriven_8, not_7_out);
  not not_7 (not_7_out, undriven_10);
  CPU_MEM_1 cpu_mem_1_10 (.S(undriven_9), .E(or_2_out));  // open: O
  CPU_MEM_1 cpu_mem_1_11 (.S(undriven_10), .E(or_1_out));  // open: O
  and and_5 (O_6, undriven_10, not_8_out);
  not not_8 (not_8_out, O_7);
  CPU_MEM_1 cpu_mem_1_12 (.S(undriven_11), .E(or_2_out));  // open: O
endmodule
