// Digital circuit CPU_REG_8.dig as structural Verilog
module CPU_REG_8 (
  input  [7:0] I,
  input  S,
  input  E,
  output [7:0] O
);

  wire [7:0] cpu_mem_8_1_p3;

  // CPU_MEM_8 cpu_mem_8_1: pin names not known; wires that end beside it: I, S, cpu_mem_8_1_p3, O
  CPU_ENABLE cpu_enable_1 (.I(cpu_mem_8_1_p3), .E(E));  // open: O
endmodule
