// Digital circuit CPU_REG_BYTE_DBG.dig as structural Verilog
module CPU_REG_BYTE_DBG (
  input  H,
  input  V,
  input  S,
  input  E,
  input  Reset,
  input  [7:0] I,
  output [7:0] O,
  output [7:0] Reg
);

  wire and_1_out, and_2_out, and_3_out, or_1_out;
  wire [7:0] undriven;

  and and_1 (and_1_out, H, V);
  and and_2 (and_2_out, and_1_out, S);
  and and_3 (and_3_out, and_1_out, E);
  or or_1 (or_1_out, Reset, and_2_out);
  CPU_REGISTER_8_DBG cpu_register_8_dbg_1 ();
  assign O = and_3_out ? undriven : 8'bz;  // Driver driver_1
endmodule
