// Digital circuit CPU_SHL.dig as structural Verilog
module CPU_SHL (
  input  Shft_in,
  input  [7:0] I,
  output Shft_out,
  output [7:0] O
);

  wire [6:0] undriven;

  CPU_REG_8 cpu_reg_8_1 (.I(I), .E(1'b1));  // open: S, O
  CPU_ENABLE_8 cpu_enable_8_1 (.I({undriven, Shft_in}), .E(1'b1));  // open: O
endmodule
