// Digital circuit CPU_XOR_LE_1.dig as structural Verilog
module CPU_XOR_LE_1 (
  input  A,
  input  B,
  input  eq__out,
  input  A_gt__in,
  output eq,
  output A_gt__out,
  output O
);

  wire and_2_out, not_1_out;

  xor xor_1 (O, A, B);
  not not_1 (not_1_out, O);
  and and_1 (eq, eq__out, not_1_out);
  and and_2 (and_2_out, eq__out, A, O);
  or or_1 (A_gt__out, A_gt__in, and_2_out);
endmodule
