// Digital circuit CPU_XOR_LE_8.dig as structural Verilog
module CPU_XOR_LE_8 (
  input  [7:0] A,
  input  [7:0] B,
  output [7:0] O,
  output gt__A,
  output eq
);

  CPU_XOR_LE_1 cpu_xor_le_1_1 ();
  CPU_XOR_LE_1 cpu_xor_le_1_2 ();
  CPU_XOR_LE_1 cpu_xor_le_1_3 ();
  CPU_XOR_LE_1 cpu_xor_le_1_4 ();
  CPU_XOR_LE_1 cpu_xor_le_1_5 ();
  CPU_XOR_LE_1 cpu_xor_le_1_6 ();
  CPU_XOR_LE_1 cpu_xor_le_1_7 ();
  CPU_XOR_LE_1 cpu_xor_le_1_8 ();
endmodule
