// Digital circuit CPU_CLK.dig as structural Verilog
module CPU_CLK (
  input  Clk_in,
  output Clk_out,
  output Clk_s,
  output Clk_e
);

  wire jk_ff_1_nq, nand_1_out, nand_2_out, not_1_out, not_2_out, not_3_out, not_4_out, not_5_out, not_6_out,
       not_7_out;

  not not_1 (not_1_out, Clk_in);
  not not_2 (not_2_out, Clk_in);
  not not_3 (not_3_out, not_2_out);
  not not_4 (not_4_out, not_1_out);
  JK_FF jk_ff_1 (.J(1'b1), .C(Clk_in), .K(1'b1), .Q(Clk_out), .nQ(jk_ff_1_nq));
  not not_5 (not_5_out, not_3_out);
  not not_6 (not_6_out, not_5_out);
  nand nand_1 (nand_1_out, not_4_out, Clk_out);
  nand nand_2 (nand_2_out, jk_ff_1_nq, not_6_out);
  not not_7 (not_7_out, nand_2_out);
  not not_8 (Clk_s, nand_1_out);
  not not_9 (Clk_e, not_7_out);
endmodule
