// Digital circuit CPU_DATA_INSTRUCTION_WITH_RESET.dig as structural Verilog
module CPU_DATA_INSTRUCTION_WITH_RESET (
  input  clk,
  input  [7:0] IR_in,
  input  [7:0] RAM,
  input  in_4,
  input  in_5
);

  wire Acc_p1, Acc_p2, Acc_p3, Acc_p5, Acc_p6, Acc_p8, IAR_p1, IAR_p9, IAR_p10, IAR_p11, IAR_p12, IAR_p16,
       IR_p3, Memory_p4, R_0_p2, R_0_p3, R_0_p5, R_0_p6, R_0_p8, R_1_p3, R_1_p5, R_1_p6, R_1_p7, R_1_p8,
       TEMP_p2, TEMP_p5, TEMP_p7, undriven;
  wire [7:0] TEMP_p1, TEMP_p3;

  LED led_1 (.in(TEMP_p2));
  // CPU_MEM_8 TEMP: pin names not known; wires that end beside it: TEMP_p1, TEMP_p2, TEMP_p3, TEMP_p1, TEMP_p5, 1'b0, TEMP_p7, TEMP_p5
  CPU_ALU ALU ();
  CPU_BUS_1 Bus (.I(TEMP_p3), .S_1(Acc_p8));  // open: O
  LED led_2 (.in(Acc_p8));
  // CPU_ACCUMULATOR Acc: pin names not known; wires that end beside it: Acc_p1, Acc_p2, Acc_p3, Acc_p3, Acc_p5, Acc_p6, TEMP_p1, Acc_p8
  LED led_3 (.in(Acc_p5));
  LED led_4 (.in(Acc_p6));
  LED led_5 (.in(R_0_p2));
  LED led_6 (.in(R_0_p3));
  // CPU_REGISTER_8 R_0: pin names not known; wires that end beside it: TEMP_p1, R_0_p2, R_0_p3, clk, R_0_p5, R_0_p6, TEMP_p1, R_0_p8, R_0_p5
  CPU_CLK Clock ();
  LED led_7 (.in(undriven));
  LED led_8 (.in(R_1_p3));
  CPU_CONTROL Control ();
  // CPU_REGISTER_8 R_1: pin names not known; wires that end beside it: TEMP_p1, 1'b1, R_1_p3, TEMP_p1, R_1_p5, R_1_p6, R_1_p7, R_1_p8
  LED led_9 (.in(IAR_p9));
  LED led_10 (.in(R_1_p7));
  LED led_11 (.in(IAR_p10));
  // CPU_REGISTER_8 IAR: pin names not known; wires that end beside it: IAR_p1, TEMP_p2, TEMP_p7, Acc_p1, Acc_p2, R_1_p3, R_0_p2, R_0_p3, IAR_p9, IAR_p10, IAR_p11, IAR_p12, IAR_p9, TEMP_p1, in_4, IAR_p16, IAR_p16
  // CPU_REGISTER_8 R_2: pin names not known; wires that end beside it: TEMP_p1, R_1_p7, R_1_p8, TEMP_p1
  LED led_12 (.in(R_1_p8));
  RESET8 reset8_1 (.Reset_0(in_5), .Bus_in(TEMP_p1));  // open: Bus_out
  LED led_13 (.in(R_1_p5));
  // CPU_MEM_8 IR: pin names not known; wires that end beside it: IR_in, 1'b1, IR_p3
  // CPU_REGISTER_8 R_3: pin names not known; wires that end beside it: TEMP_p1, R_1_p5, R_1_p6, TEMP_p1
  LED led_14 (.in(R_1_p6));
  LED led_15 (.in(1'b1));
  // CPU_RAM_256 Memory: pin names not known; wires that end beside it: IAR_p1, TEMP_p1, RAM, Memory_p4, TEMP_p1, IAR_p12, 1'b1
  Button button_1 (.out(Memory_p4));

  // Notes on the sheet:
  //   clk: Hz: 2147483647
endmodule
