// Digital circuit CPU_DECODER_3x8.dig as structural Verilog
module CPU_DECODER_3x8 (
  input  C,
  input  B,
  input  A,
  output [7:0] O
);

  wire not_1_out, not_2_out, not_3_out;

  not not_1 (not_1_out, A);
  not not_2 (not_2_out, B);
  not not_3 (not_3_out, C);
  and and_1 (O[0], not_1_out, not_2_out, not_3_out);
  and and_2 (O[1], not_1_out, not_2_out, C);
  and and_3 (O[2], not_1_out, B, not_3_out);
  and and_4 (O[3], not_1_out, B, C);
  and and_5 (O[4], A, not_2_out, not_3_out);
  and and_6 (O[5], A, not_2_out, C);
  and and_7 (O[6], A, B, not_3_out);
  and and_8 (O[7], A, B, C);
endmodule
