// Digital circuit RESET1.dig as structural Verilog
module RESET1 (
  input  Set_1,
  input  Line_in,
  output Line_out
);

  assign Line_out = ~Set_1 ? Line_in : 1'bz;  // DriverInvSel driverinvsel_1
  assign Line_out = Set_1 ? 1'b1 : 1'bz;  // Driver driver_1
endmodule
