// Digital circuit RESET8.dig as structural Verilog
module RESET8 (
  input  Reset_0,
  input  [7:0] Bus_in,
  output [7:0] Bus_out
);

  assign Bus_out = ~Reset_0 ? Bus_in : 8'bz;  // DriverInvSel driverinvsel_1
  assign Bus_out = Reset_0 ? {8{1'b0}} : 8'bz;  // Driver driver_1
endmodule
