// Digital circuit CPU_FETCH.dig as structural Verilog
module CPU_FETCH (
  input  R_0,
  input  R_1,
  input  R_2,
  input  clk,
  input  [7:0] MEM_IN,
  output [7:0] IR_in
);

  wire cpu_accumulator_1_p2, cpu_accumulator_1_p4, cpu_accumulator_1_p5, cpu_accumulator_1_p7,
       cpu_ram_256_1_p4, IAR_p1, IAR_p2, IAR_p4, IAR_p5, IAR_p7, IAR_p9, IAR_p10, IAR_p11, IAR_p15, IAR_p16,
       IAR_p17, R_0_p2, R_0_p3, R_0_p5, R_0_p6, R_0_p8, R_1_p2, R_1_p8, R_1_p11, Reset_0_out, TEMP_p2,
       TEMP_p5;
  wire [7:0] TEMP_p1, TEMP_p3;

  LED led_1 (.in(TEMP_p2));
  // CPU_MEM_8 TEMP: pin names not known; wires that end beside it: TEMP_p1, TEMP_p2, TEMP_p3, TEMP_p1, TEMP_p5, 1'b0, R_0, R_1, TEMP_p5
  CPU_ALU cpu_alu_1 ();
  CPU_BUS_1 cpu_bus_1_1 (.I(TEMP_p3), .S_1(IAR_p9));  // open: O
  LED led_2 (.in(IAR_p9));
  LED led_3 (.in(cpu_accumulator_1_p4));
  LED led_4 (.in(cpu_accumulator_1_p5));
  // CPU_ACCUMULATOR cpu_accumulator_1: pin names not known; wires that end beside it: R_2, cpu_accumulator_1_p2, cpu_accumulator_1_p2, cpu_accumulator_1_p4, cpu_accumulator_1_p5, TEMP_p1, cpu_accumulator_1_p7
  LED led_5 (.in(R_0_p2));
  LED led_6 (.in(R_0_p3));
  // CPU_REGISTER_8 R_0: pin names not known; wires that end beside it: TEMP_p1, R_0_p2, R_0_p3, clk, R_0_p5, R_0_p6, TEMP_p1, R_0_p8
  CPU_CLK cpu_clk_1 ();
  LED led_7 (.in(R_1_p2));
  LED led_8 (.in(cpu_accumulator_1_p7));
  // CPU_REGISTER_8 R_1: pin names not known; wires that end beside it: TEMP_p1, R_1_p2, cpu_accumulator_1_p7, R_0_p6, R_0_p8, R_0_p5, cpu_accumulator_1_p5, R_1_p8, R_0_p3, TEMP_p1, R_1_p11
  CPU_CONTROL cpu_control_1 ();
  Button Reset_0 (.out(Reset_0_out));
  LED led_9 (.in(IAR_p5));
  LED led_10 (.in(IAR_p11));
  LED led_11 (.in(IAR_p16));
  // CPU_REGISTER_8 IAR: pin names not known; wires that end beside it: IAR_p1, IAR_p2, cpu_accumulator_1_p4, IAR_p4, IAR_p5, TEMP_p1, IAR_p7, IAR_p5, IAR_p9, IAR_p10, IAR_p11, R_1_p2, R_0_p2, TEMP_p2, IAR_p15, IAR_p16, IAR_p17, IAR_p17
  // CPU_REGISTER_8 R_2: pin names not known; wires that end beside it: TEMP_p1, IAR_p11, IAR_p1, IAR_p16, TEMP_p1
  LED led_12 (.in(IAR_p1));
  RESET8 reset8_1 (.Reset_0(Reset_0_out), .Bus_in(TEMP_p1));  // open: Bus_out
  RESET1 reset1_1 (.Set_1(Reset_0_out), .Line_in(R_1_p11));  // open: Line_out
  LED led_13 (.in(IAR_p10));
  // CPU_MEM_8 IR: pin names not known; wires that end beside it: TEMP_p1, IAR_p7, MEM_IN, IR_in
  // CPU_REGISTER_8 R_3: pin names not known; wires that end beside it: TEMP_p1, IAR_p10, IAR_p2, TEMP_p1
  LED led_14 (.in(IAR_p2));
  LED led_15 (.in(IAR_p7));
  // CPU_RAM_256 cpu_ram_256_1: pin names not known; wires that end beside it: IAR_p4, TEMP_p1, MEM_IN, cpu_ram_256_1_p4, TEMP_p1, R_1_p8, IAR_p15
  Button button_1 (.out(cpu_ram_256_1_p4));

  // Notes on the sheet:
  //   clk: Hz: 2147483647
endmodule
