// Digital circuit CPU_ACCUMULATOR.dig as structural Verilog
module CPU_ACCUMULATOR (
  input  [7:0] I,
  input  S,
  input  E,
  output [7:0] O
);

  // CPU_REGISTER_8 cpu_register_8_1: pin names not known; wires that end beside it: I, S, E, O

  // Notes on the sheet:
  //   S: default 1
endmodule
