// Digital circuit CPU_DECODER_2x4.dig as structural Verilog
module CPU_DECODER_2x4 (
  input  A,
  input  B,
  output L_0,
  output L_1,
  output L_2,
  output L_3
);

  wire not_1_out, not_2_out;

  not not_1 (not_1_out, A);
  not not_2 (not_2_out, B);
  and and_1 (L_0, not_2_out, not_1_out);
  and and_2 (L_1, A, not_2_out);
  and and_3 (L_2, B, not_1_out);
  and and_4 (L_3, A, B);
endmodule
