// Digital circuit CPU_REGISTER_8_DBG.dig as structural Verilog
module CPU_REGISTER_8_DBG (
  input  [7:0] I,
  input  S,
  input  E,
  output [7:0] O,
  output [7:0] Reg
);

  wire [7:0] cpu_mem_8_1_p4;

  // CPU_MEM_8 cpu_mem_8_1: pin names not known; wires that end beside it: I, S, Reg, cpu_mem_8_1_p4
  CPU_ENABLE cpu_enable_1 (.I(Reg), .E(E));  // open: O
  assign O = E ? cpu_mem_8_1_p4 : 8'bz;  // Driver driver_1
endmodule
