// Digital circuit CPU_ADDER_8.dig as structural Verilog
module CPU_ADDER_8 (
  input  [7:0] A,
  input  [7:0] B,
  input  C_in,
  output [7:0] O,
  output C_out
);

  CPU_ADDER cpu_adder_1 ();
  CPU_ADDER cpu_adder_2 ();
  CPU_ADDER cpu_adder_3 ();
  CPU_ADDER cpu_adder_4 ();
  CPU_ADDER cpu_adder_5 ();
  CPU_ADDER cpu_adder_6 ();
  CPU_ADDER cpu_adder_7 ();
  CPU_ADDER cpu_adder_8 ();
endmodule
