// Digital circuit CPU_CONTROL.dig as structural Verilog
module CPU_CONTROL (
  input  CLK,
  input  CLK_S,
  input  CLK_E,
  input  [7:0] IR_IN,
  input  C,
  input  A,
  input  E,
  input  Z,
  output BUS_1,
  output IOCLK_E,
  output ACC_E,
  output ACC_S,
  output MAR_S,
  output ALU_0,
  output ALU_1,
  output ALU_2,
  output RAM_E,
  output IR_S,
  output IAR_S,
  output IAR_E,
  output TMP_S,
  output RAM_S,
  output FLAG_S
);

  wire ACC_E_t, and_5_out, and_6_out, and_7_out, and_8_out, and_14_out, not_1_out, or_1_out, or_2_out,
       RAM_E_t, undriven_2, undriven_3, undriven_4;
  wire [7:0] undriven;

  and and_1 (IAR_E, BUS_1, CLK_E);
  and and_2 (RAM_E, RAM_E_t, CLK_E);
  and and_3 (ACC_E, ACC_E_t, CLK_E);
  and and_4 (IOCLK_E, 1'b0, CLK_E);
  CPU_DECODER_3x8 cpu_decoder_3x8_1 (.A_lsb(IR_IN[4]), .C_msb(IR_IN[5]));  // open: B, O
  and and_5 (and_5_out, C, IR_IN[3]);
  and and_6 (and_6_out, A, IR_IN[2]);
  and and_7 (and_7_out, E, IR_IN[1]);
  and and_8 (and_8_out, Z, IR_IN[0]);
  not not_1 (not_1_out, IR_IN[7]);
  or or_1 (or_1_out, and_5_out, and_6_out, and_7_out, and_8_out);
  // And and_9 has open pins: In_1=not_1_out, In_2=undriven[0], out=open
  // And and_10 has open pins: In_1=not_1_out, In_2=undriven[1], out=open
  // And and_11 has open pins: In_1=not_1_out, In_2=undriven[2], out=open
  // And and_12 has open pins: In_1=not_1_out, In_2=undriven[3], out=open
  // And and_13 has open pins: In_1=not_1_out, In_2=undriven[4], out=open
  and and_14 (and_14_out, not_1_out, undriven[5]);
  // And and_15 has open pins: In_1=not_1_out, In_2=undriven[6], out=open
  // And and_16 has open pins: In_1=not_1_out, In_2=undriven[7], out=open
  and and_17 (BUS_1, undriven_2, and_14_out);
  CPU_STEPPER cpu_stepper_1 ();
  and and_18 (ACC_E_t, undriven_3, and_14_out);
  and and_19 (RAM_E_t, undriven_4, or_1_out);
  or or_2 (or_2_out, ACC_E_t, RAM_E_t);
  and and_20 (IR_S, CLK_S, 1'b0);
  and and_21 (MAR_S, CLK_S, BUS_1);
  and and_22 (IAR_S, CLK_S, or_2_out);
  and and_23 (ACC_S, CLK_S, BUS_1);
  and and_24 (RAM_S, CLK_S, 1'b0);
  and and_25 (TMP_S, CLK_S, 1'b0);
  and and_26 (FLAG_S, CLK_S, 1'b0);

  assign ALU_0 = 1'b0;
  assign ALU_1 = 1'b0;
  assign ALU_2 = 1'b0;

  // Other names for the same wires on the sheet: ACC_S_t = BUS_1; IAR_E_t = BUS_1; MAR_S_t = BUS_1

  // Notes on the sheet:
  //   1
  //   2
  //   3
  //   4
  //   5
  //   6
endmodule
