// Digital circuit CPU_FLAGS.dig as structural Verilog
module CPU_FLAGS (
  input  A_in,
  input  E_in,
  input  Z_in,
  input  C_in,
  input  S,
  output Z,
  output C,
  output E,
  output A
);

  CPU_MEM_1 cpu_mem_1_1 (.S(S), .E(C_in));  // open: O
  CPU_MEM_1 cpu_mem_1_2 (.S(S), .E(A_in));  // open: O
  CPU_MEM_1 cpu_mem_1_3 (.S(S), .E(E_in));  // open: O
  CPU_MEM_1 cpu_mem_1_4 (.S(S), .E(Z_in));  // open: O
endmodule
