// Digital circuit CPU_SHL.dig as structural Verilog
module CPU_SHL (
  input  Shft_in,
  input  [7:0] I,
  output Shft_out,
  output [7:0] O
);

  wire [6:0] cpu_register_8_1_p4;

  // CPU_REGISTER_8 cpu_register_8_1: pin names not known; wires that end beside it: I, 1'b1, 1'b1, {Shft_out, cpu_register_8_1_p4}
  // CPU_REGISTER_8 cpu_register_8_2: pin names not known; wires that end beside it: {cpu_register_8_1_p4, Shft_in}, 1'b1, 1'b1, O
endmodule
