// Digital circuit JUMP_IF.dig as structural Verilog
module JUMP_IF (
  input  clk,
  input  [7:0] IN,
  input  [7:0] IR_in,
  input  in_4,
  input  in_5,
  input  [7:0] IN_2
);

  wire Acc_p1, Acc_p2, Acc_p3, Acc_p4, Acc_p5, Acc_p6, Acc_p8, Acc_p9, IAR_p3, IAR_p7, IAR_p8, IAR_p11,
       IR_p3, Memory_p4, R_0_p5, R_0_p6, R_0_p8, R_1_p5, R_1_p6, TEMP_p2, TEMP_p5, TEMP_p8, TEMP_p9,
       TEMP_p11, undriven, undriven_2;
  wire [7:0] TEMP_p1, TEMP_p3;

  LED led_1 (.in(TEMP_p2));
  // CPU_MEM_8 TEMP: pin names not known; wires that end beside it: TEMP_p1, TEMP_p2, TEMP_p3, TEMP_p1, TEMP_p5, 1'b0, TEMP_p5, TEMP_p8, TEMP_p9, TEMP_p8, TEMP_p11
  CPU_BUS_1 Bus (.I(TEMP_p3), .S_1(undriven_2));  // open: O
  LED led_2 (.in(undriven_2));
  CPU_ALU ALU ();
  // CPU_ACCUMULATOR Acc: pin names not known; wires that end beside it: Acc_p1, Acc_p2, Acc_p3, Acc_p4, Acc_p5, Acc_p6, TEMP_p1, Acc_p8, Acc_p9, Acc_p4
  LED led_3 (.in(Acc_p5));
  LED led_4 (.in(Acc_p6));
  // And and_1 has open pins: In_1=open, In_2=TEMP_p11, out=open
  CPU_FLAGS cpu_flags_1 ();
  LED led_5 (.in(R_1_p5));
  ctemp ctemp_1 (.S(TEMP_p2), .E(undriven));  // open: O
  LED led_6 (.in(1'b0));
  LED led_7 (.in(1'b0));
  // CPU_REGISTER_8 R_0: pin names not known; wires that end beside it: TEMP_p1, 1'b0, 1'b0, clk, R_0_p5, R_0_p6, TEMP_p1, R_0_p8, R_0_p5
  CPU_CLK Clock ();
  LED led_8 (.in(1'b0));
  LED led_9 (.in(1'b0));
  CPU_CONTROL Control ();
  // CPU_REGISTER_8 R_1: pin names not known; wires that end beside it: TEMP_p1, 1'b0, 1'b0, TEMP_p1, R_1_p5, R_1_p6, TEMP_p2
  LED led_10 (.in(1'b0));
  LED led_11 (.in(IAR_p8));
  LED led_12 (.in(1'b0));
  LED led_13 (.in(in_4));
  // CPU_REGISTER_8 IAR: pin names not known; wires that end beside it: Acc_p6, Acc_p5, IAR_p3, Acc_p3, Acc_p2, Acc_p1, IAR_p7, IAR_p8, TEMP_p1, in_4, IAR_p11, IAR_p11
  // CPU_REGISTER_8 R_2: pin names not known; wires that end beside it: TEMP_p1, 1'b0, 1'b0, TEMP_p1
  RESET8 reset8_1 (.Reset_0(in_5), .Bus_in(TEMP_p1));  // open: Bus_out
  LED led_14 (.in(1'b0));
  // CPU_REGISTER_8 R_3: pin names not known; wires that end beside it: IN, 1'b0, 1'b0, TEMP_p1
  LED led_15 (.in(1'b0));
  // CPU_MEM_8 IR: pin names not known; wires that end beside it: IR_in, 1'b1, IR_p3
  LED led_16 (.in(1'b1));
  // CPU_RAM_256 Memory: pin names not known; wires that end beside it: IAR_p7, TEMP_p1, IN_2, Memory_p4, TEMP_p1, IAR_p3, R_1_p6
  Button button_1 (.out(Memory_p4));

  // Notes on the sheet:
  //   clk: Hz: 2147483647
endmodule
