// Digital circuit CPU_CONTROL.dig as structural Verilog
module CPU_CONTROL (
  input  CLK,
  input  CLK_S,
  input  CLK_E,
  input  [7:0] IR_IN,
  output BUS_1,
  output IOCLK_E,
  output IOCLK_S,
  output ACC_E,
  output ACC_S,
  output MAR_S,
  output TMP_S,
  output ALU_0,
  output ALU_1,
  output ALU_2,
  output RAM_E,
  output RAM_S,
  output IR_S,
  output IAR_S,
  output IAR_E,
  output FLAGS_S,
  output R0_E,
  output R0_S,
  output R1_E,
  output R1_S,
  output R2_E,
  output R2_S,
  output R3_E,
  output R3_S
);

  wire and_5_out, and_6_out, and_7_out, and_8_out, and_9_out, and_10_out, and_11_out, and_12_out, and_16_out,
       IAR_S_t, not_1_out, undriven_2, undriven_3, undriven_4, undriven_5, undriven_6, undriven_7,
       undriven_8, undriven_9, undriven_10, undriven_11, undriven_12, undriven_13, undriven_14;
  wire [7:0] undriven;

  or or_1 (R0_E, and_9_out, and_5_out);
  or or_2 (R1_E, and_10_out, and_6_out);
  or or_3 (R2_E, and_11_out, and_7_out);
  or or_4 (R3_E, and_12_out, and_8_out);
  and and_1 (IAR_E, 1'b0, CLK_E);
  and and_2 (RAM_E, 1'b0, CLK_E);
  and and_3 (ACC_E, 1'b0, CLK_E);
  and and_4 (IOCLK_E, 1'b0, CLK_E);
  and and_5 (and_5_out, undriven_7, IAR_S_t, CLK_E);
  and and_6 (and_6_out, undriven_8, IAR_S_t, CLK_E);
  and and_7 (and_7_out, undriven_9, IAR_S_t, CLK_E);
  and and_8 (and_8_out, undriven_10, IAR_S_t, CLK_E);
  and and_9 (and_9_out, undriven_11, 1'b0, CLK_E);
  and and_10 (and_10_out, undriven_12, 1'b0, CLK_E);
  and and_11 (and_11_out, undriven_13, 1'b0, CLK_E);
  and and_12 (and_12_out, undriven_14, 1'b0, CLK_E);
  CPU_DECODER_2x4 REG_B ();
  CPU_DECODER_2x4 REG_A ();
  CPU_DECODER_3x8 cpu_decoder_3x8_1 (.A_lsb(IR_IN[4]), .C_msb(IR_IN[5]));  // open: B, O
  not not_1 (not_1_out, IR_IN[7]);
  // And and_13 has open pins: In_1=not_1_out, In_2=undriven[0], out=open
  // And and_14 has open pins: In_1=not_1_out, In_2=undriven[1], out=open
  // And and_15 has open pins: In_1=not_1_out, In_2=undriven[2], out=open
  and and_16 (and_16_out, not_1_out, undriven[3]);
  // And and_17 has open pins: In_1=not_1_out, In_2=undriven[4], out=open
  // And and_18 has open pins: In_1=not_1_out, In_2=undriven[5], out=open
  // And and_19 has open pins: In_1=not_1_out, In_2=undriven[6], out=open
  // And and_20 has open pins: In_1=not_1_out, In_2=undriven[7], out=open
  and and_21 (IAR_S_t, undriven_2, and_16_out);
  CPU_STEPPER cpu_stepper_1 ();
  CPU_DECODER_2x4 cpu_decoder_2x4_1 ();
  and and_22 (IR_S, CLK_S, 1'b0);
  and and_23 (MAR_S, CLK_S, 1'b0);
  and and_24 (IAR_S, CLK_S, IAR_S_t);
  and and_25 (ACC_S, CLK_S, 1'b0);
  and and_26 (RAM_S, CLK_S, 1'b0);
  and and_27 (TMP_S, CLK_S, 1'b0);
  and and_28 (FLAGS_S, CLK_S, 1'b0);
  and and_29 (IOCLK_S, CLK_S, 1'b0);
  and and_30 (R0_S, CLK_S, 1'b0, undriven_3);
  and and_31 (R1_S, CLK_S, 1'b0, undriven_6);
  and and_32 (R2_S, CLK_S, 1'b0, undriven_5);
  and and_33 (R3_S, CLK_S, 1'b0, undriven_4);

  assign ALU_0 = 1'b0;
  assign ALU_1 = 1'b0;
  assign ALU_2 = 1'b0;

  // Other names for the same wires on the sheet: REGB_E = IAR_S_t

  // Notes on the sheet:
  //   1
  //   2
  //   3
  //   4
  //   5
  //   6
endmodule
