// Digital circuit CPU_RAM_256.dig as structural Verilog
module CPU_RAM_256 (
  input  SA,
  input  [7:0] Address,
  input  [7:0] I,
  input  Reset,
  input  S,
  input  E,
  output [7:0] O
);

  wire driverinvsel_1_out;
  wire [7:0] cpu_mem_8_1_p3, cpu_reg_byte_1_p5, driverinvsel_2_out;
  wire [15:0] cpu_reg_byte_1_p1, cpu_reg_byte_242_p2;

  assign O = E ? cpu_reg_byte_1_p5 : 8'bz;  // Driver driver_1
  // CPU_MEM_8 cpu_mem_8_1: pin names not known; wires that end beside it: Address, SA, cpu_mem_8_1_p3
  CPU_DECODER_4x16 cpu_decoder_4x16_1 ();
  assign driverinvsel_1_out = ~Reset ? E : 1'bz;  // DriverInvSel driverinvsel_1
  assign driverinvsel_2_out = ~Reset ? I : 8'bz;  // DriverInvSel driverinvsel_2
  // CPU_REG_BYTE cpu_reg_byte_1: pin names not known; wires that end beside it: cpu_reg_byte_1_p1[0], cpu_reg_byte_242_p2[15], S, driverinvsel_1_out, cpu_reg_byte_1_p5, driverinvsel_2_out, Reset
  // CPU_REG_BYTE cpu_reg_byte_2: pin names not known
  // CPU_REG_BYTE cpu_reg_byte_3: pin names not known; wires that end beside it: cpu_reg_byte_1_p1[1], cpu_reg_byte_242_p2[15], S, driverinvsel_1_out, cpu_reg_byte_1_p5, driverinvsel_2_out, Reset
  // CPU_REG_BYTE cpu_reg_byte_4: pin names not known; wires that end beside it: cpu_reg_byte_1_p1[2], cpu_reg_byte_242_p2[15], S, driverinvsel_1_out, cpu_reg_byte_1_p5, driverinvsel_2_out, Reset
  // CPU_REG_BYTE cpu_reg_byte_5: pin names not known; wires that end beside it: cpu_reg_byte_1_p1[3], cpu_reg_byte_242_p2[15], S, driverinvsel_1_out, cpu_reg_byte_1_p5, driverinvsel_2_out, Reset
  // CPU_REG_BYTE cpu_reg_byte_6: pin names not known; wires that end beside it: cpu_reg_byte_1_p1[4], cpu_reg_byte_242_p2[15], S, driverinvsel_1_out, cpu_reg_byte_1_p5, driverinvsel_2_out, Reset
  // CPU_REG_BYTE cpu_reg_byte_7: pin names not known; wires that end beside it: cpu_reg_byte_1_p1[5], cpu_reg_byte_242_p2[15], S, driverinvsel_1_out, cpu_reg_byte_1_p5, driverinvsel_2_out, Reset
  // CPU_REG_BYTE cpu_reg_byte_8: pin names not known; wires that end beside it: cpu_reg_byte_1_p1[6], cpu_reg_byte_242_p2[15], S, driverinvsel_1_out, cpu_reg_byte_1_p5, driverinvsel_2_out, Reset
  // CPU_REG_BYTE cpu_reg_byte_9: pin names not known; wires that end beside it: cpu_reg_byte_1_p1[7], cpu_reg_byte_242_p2[15], S, driverinvsel_1_out, cpu_reg_byte_1_p5, driverinvsel_2_out, Reset
  // CPU_REG_BYTE cpu_reg_byte_10: pin names not known; wires that end beside it: cpu_reg_byte_1_p1[8], cpu_reg_byte_242_p2[15], S, driverinvsel_1_out, cpu_reg_byte_1_p5, driverinvsel_2_out, Reset
  // CPU_REG_BYTE cpu_reg_byte_11: pin names not known; wires that end beside it: cpu_reg_byte_1_p1[9], cpu_reg_byte_242_p2[15], S, driverinvsel_1_out, cpu_reg_byte_1_p5, driverinvsel_2_out, Reset
  // CPU_REG_BYTE cpu_reg_byte_12: pin names not known; wires that end beside it: cpu_reg_byte_1_p1[10], cpu_reg_byte_242_p2[15], S, driverinvsel_1_out, cpu_reg_byte_1_p5, driverinvsel_2_out, Reset
  // CPU_REG_BYTE cpu_reg_byte_13: pin names not known; wires that end beside it: cpu_reg_byte_1_p1[11], cpu_reg_byte_242_p2[15], S, driverinvsel_1_out, cpu_reg_byte_1_p5, driverinvsel_2_out, Reset
  // CPU_REG_BYTE cpu_reg_byte_14: pin names not known; wires that end beside it: cpu_reg_byte_1_p1[12], cpu_reg_byte_242_p2[15], S, driverinvsel_1_out, cpu_reg_byte_1_p5, driverinvsel_2_out, Reset
  // CPU_REG_BYTE cpu_reg_byte_15: pin names not known; wires that end beside it: cpu_reg_byte_1_p1[13], cpu_reg_byte_242_p2[15], S, driverinvsel_1_out, cpu_reg_byte_1_p5, driverinvsel_2_out, Reset
  // CPU_REG_BYTE cpu_reg_byte_16: pin names not known; wires that end beside it: cpu_reg_byte_1_p1[14], cpu_reg_byte_242_p2[15], S, driverinvsel_1_out, cpu_reg_byte_1_p5, driverinvsel_2_out, Reset
  // CPU_REG_BYTE cpu_reg_byte_17: pin names not known; wires that end beside it: cpu_reg_byte_1_p1[15], cpu_reg_byte_242_p2[15], S, driverinvsel_1_out, cpu_reg_byte_1_p5, driverinvsel_2_out, Reset
  // CPU_REG_BYTE cpu_reg_byte_18: pin names not known; wires that end beside it: cpu_reg_byte_1_p1[0], cpu_reg_byte_242_p2[14], S, driverinvsel_1_out, cpu_reg_byte_1_p5, driverinvsel_2_out, Reset
  // CPU_REG_BYTE cpu_reg_byte_19: pin names not known; wires that end beside it: cpu_reg_byte_1_p1[1], cpu_reg_byte_242_p2[14], S, driverinvsel_1_out, cpu_reg_byte_1_p5, driverinvsel_2_out, Reset
  // CPU_REG_BYTE cpu_reg_byte_20: pin names not known; wires that end beside it: cpu_reg_byte_1_p1[2], cpu_reg_byte_242_p2[14], S, driverinvsel_1_out, cpu_reg_byte_1_p5, driverinvsel_2_out, Reset
  // CPU_REG_BYTE cpu_reg_byte_21: pin names not known; wires that end beside it: cpu_reg_byte_1_p1[3], cpu_reg_byte_242_p2[14], S, driverinvsel_1_out, cpu_reg_byte_1_p5, driverinvsel_2_out, Reset
  // CPU_REG_BYTE cpu_reg_byte_22: pin names not known; wires that end beside it: cpu_reg_byte_1_p1[4], cpu_reg_byte_242_p2[14], S, driverinvsel_1_out, cpu_reg_byte_1_p5, driverinvsel_2_out, Reset
  // CPU_REG_BYTE cpu_reg_byte_23: pin names not known; wires that end beside it: cpu_reg_byte_1_p1[5], cpu_reg_byte_242_p2[14], S, driverinvsel_1_out, cpu_reg_byte_1_p5, driverinvsel_2_out, Reset
  // CPU_REG_BYTE cpu_reg_byte_24: pin names not known; wires that end beside it: cpu_reg_byte_1_p1[6], cpu_reg_byte_242_p2[14], S, driverinvsel_1_out, cpu_reg_byte_1_p5, driverinvsel_2_out, Reset
  // CPU_REG_BYTE cpu_reg_byte_25: pin names not known; wires that end beside it: cpu_reg_byte_1_p1[7], cpu_reg_byte_242_p2[14], S, driverinvsel_1_out, cpu_reg_byte_1_p5, driverinvsel_2_out, Reset
  // CPU_REG_BYTE cpu_reg_byte_26: pin names not known; wires that end beside it: cpu_reg_byte_1_p1[8], cpu_reg_byte_242_p2[14], S, driverinvsel_1_out, cpu_reg_byte_1_p5, driverinvsel_2_out, Reset
  // CPU_REG_BYTE cpu_reg_byte_27: pin names not known; wires that end beside it: cpu_reg_byte_1_p1[9], cpu_reg_byte_242_p2[14], S, driverinvsel_1_out, cpu_reg_byte_1_p5, driverinvsel_2_out, Reset
  // CPU_REG_BYTE cpu_reg_byte_28: pin names not known; wires that end beside it: cpu_reg_byte_1_p1[10], cpu_reg_byte_242_p2[14], S, driverinvsel_1_out, cpu_reg_byte_1_p5, driverinvsel_2_out, Reset
  // CPU_REG_BYTE cpu_reg_byte_29: pin names not known; wires that end beside it: cpu_reg_byte_1_p1[11], cpu_reg_byte_242_p2[14], S, driverinvsel_1_out, cpu_reg_byte_1_p5, driverinvsel_2_out, Reset
  // CPU_REG_BYTE cpu_reg_byte_30: pin names not known; wires that end beside it: cpu_reg_byte_1_p1[12], cpu_reg_byte_242_p2[14], S, driverinvsel_1_out, cpu_reg_byte_1_p5, driverinvsel_2_out, Reset
  // CPU_REG_BYTE cpu_reg_byte_31: pin names not known; wires that end beside it: cpu_reg_byte_1_p1[13], cpu_reg_byte_242_p2[14], S, driverinvsel_1_out, cpu_reg_byte_1_p5, driverinvsel_2_out, Reset
  // CPU_REG_BYTE cpu_reg_byte_32: pin names not known; wires that end beside it: cpu_reg_byte_1_p1[14], cpu_reg_byte_242_p2[14], S, driverinvsel_1_out, cpu_reg_byte_1_p5, driverinvsel_2_out, Reset
  // CPU_REG_BYTE cpu_reg_byte_33: pin names not known; wires that end beside it: cpu_reg_byte_1_p1[15], cpu_reg_byte_242_p2[14], S, driverinvsel_1_out, cpu_reg_byte_1_p5, driverinvsel_2_out, Reset
  // CPU_REG_BYTE cpu_reg_byte_34: pin names not known; wires that end beside it: cpu_reg_byte_1_p1[0], cpu_reg_byte_242_p2[13], S, driverinvsel_1_out, cpu_reg_byte_1_p5, driverinvsel_2_out, Reset
  // CPU_REG_BYTE cpu_reg_byte_35: pin names not known; wires that end beside it: cpu_reg_byte_1_p1[1], cpu_reg_byte_242_p2[13], S, driverinvsel_1_out, cpu_reg_byte_1_p5, driverinvsel_2_out, Reset
  // CPU_REG_BYTE cpu_reg_byte_36: pin names not known; wires that end beside it: cpu_reg_byte_1_p1[2], cpu_reg_byte_242_p2[13], S, driverinvsel_1_out, cpu_reg_byte_1_p5, driverinvsel_2_out, Reset
  // CPU_REG_BYTE cpu_reg_byte_37: pin names not known; wires that end beside it: cpu_reg_byte_1_p1[3], cpu_reg_byte_242_p2[13], S, driverinvsel_1_out, cpu_reg_byte_1_p5, driverinvsel_2_out, Reset
  // CPU_REG_BYTE cpu_reg_byte_38: pin names not known; wires that end beside it: cpu_reg_byte_1_p1[4], cpu_reg_byte_242_p2[13], S, driverinvsel_1_out, cpu_reg_byte_1_p5, driverinvsel_2_out, Reset
  // CPU_REG_BYTE cpu_reg_byte_39: pin names not known; wires that end beside it: cpu_reg_byte_1_p1[5], cpu_reg_byte_242_p2[13], S, driverinvsel_1_out, cpu_reg_byte_1_p5, driverinvsel_2_out, Reset
  // CPU_REG_BYTE cpu_reg_byte_40: pin names not known; wires that end beside it: cpu_reg_byte_1_p1[6], cpu_reg_byte_242_p2[13], S, driverinvsel_1_out, cpu_reg_byte_1_p5, driverinvsel_2_out, Reset
  // CPU_REG_BYTE cpu_reg_byte_41: pin names not known; wires that end beside it: cpu_reg_byte_1_p1[7], cpu_reg_byte_242_p2[13], S, driverinvsel_1_out, cpu_reg_byte_1_p5, driverinvsel_2_out, Reset
  // CPU_REG_BYTE cpu_reg_byte_42: pin names not known; wires that end beside it: cpu_reg_byte_1_p1[8], cpu_reg_byte_242_p2[13], S, driverinvsel_1_out, cpu_reg_byte_1_p5, driverinvsel_2_out, Reset
  // CPU_REG_BYTE cpu_reg_byte_43: pin names not known; wires that end beside it: cpu_reg_byte_1_p1[9], cpu_reg_byte_242_p2[13], S, driverinvsel_1_out, cpu_reg_byte_1_p5, driverinvsel_2_out, Reset
  // CPU_REG_BYTE cpu_reg_byte_44: pin names not known; wires that end beside it: cpu_reg_byte_1_p1[10], cpu_reg_byte_242_p2[13], S, driverinvsel_1_out, cpu_reg_byte_1_p5, driverinvsel_2_out, Reset
  // CPU_REG_BYTE cpu_reg_byte_45: pin names not known; wires that end beside it: cpu_reg_byte_1_p1[11], cpu_reg_byte_242_p2[13], S, driverinvsel_1_out, cpu_reg_byte_1_p5, driverinvsel_2_out, Reset
  // CPU_REG_BYTE cpu_reg_byte_46: pin names not known; wires that end beside it: cpu_reg_byte_1_p1[12], cpu_reg_byte_242_p2[13], S, driverinvsel_1_out, cpu_reg_byte_1_p5, driverinvsel_2_out, Reset
  // CPU_REG_BYTE cpu_reg_byte_47: pin names not known; wires that end beside it: cpu_reg_byte_1_p1[13], cpu_reg_byte_242_p2[13], S, driverinvsel_1_out, cpu_reg_byte_1_p5, driverinvsel_2_out, Reset
  // CPU_REG_BYTE cpu_reg_byte_48: pin names not known; wires that end beside it: cpu_reg_byte_1_p1[14], cpu_reg_byte_242_p2[13], S, driverinvsel_1_out, cpu_reg_byte_1_p5, driverinvsel_2_out, Reset
  // CPU_REG_BYTE cpu_reg_byte_49: pin names not known; wires that end beside it: cpu_reg_byte_1_p1[15], cpu_reg_byte_242_p2[13], S, driverinvsel_1_out, cpu_reg_byte_1_p5, driverinvsel_2_out, Reset
  // CPU_REG_BYTE cpu_reg_byte_50: pin names not known; wires that end beside it: cpu_reg_byte_1_p1[0], cpu_reg_byte_242_p2[12], S, driverinvsel_1_out, cpu_reg_byte_1_p5, driverinvsel_2_out, Reset
  // CPU_REG_BYTE cpu_reg_byte_51: pin names not known; wires that end beside it: cpu_reg_byte_1_p1[1], cpu_reg_byte_242_p2[12], S, driverinvsel_1_out, cpu_reg_byte_1_p5, driverinvsel_2_out, Reset
  // CPU_REG_BYTE cpu_reg_byte_52: pin names not known; wires that end beside it: cpu_reg_byte_1_p1[2], cpu_reg_byte_242_p2[12], S, driverinvsel_1_out, cpu_reg_byte_1_p5, driverinvsel_2_out, Reset
  // CPU_REG_BYTE cpu_reg_byte_53: pin names not known; wires that end beside it: cpu_reg_byte_1_p1[3], cpu_reg_byte_242_p2[12], S, driverinvsel_1_out, cpu_reg_byte_1_p5, driverinvsel_2_out, Reset
  // CPU_REG_BYTE cpu_reg_byte_54: pin names not known; wires that end beside it: cpu_reg_byte_1_p1[4], cpu_reg_byte_242_p2[12], S, driverinvsel_1_out, cpu_reg_byte_1_p5, driverinvsel_2_out, Reset
  // CPU_REG_BYTE cpu_reg_byte_55: pin names not known; wires that end beside it: cpu_reg_byte_1_p1[5], cpu_reg_byte_242_p2[12], S, driverinvsel_1_out, cpu_reg_byte_1_p5, driverinvsel_2_out, Reset
  // CPU_REG_BYTE cpu_reg_byte_56: pin names not known; wires that end beside it: cpu_reg_byte_1_p1[6], cpu_reg_byte_242_p2[12], S, driverinvsel_1_out, cpu_reg_byte_1_p5, driverinvsel_2_out, Reset
  // CPU_REG_BYTE cpu_reg_byte_57: pin names not known; wires that end beside it: cpu_reg_byte_1_p1[7], cpu_reg_byte_242_p2[12], S, driverinvsel_1_out, cpu_reg_byte_1_p5, driverinvsel_2_out, Reset
  // CPU_REG_BYTE cpu_reg_byte_58: pin names not known; wires that end beside it: cpu_reg_byte_1_p1[8], cpu_reg_byte_242_p2[12], S, driverinvsel_1_out, cpu_reg_byte_1_p5, driverinvsel_2_out, Reset
  // CPU_REG_BYTE cpu_reg_byte_59: pin names not known; wires that end beside it: cpu_reg_byte_1_p1[9], cpu_reg_byte_242_p2[12], S, driverinvsel_1_out, cpu_reg_byte_1_p5, driverinvsel_2_out, Reset
  // CPU_REG_BYTE cpu_reg_byte_60: pin names not known; wires that end beside it: cpu_reg_byte_1_p1[10], cpu_reg_byte_242_p2[12], S, driverinvsel_1_out, cpu_reg_byte_1_p5, driverinvsel_2_out, Reset
  // CPU_REG_BYTE cpu_reg_byte_61: pin names not known; wires that end beside it: cpu_reg_byte_1_p1[11], cpu_reg_byte_242_p2[12], S, driverinvsel_1_out, cpu_reg_byte_1_p5, driverinvsel_2_out, Reset
  // CPU_REG_BYTE cpu_reg_byte_62: pin names not known; wires that end beside it: cpu_reg_byte_1_p1[12], cpu_reg_byte_242_p2[12], S, driverinvsel_1_out, cpu_reg_byte_1_p5, driverinvsel_2_out, Reset
  // CPU_REG_BYTE cpu_reg_byte_63: pin names not known; wires that end beside it: cpu_reg_byte_1_p1[13], cpu_reg_byte_242_p2[12], S, driverinvsel_1_out, cpu_reg_byte_1_p5, driverinvsel_2_out, Reset
  // CPU_REG_BYTE cpu_reg_byte_64: pin names not known; wires that end beside it: cpu_reg_byte_1_p1[14], cpu_reg_byte_242_p2[12], S, driverinvsel_1_out, cpu_reg_byte_1_p5, driverinvsel_2_out, Reset
  // CPU_REG_BYTE cpu_reg_byte_65: pin names not known; wires that end beside it: cpu_reg_byte_1_p1[15], cpu_reg_byte_242_p2[12], S, driverinvsel_1_out, cpu_reg_byte_1_p5, driverinvsel_2_out, Reset
  // CPU_REG_BYTE cpu_reg_byte_66: pin names not known; wires that end beside it: cpu_reg_byte_1_p1[0], cpu_reg_byte_242_p2[11], S, driverinvsel_1_out, cpu_reg_byte_1_p5, driverinvsel_2_out, Reset
  // CPU_REG_BYTE cpu_reg_byte_67: pin names not known; wires that end beside it: cpu_reg_byte_1_p1[1], cpu_reg_byte_242_p2[11], S, driverinvsel_1_out, cpu_reg_byte_1_p5, driverinvsel_2_out, Reset
  // CPU_REG_BYTE cpu_reg_byte_68: pin names not known; wires that end beside it: cpu_reg_byte_1_p1[2], cpu_reg_byte_242_p2[11], S, driverinvsel_1_out, cpu_reg_byte_1_p5, driverinvsel_2_out, Reset
  // CPU_REG_BYTE cpu_reg_byte_69: pin names not known; wires that end beside it: cpu_reg_byte_1_p1[3], cpu_reg_byte_242_p2[11], S, driverinvsel_1_out, cpu_reg_byte_1_p5, driverinvsel_2_out, Reset
  // CPU_REG_BYTE cpu_reg_byte_70: pin names not known; wires that end beside it: cpu_reg_byte_1_p1[4], cpu_reg_byte_242_p2[11], S, driverinvsel_1_out, cpu_reg_byte_1_p5, driverinvsel_2_out, Reset
  // CPU_REG_BYTE cpu_reg_byte_71: pin names not known; wires that end beside it: cpu_reg_byte_1_p1[5], cpu_reg_byte_242_p2[11], S, driverinvsel_1_out, cpu_reg_byte_1_p5, driverinvsel_2_out, Reset
  // CPU_REG_BYTE cpu_reg_byte_72: pin names not known; wires that end beside it: cpu_reg_byte_1_p1[6], cpu_reg_byte_242_p2[11], S, driverinvsel_1_out, cpu_reg_byte_1_p5, driverinvsel_2_out, Reset
  // CPU_REG_BYTE cpu_reg_byte_73: pin names not known; wires that end beside it: cpu_reg_byte_1_p1[7], cpu_reg_byte_242_p2[11], S, driverinvsel_1_out, cpu_reg_byte_1_p5, driverinvsel_2_out, Reset
  // CPU_REG_BYTE cpu_reg_byte_74: pin names not known; wires that end beside it: cpu_reg_byte_1_p1[8], cpu_reg_byte_242_p2[11], S, driverinvsel_1_out, cpu_reg_byte_1_p5, driverinvsel_2_out, Reset
  // CPU_REG_BYTE cpu_reg_byte_75: pin names not known; wires that end beside it: cpu_reg_byte_1_p1[9], cpu_reg_byte_242_p2[11], S, driverinvsel_1_out, cpu_reg_byte_1_p5, driverinvsel_2_out, Reset
  // CPU_REG_BYTE cpu_reg_byte_76: pin names not known; wires that end beside it: cpu_reg_byte_1_p1[10], cpu_reg_byte_242_p2[11], S, driverinvsel_1_out, cpu_reg_byte_1_p5, driverinvsel_2_out, Reset
  // CPU_REG_BYTE cpu_reg_byte_77: pin names not known; wires that end beside it: cpu_reg_byte_1_p1[11], cpu_reg_byte_242_p2[11], S, driverinvsel_1_out, cpu_reg_byte_1_p5, driverinvsel_2_out, Reset
  // CPU_REG_BYTE cpu_reg_byte_78: pin names not known; wires that end beside it: cpu_reg_byte_1_p1[12], cpu_reg_byte_242_p2[11], S, driverinvsel_1_out, cpu_reg_byte_1_p5, driverinvsel_2_out, Reset
  // CPU_REG_BYTE cpu_reg_byte_79: pin names not known; wires that end beside it: cpu_reg_byte_1_p1[13], cpu_reg_byte_242_p2[11], S, driverinvsel_1_out, cpu_reg_byte_1_p5, driverinvsel_2_out, Reset
  // CPU_REG_BYTE cpu_reg_byte_80: pin names not known; wires that end beside it: cpu_reg_byte_1_p1[14], cpu_reg_byte_242_p2[11], S, driverinvsel_1_out, cpu_reg_byte_1_p5, driverinvsel_2_out, Reset
  // CPU_REG_BYTE cpu_reg_byte_81: pin names not known; wires that end beside it: cpu_reg_byte_1_p1[15], cpu_reg_byte_242_p2[11], S, driverinvsel_1_out, cpu_reg_byte_1_p5, driverinvsel_2_out, Reset
  // CPU_REG_BYTE cpu_reg_byte_82: pin names not known; wires that end beside it: cpu_reg_byte_1_p1[0], cpu_reg_byte_242_p2[10], S, driverinvsel_1_out, cpu_reg_byte_1_p5, driverinvsel_2_out, Reset
  // CPU_REG_BYTE cpu_reg_byte_83: pin names not known; wires that end beside it: cpu_reg_byte_1_p1[1], cpu_reg_byte_242_p2[10], S, driverinvsel_1_out, cpu_reg_byte_1_p5, driverinvsel_2_out, Reset
  // CPU_REG_BYTE cpu_reg_byte_84: pin names not known; wires that end beside it: cpu_reg_byte_1_p1[2], cpu_reg_byte_242_p2[10], S, driverinvsel_1_out, cpu_reg_byte_1_p5, driverinvsel_2_out, Reset
  // CPU_REG_BYTE cpu_reg_byte_85: pin names not known; wires that end beside it: cpu_reg_byte_1_p1[3], cpu_reg_byte_242_p2[10], S, driverinvsel_1_out, cpu_reg_byte_1_p5, driverinvsel_2_out, Reset
  // CPU_REG_BYTE cpu_reg_byte_86: pin names not known; wires that end beside it: cpu_reg_byte_1_p1[4], cpu_reg_byte_242_p2[10], S, driverinvsel_1_out, cpu_reg_byte_1_p5, driverinvsel_2_out, Reset
  // CPU_REG_BYTE cpu_reg_byte_87: pin names not known; wires that end beside it: cpu_reg_byte_1_p1[5], cpu_reg_byte_242_p2[10], S, driverinvsel_1_out, cpu_reg_byte_1_p5, driverinvsel_2_out, Reset
  // CPU_REG_BYTE cpu_reg_byte_88: pin names not known; wires that end beside it: cpu_reg_byte_1_p1[6], cpu_reg_byte_242_p2[10], S, driverinvsel_1_out, cpu_reg_byte_1_p5, driverinvsel_2_out, Reset
  // CPU_REG_BYTE cpu_reg_byte_89: pin names not known; wires that end beside it: cpu_reg_byte_1_p1[7], cpu_reg_byte_242_p2[10], S, driverinvsel_1_out, cpu_reg_byte_1_p5, driverinvsel_2_out, Reset
  // CPU_REG_BYTE cpu_reg_byte_90: pin names not known; wires that end beside it: cpu_reg_byte_1_p1[8], cpu_reg_byte_242_p2[10], S, driverinvsel_1_out, cpu_reg_byte_1_p5, driverinvsel_2_out, Reset
  // CPU_REG_BYTE cpu_reg_byte_91: pin names not known; wires that end beside it: cpu_reg_byte_1_p1[9], cpu_reg_byte_242_p2[10], S, driverinvsel_1_out, cpu_reg_byte_1_p5, driverinvsel_2_out, Reset
  // CPU_REG_BYTE cpu_reg_byte_92: pin names not known; wires that end beside it: cpu_reg_byte_1_p1[10], cpu_reg_byte_242_p2[10], S, driverinvsel_1_out, cpu_reg_byte_1_p5, driverinvsel_2_out, Reset
  // CPU_REG_BYTE cpu_reg_byte_93: pin names not known; wires that end beside it: cpu_reg_byte_1_p1[11], cpu_reg_byte_242_p2[10], S, driverinvsel_1_out, cpu_reg_byte_1_p5, driverinvsel_2_out, Reset
  // CPU_REG_BYTE cpu_reg_byte_94: pin names not known; wires that end beside it: cpu_reg_byte_1_p1[12], cpu_reg_byte_242_p2[10], S, driverinvsel_1_out, cpu_reg_byte_1_p5, driverinvsel_2_out, Reset
  // CPU_REG_BYTE cpu_reg_byte_95: pin names not known; wires that end beside it: cpu_reg_byte_1_p1[13], cpu_reg_byte_242_p2[10], S, driverinvsel_1_out, cpu_reg_byte_1_p5, driverinvsel_2_out, Reset
  // CPU_REG_BYTE cpu_reg_byte_96: pin names not known; wires that end beside it: cpu_reg_byte_1_p1[14], cpu_reg_byte_242_p2[10], S, driverinvsel_1_out, cpu_reg_byte_1_p5, driverinvsel_2_out, Reset
  // CPU_REG_BYTE cpu_reg_byte_97: pin names not known; wires that end beside it: cpu_reg_byte_1_p1[15], cpu_reg_byte_242_p2[10], S, driverinvsel_1_out, cpu_reg_byte_1_p5, driverinvsel_2_out, Reset
  // CPU_REG_BYTE cpu_reg_byte_98: pin names not known; wires that end beside it: cpu_reg_byte_1_p1[0], cpu_reg_byte_242_p2[9], S, driverinvsel_1_out, cpu_reg_byte_1_p5, driverinvsel_2_out, Reset
  // CPU_REG_BYTE cpu_reg_byte_99: pin names not known; wires that end beside it: cpu_reg_byte_1_p1[1], cpu_reg_byte_242_p2[9], S, driverinvsel_1_out, cpu_reg_byte_1_p5, driverinvsel_2_out, Reset
  // CPU_REG_BYTE cpu_reg_byte_100: pin names not known; wires that end beside it: cpu_reg_byte_1_p1[2], cpu_reg_byte_242_p2[9], S, driverinvsel_1_out, cpu_reg_byte_1_p5, driverinvsel_2_out, Reset
  // CPU_REG_BYTE cpu_reg_byte_101: pin names not known; wires that end beside it: cpu_reg_byte_1_p1[3], cpu_reg_byte_242_p2[9], S, driverinvsel_1_out, cpu_reg_byte_1_p5, driverinvsel_2_out, Reset
  // CPU_REG_BYTE cpu_reg_byte_102: pin names not known; wires that end beside it: cpu_reg_byte_1_p1[4], cpu_reg_byte_242_p2[9], S, driverinvsel_1_out, cpu_reg_byte_1_p5, driverinvsel_2_out, Reset
  // CPU_REG_BYTE cpu_reg_byte_103: pin names not known; wires that end beside it: cpu_reg_byte_1_p1[5], cpu_reg_byte_242_p2[9], S, driverinvsel_1_out, cpu_reg_byte_1_p5, driverinvsel_2_out, Reset
  // CPU_REG_BYTE cpu_reg_byte_104: pin names not known; wires that end beside it: cpu_reg_byte_1_p1[6], cpu_reg_byte_242_p2[9], S, driverinvsel_1_out, cpu_reg_byte_1_p5, driverinvsel_2_out, Reset
  // CPU_REG_BYTE cpu_reg_byte_105: pin names not known; wires that end beside it: cpu_reg_byte_1_p1[7], cpu_reg_byte_242_p2[9], S, driverinvsel_1_out, cpu_reg_byte_1_p5, driverinvsel_2_out, Reset
  // CPU_REG_BYTE cpu_reg_byte_106: pin names not known; wires that end beside it: cpu_reg_byte_1_p1[8], cpu_reg_byte_242_p2[9], S, driverinvsel_1_out, cpu_reg_byte_1_p5, driverinvsel_2_out, Reset
  // CPU_REG_BYTE cpu_reg_byte_107: pin names not known; wires that end beside it: cpu_reg_byte_1_p1[9], cpu_reg_byte_242_p2[9], S, driverinvsel_1_out, cpu_reg_byte_1_p5, driverinvsel_2_out, Reset
  // CPU_REG_BYTE cpu_reg_byte_108: pin names not known; wires that end beside it: cpu_reg_byte_1_p1[10], cpu_reg_byte_242_p2[9], S, driverinvsel_1_out, cpu_reg_byte_1_p5, driverinvsel_2_out, Reset
  // CPU_REG_BYTE cpu_reg_byte_109: pin names not known; wires that end beside it: cpu_reg_byte_1_p1[11], cpu_reg_byte_242_p2[9], S, driverinvsel_1_out, cpu_reg_byte_1_p5, driverinvsel_2_out, Reset
  // CPU_REG_BYTE cpu_reg_byte_110: pin names not known; wires that end beside it: cpu_reg_byte_1_p1[12], cpu_reg_byte_242_p2[9], S, driverinvsel_1_out, cpu_reg_byte_1_p5, driverinvsel_2_out, Reset
  // CPU_REG_BYTE cpu_reg_byte_111: pin names not known; wires that end beside it: cpu_reg_byte_1_p1[13], cpu_reg_byte_242_p2[9], S, driverinvsel_1_out, cpu_reg_byte_1_p5, driverinvsel_2_out, Reset
  // CPU_REG_BYTE cpu_reg_byte_112: pin names not known; wires that end beside it: cpu_reg_byte_1_p1[14], cpu_reg_byte_242_p2[9], S, driverinvsel_1_out, cpu_reg_byte_1_p5, driverinvsel_2_out, Reset
  // CPU_REG_BYTE cpu_reg_byte_113: pin names not known; wires that end beside it: cpu_reg_byte_1_p1[15], cpu_reg_byte_242_p2[9], S, driverinvsel_1_out, cpu_reg_byte_1_p5, driverinvsel_2_out, Reset
  // CPU_REG_BYTE cpu_reg_byte_114: pin names not known; wires that end beside it: cpu_reg_byte_1_p1[0], cpu_reg_byte_242_p2[8], S, driverinvsel_1_out, cpu_reg_byte_1_p5, driverinvsel_2_out, Reset
  // CPU_REG_BYTE cpu_reg_byte_115: pin names not known; wires that end beside it: cpu_reg_byte_1_p1[1], cpu_reg_byte_242_p2[8], S, driverinvsel_1_out, cpu_reg_byte_1_p5, driverinvsel_2_out, Reset
  // CPU_REG_BYTE cpu_reg_byte_116: pin names not known; wires that end beside it: cpu_reg_byte_1_p1[2], cpu_reg_byte_242_p2[8], S, driverinvsel_1_out, cpu_reg_byte_1_p5, driverinvsel_2_out, Reset
  // CPU_REG_BYTE cpu_reg_byte_117: pin names not known; wires that end beside it: cpu_reg_byte_1_p1[3], cpu_reg_byte_242_p2[8], S, driverinvsel_1_out, cpu_reg_byte_1_p5, driverinvsel_2_out, Reset
  // CPU_REG_BYTE cpu_reg_byte_118: pin names not known; wires that end beside it: cpu_reg_byte_1_p1[4], cpu_reg_byte_242_p2[8], S, driverinvsel_1_out, cpu_reg_byte_1_p5, driverinvsel_2_out, Reset
  // CPU_REG_BYTE cpu_reg_byte_119: pin names not known; wires that end beside it: cpu_reg_byte_1_p1[5], cpu_reg_byte_242_p2[8], S, driverinvsel_1_out, cpu_reg_byte_1_p5, driverinvsel_2_out, Reset
  // CPU_REG_BYTE cpu_reg_byte_120: pin names not known; wires that end beside it: cpu_reg_byte_1_p1[6], cpu_reg_byte_242_p2[8], S, driverinvsel_1_out, cpu_reg_byte_1_p5, driverinvsel_2_out, Reset
  // CPU_REG_BYTE cpu_reg_byte_121: pin names not known; wires that end beside it: cpu_reg_byte_1_p1[7], cpu_reg_byte_242_p2[8], S, driverinvsel_1_out, cpu_reg_byte_1_p5, driverinvsel_2_out, Reset
  // CPU_REG_BYTE cpu_reg_byte_122: pin names not known; wires that end beside it: cpu_reg_byte_1_p1[8], cpu_reg_byte_242_p2[8], S, driverinvsel_1_out, cpu_reg_byte_1_p5, driverinvsel_2_out, Reset
  // CPU_REG_BYTE cpu_reg_byte_123: pin names not known; wires that end beside it: cpu_reg_byte_1_p1[9], cpu_reg_byte_242_p2[8], S, driverinvsel_1_out, cpu_reg_byte_1_p5, driverinvsel_2_out, Reset
  // CPU_REG_BYTE cpu_reg_byte_124: pin names not known; wires that end beside it: cpu_reg_byte_1_p1[10], cpu_reg_byte_242_p2[8], S, driverinvsel_1_out, cpu_reg_byte_1_p5, driverinvsel_2_out, Reset
  // CPU_REG_BYTE cpu_reg_byte_125: pin names not known; wires that end beside it: cpu_reg_byte_1_p1[11], cpu_reg_byte_242_p2[8], S, driverinvsel_1_out, cpu_reg_byte_1_p5, driverinvsel_2_out, Reset
  // CPU_REG_BYTE cpu_reg_byte_126: pin names not known; wires that end beside it: cpu_reg_byte_1_p1[12], cpu_reg_byte_242_p2[8], S, driverinvsel_1_out, cpu_reg_byte_1_p5, driverinvsel_2_out, Reset
  // CPU_REG_BYTE cpu_reg_byte_127: pin names not known; wires that end beside it: cpu_reg_byte_1_p1[13], cpu_reg_byte_242_p2[8], S, driverinvsel_1_out, cpu_reg_byte_1_p5, driverinvsel_2_out, Reset
  // CPU_REG_BYTE cpu_reg_byte_128: pin names not known; wires that end beside it: cpu_reg_byte_1_p1[14], cpu_reg_byte_242_p2[8], S, driverinvsel_1_out, cpu_reg_byte_1_p5, driverinvsel_2_out, Reset
  // CPU_REG_BYTE cpu_reg_byte_129: pin names not known; wires that end beside it: cpu_reg_byte_1_p1[15], cpu_reg_byte_242_p2[8], S, driverinvsel_1_out, cpu_reg_byte_1_p5, driverinvsel_2_out, Reset
  CPU_DECODER_4x16 cpu_decoder_4x16_2 ();
  // CPU_REG_BYTE cpu_reg_byte_130: pin names not known; wires that end beside it: cpu_reg_byte_1_p1[0], cpu_reg_byte_242_p2[7], S, driverinvsel_1_out, cpu_reg_byte_1_p5, driverinvsel_2_out, Reset
  // CPU_REG_BYTE cpu_reg_byte_131: pin names not known; wires that end beside it: cpu_reg_byte_1_p1[1], cpu_reg_byte_242_p2[7], S, driverinvsel_1_out, cpu_reg_byte_1_p5, driverinvsel_2_out, Reset
  // CPU_REG_BYTE cpu_reg_byte_132: pin names not known; wires that end beside it: cpu_reg_byte_1_p1[2], cpu_reg_byte_242_p2[7], S, driverinvsel_1_out, cpu_reg_byte_1_p5, driverinvsel_2_out, Reset
  // CPU_REG_BYTE cpu_reg_byte_133: pin names not known; wires that end beside it: cpu_reg_byte_1_p1[3], cpu_reg_byte_242_p2[7], S, driverinvsel_1_out, cpu_reg_byte_1_p5, driverinvsel_2_out, Reset
  // CPU_REG_BYTE cpu_reg_byte_134: pin names not known; wires that end beside it: cpu_reg_byte_1_p1[4], cpu_reg_byte_242_p2[7], S, driverinvsel_1_out, cpu_reg_byte_1_p5, driverinvsel_2_out, Reset
  // CPU_REG_BYTE cpu_reg_byte_135: pin names not known; wires that end beside it: cpu_reg_byte_1_p1[5], cpu_reg_byte_242_p2[7], S, driverinvsel_1_out, cpu_reg_byte_1_p5, driverinvsel_2_out, Reset
  // CPU_REG_BYTE cpu_reg_byte_136: pin names not known; wires that end beside it: cpu_reg_byte_1_p1[6], cpu_reg_byte_242_p2[7], S, driverinvsel_1_out, cpu_reg_byte_1_p5, driverinvsel_2_out, Reset
  // CPU_REG_BYTE cpu_reg_byte_137: pin names not known; wires that end beside it: cpu_reg_byte_1_p1[7], cpu_reg_byte_242_p2[7], S, driverinvsel_1_out, cpu_reg_byte_1_p5, driverinvsel_2_out, Reset
  // CPU_REG_BYTE cpu_reg_byte_138: pin names not known; wires that end beside it: cpu_reg_byte_1_p1[8], cpu_reg_byte_242_p2[7], S, driverinvsel_1_out, cpu_reg_byte_1_p5, driverinvsel_2_out, Reset
  // CPU_REG_BYTE cpu_reg_byte_139: pin names not known; wires that end beside it: cpu_reg_byte_1_p1[9], cpu_reg_byte_242_p2[7], S, driverinvsel_1_out, cpu_reg_byte_1_p5, driverinvsel_2_out, Reset
  // CPU_REG_BYTE cpu_reg_byte_140: pin names not known; wires that end beside it: cpu_reg_byte_1_p1[10], cpu_reg_byte_242_p2[7], S, driverinvsel_1_out, cpu_reg_byte_1_p5, driverinvsel_2_out, Reset
  // CPU_REG_BYTE cpu_reg_byte_141: pin names not known; wires that end beside it: cpu_reg_byte_1_p1[11], cpu_reg_byte_242_p2[7], S, driverinvsel_1_out, cpu_reg_byte_1_p5, driverinvsel_2_out, Reset
  // CPU_REG_BYTE cpu_reg_byte_142: pin names not known; wires that end beside it: cpu_reg_byte_1_p1[12], cpu_reg_byte_242_p2[7], S, driverinvsel_1_out, cpu_reg_byte_1_p5, driverinvsel_2_out, Reset
  // CPU_REG_BYTE cpu_reg_byte_143: pin names not known; wires that end beside it: cpu_reg_byte_1_p1[13], cpu_reg_byte_242_p2[7], S, driverinvsel_1_out, cpu_reg_byte_1_p5, driverinvsel_2_out, Reset
  // CPU_REG_BYTE cpu_reg_byte_144: pin names not known; wires that end beside it: cpu_reg_byte_1_p1[14], cpu_reg_byte_242_p2[7], S, driverinvsel_1_out, cpu_reg_byte_1_p5, driverinvsel_2_out, Reset
  // CPU_REG_BYTE cpu_reg_byte_145: pin names not known; wires that end beside it: cpu_reg_byte_1_p1[15], cpu_reg_byte_242_p2[7], S, driverinvsel_1_out, cpu_reg_byte_1_p5, driverinvsel_2_out, Reset
  // CPU_REG_BYTE cpu_reg_byte_146: pin names not known; wires that end beside it: cpu_reg_byte_1_p1[0], cpu_reg_byte_242_p2[6], S, driverinvsel_1_out, cpu_reg_byte_1_p5, driverinvsel_2_out, Reset
  // CPU_REG_BYTE cpu_reg_byte_147: pin names not known; wires that end beside it: cpu_reg_byte_1_p1[1], cpu_reg_byte_242_p2[6], S, driverinvsel_1_out, cpu_reg_byte_1_p5, driverinvsel_2_out, Reset
  // CPU_REG_BYTE cpu_reg_byte_148: pin names not known; wires that end beside it: cpu_reg_byte_1_p1[2], cpu_reg_byte_242_p2[6], S, driverinvsel_1_out, cpu_reg_byte_1_p5, driverinvsel_2_out, Reset
  // CPU_REG_BYTE cpu_reg_byte_149: pin names not known; wires that end beside it: cpu_reg_byte_1_p1[3], cpu_reg_byte_242_p2[6], S, driverinvsel_1_out, cpu_reg_byte_1_p5, driverinvsel_2_out, Reset
  // CPU_REG_BYTE cpu_reg_byte_150: pin names not known; wires that end beside it: cpu_reg_byte_1_p1[4], cpu_reg_byte_242_p2[6], S, driverinvsel_1_out, cpu_reg_byte_1_p5, driverinvsel_2_out, Reset
  // CPU_REG_BYTE cpu_reg_byte_151: pin names not known; wires that end beside it: cpu_reg_byte_1_p1[5], cpu_reg_byte_242_p2[6], S, driverinvsel_1_out, cpu_reg_byte_1_p5, driverinvsel_2_out, Reset
  // CPU_REG_BYTE cpu_reg_byte_152: pin names not known; wires that end beside it: cpu_reg_byte_1_p1[6], cpu_reg_byte_242_p2[6], S, driverinvsel_1_out, cpu_reg_byte_1_p5, driverinvsel_2_out, Reset
  // CPU_REG_BYTE cpu_reg_byte_153: pin names not known; wires that end beside it: cpu_reg_byte_1_p1[7], cpu_reg_byte_242_p2[6], S, driverinvsel_1_out, cpu_reg_byte_1_p5, driverinvsel_2_out, Reset
  // CPU_REG_BYTE cpu_reg_byte_154: pin names not known; wires that end beside it: cpu_reg_byte_1_p1[8], cpu_reg_byte_242_p2[6], S, driverinvsel_1_out, cpu_reg_byte_1_p5, driverinvsel_2_out, Reset
  // CPU_REG_BYTE cpu_reg_byte_155: pin names not known; wires that end beside it: cpu_reg_byte_1_p1[9], cpu_reg_byte_242_p2[6], S, driverinvsel_1_out, cpu_reg_byte_1_p5, driverinvsel_2_out, Reset
  // CPU_REG_BYTE cpu_reg_byte_156: pin names not known; wires that end beside it: cpu_reg_byte_1_p1[10], cpu_reg_byte_242_p2[6], S, driverinvsel_1_out, cpu_reg_byte_1_p5, driverinvsel_2_out, Reset
  // CPU_REG_BYTE cpu_reg_byte_157: pin names not known; wires that end beside it: cpu_reg_byte_1_p1[11], cpu_reg_byte_242_p2[6], S, driverinvsel_1_out, cpu_reg_byte_1_p5, driverinvsel_2_out, Reset
  // CPU_REG_BYTE cpu_reg_byte_158: pin names not known; wires that end beside it: cpu_reg_byte_1_p1[12], cpu_reg_byte_242_p2[6], S, driverinvsel_1_out, cpu_reg_byte_1_p5, driverinvsel_2_out, Reset
  // CPU_REG_BYTE cpu_reg_byte_159: pin names not known; wires that end beside it: cpu_reg_byte_1_p1[13], cpu_reg_byte_242_p2[6], S, driverinvsel_1_out, cpu_reg_byte_1_p5, driverinvsel_2_out, Reset
  // CPU_REG_BYTE cpu_reg_byte_160: pin names not known; wires that end beside it: cpu_reg_byte_1_p1[14], cpu_reg_byte_242_p2[6], S, driverinvsel_1_out, cpu_reg_byte_1_p5, driverinvsel_2_out, Reset
  // CPU_REG_BYTE cpu_reg_byte_161: pin names not known; wires that end beside it: cpu_reg_byte_1_p1[15], cpu_reg_byte_242_p2[6], S, driverinvsel_1_out, cpu_reg_byte_1_p5, driverinvsel_2_out, Reset
  // CPU_REG_BYTE cpu_reg_byte_162: pin names not known; wires that end beside it: cpu_reg_byte_1_p1[0], cpu_reg_byte_242_p2[5], S, driverinvsel_1_out, cpu_reg_byte_1_p5, driverinvsel_2_out, Reset
  // CPU_REG_BYTE cpu_reg_byte_163: pin names not known; wires that end beside it: cpu_reg_byte_1_p1[1], cpu_reg_byte_242_p2[5], S, driverinvsel_1_out, cpu_reg_byte_1_p5, driverinvsel_2_out, Reset
  // CPU_REG_BYTE cpu_reg_byte_164: pin names not known; wires that end beside it: cpu_reg_byte_1_p1[2], cpu_reg_byte_242_p2[5], S, driverinvsel_1_out, cpu_reg_byte_1_p5, driverinvsel_2_out, Reset
  // CPU_REG_BYTE cpu_reg_byte_165: pin names not known; wires that end beside it: cpu_reg_byte_1_p1[3], cpu_reg_byte_242_p2[5], S, driverinvsel_1_out, cpu_reg_byte_1_p5, driverinvsel_2_out, Reset
  // CPU_REG_BYTE cpu_reg_byte_166: pin names not known; wires that end beside it: cpu_reg_byte_1_p1[4], cpu_reg_byte_242_p2[5], S, driverinvsel_1_out, cpu_reg_byte_1_p5, driverinvsel_2_out, Reset
  // CPU_REG_BYTE cpu_reg_byte_167: pin names not known; wires that end beside it: cpu_reg_byte_1_p1[5], cpu_reg_byte_242_p2[5], S, driverinvsel_1_out, cpu_reg_byte_1_p5, driverinvsel_2_out, Reset
  // CPU_REG_BYTE cpu_reg_byte_168: pin names not known; wires that end beside it: cpu_reg_byte_1_p1[6], cpu_reg_byte_242_p2[5], S, driverinvsel_1_out, cpu_reg_byte_1_p5, driverinvsel_2_out, Reset
  // CPU_REG_BYTE cpu_reg_byte_169: pin names not known; wires that end beside it: cpu_reg_byte_1_p1[7], cpu_reg_byte_242_p2[5], S, driverinvsel_1_out, cpu_reg_byte_1_p5, driverinvsel_2_out, Reset
  // CPU_REG_BYTE cpu_reg_byte_170: pin names not known; wires that end beside it: cpu_reg_byte_1_p1[8], cpu_reg_byte_242_p2[5], S, driverinvsel_1_out, cpu_reg_byte_1_p5, driverinvsel_2_out, Reset
  // CPU_REG_BYTE cpu_reg_byte_171: pin names not known; wires that end beside it: cpu_reg_byte_1_p1[9], cpu_reg_byte_242_p2[5], S, driverinvsel_1_out, cpu_reg_byte_1_p5, driverinvsel_2_out, Reset
  // CPU_REG_BYTE cpu_reg_byte_172: pin names not known; wires that end beside it: cpu_reg_byte_1_p1[10], cpu_reg_byte_242_p2[5], S, driverinvsel_1_out, cpu_reg_byte_1_p5, driverinvsel_2_out, Reset
  // CPU_REG_BYTE cpu_reg_byte_173: pin names not known; wires that end beside it: cpu_reg_byte_1_p1[11], cpu_reg_byte_242_p2[5], S, driverinvsel_1_out, cpu_reg_byte_1_p5, driverinvsel_2_out, Reset
  // CPU_REG_BYTE cpu_reg_byte_174: pin names not known; wires that end beside it: cpu_reg_byte_1_p1[12], cpu_reg_byte_242_p2[5], S, driverinvsel_1_out, cpu_reg_byte_1_p5, driverinvsel_2_out, Reset
  // CPU_REG_BYTE cpu_reg_byte_175: pin names not known; wires that end beside it: cpu_reg_byte_1_p1[13], cpu_reg_byte_242_p2[5], S, driverinvsel_1_out, cpu_reg_byte_1_p5, driverinvsel_2_out, Reset
  // CPU_REG_BYTE cpu_reg_byte_176: pin names not known; wires that end beside it: cpu_reg_byte_1_p1[14], cpu_reg_byte_242_p2[5], S, driverinvsel_1_out, cpu_reg_byte_1_p5, driverinvsel_2_out, Reset
  // CPU_REG_BYTE cpu_reg_byte_177: pin names not known; wires that end beside it: cpu_reg_byte_1_p1[15], cpu_reg_byte_242_p2[5], S, driverinvsel_1_out, cpu_reg_byte_1_p5, driverinvsel_2_out, Reset
  // CPU_REG_BYTE cpu_reg_byte_178: pin names not known; wires that end beside it: cpu_reg_byte_1_p1[0], cpu_reg_byte_242_p2[4], S, driverinvsel_1_out, cpu_reg_byte_1_p5, driverinvsel_2_out, Reset
  // CPU_REG_BYTE cpu_reg_byte_179: pin names not known; wires that end beside it: cpu_reg_byte_1_p1[1], cpu_reg_byte_242_p2[4], S, driverinvsel_1_out, cpu_reg_byte_1_p5, driverinvsel_2_out, Reset
  // CPU_REG_BYTE cpu_reg_byte_180: pin names not known; wires that end beside it: cpu_reg_byte_1_p1[2], cpu_reg_byte_242_p2[4], S, driverinvsel_1_out, cpu_reg_byte_1_p5, driverinvsel_2_out, Reset
  // CPU_REG_BYTE cpu_reg_byte_181: pin names not known; wires that end beside it: cpu_reg_byte_1_p1[3], cpu_reg_byte_242_p2[4], S, driverinvsel_1_out, cpu_reg_byte_1_p5, driverinvsel_2_out, Reset
  // CPU_REG_BYTE cpu_reg_byte_182: pin names not known; wires that end beside it: cpu_reg_byte_1_p1[4], cpu_reg_byte_242_p2[4], S, driverinvsel_1_out, cpu_reg_byte_1_p5, driverinvsel_2_out, Reset
  // CPU_REG_BYTE cpu_reg_byte_183: pin names not known; wires that end beside it: cpu_reg_byte_1_p1[5], cpu_reg_byte_242_p2[4], S, driverinvsel_1_out, cpu_reg_byte_1_p5, driverinvsel_2_out, Reset
  // CPU_REG_BYTE cpu_reg_byte_184: pin names not known; wires that end beside it: cpu_reg_byte_1_p1[6], cpu_reg_byte_242_p2[4], S, driverinvsel_1_out, cpu_reg_byte_1_p5, driverinvsel_2_out, Reset
  // CPU_REG_BYTE cpu_reg_byte_185: pin names not known; wires that end beside it: cpu_reg_byte_1_p1[7], cpu_reg_byte_242_p2[4], S, driverinvsel_1_out, cpu_reg_byte_1_p5, driverinvsel_2_out, Reset
  // CPU_REG_BYTE cpu_reg_byte_186: pin names not known; wires that end beside it: cpu_reg_byte_1_p1[8], cpu_reg_byte_242_p2[4], S, driverinvsel_1_out, cpu_reg_byte_1_p5, driverinvsel_2_out, Reset
  // CPU_REG_BYTE cpu_reg_byte_187: pin names not known; wires that end beside it: cpu_reg_byte_1_p1[9], cpu_reg_byte_242_p2[4], S, driverinvsel_1_out, cpu_reg_byte_1_p5, driverinvsel_2_out, Reset
  // CPU_REG_BYTE cpu_reg_byte_188: pin names not known; wires that end beside it: cpu_reg_byte_1_p1[10], cpu_reg_byte_242_p2[4], S, driverinvsel_1_out, cpu_reg_byte_1_p5, driverinvsel_2_out, Reset
  // CPU_REG_BYTE cpu_reg_byte_189: pin names not known; wires that end beside it: cpu_reg_byte_1_p1[11], cpu_reg_byte_242_p2[4], S, driverinvsel_1_out, cpu_reg_byte_1_p5, driverinvsel_2_out, Reset
  // CPU_REG_BYTE cpu_reg_byte_190: pin names not known; wires that end beside it: cpu_reg_byte_1_p1[12], cpu_reg_byte_242_p2[4], S, driverinvsel_1_out, cpu_reg_byte_1_p5, driverinvsel_2_out, Reset
  // CPU_REG_BYTE cpu_reg_byte_191: pin names not known; wires that end beside it: cpu_reg_byte_1_p1[13], cpu_reg_byte_242_p2[4], S, driverinvsel_1_out, cpu_reg_byte_1_p5, driverinvsel_2_out, Reset
  // CPU_REG_BYTE cpu_reg_byte_192: pin names not known; wires that end beside it: cpu_reg_byte_1_p1[14], cpu_reg_byte_242_p2[4], S, driverinvsel_1_out, cpu_reg_byte_1_p5, driverinvsel_2_out, Reset
  // CPU_REG_BYTE cpu_reg_byte_193: pin names not known; wires that end beside it: cpu_reg_byte_1_p1[15], cpu_reg_byte_242_p2[4], S, driverinvsel_1_out, cpu_reg_byte_1_p5, driverinvsel_2_out, Reset
  // CPU_REG_BYTE cpu_reg_byte_194: pin names not known; wires that end beside it: cpu_reg_byte_1_p1[0], cpu_reg_byte_242_p2[3], S, driverinvsel_1_out, cpu_reg_byte_1_p5, driverinvsel_2_out, Reset
  // CPU_REG_BYTE cpu_reg_byte_195: pin names not known; wires that end beside it: cpu_reg_byte_1_p1[1], cpu_reg_byte_242_p2[3], S, driverinvsel_1_out, cpu_reg_byte_1_p5, driverinvsel_2_out, Reset
  // CPU_REG_BYTE cpu_reg_byte_196: pin names not known; wires that end beside it: cpu_reg_byte_1_p1[2], cpu_reg_byte_242_p2[3], S, driverinvsel_1_out, cpu_reg_byte_1_p5, driverinvsel_2_out, Reset
  // CPU_REG_BYTE cpu_reg_byte_197: pin names not known; wires that end beside it: cpu_reg_byte_1_p1[3], cpu_reg_byte_242_p2[3], S, driverinvsel_1_out, cpu_reg_byte_1_p5, driverinvsel_2_out, Reset
  // CPU_REG_BYTE cpu_reg_byte_198: pin names not known; wires that end beside it: cpu_reg_byte_1_p1[4], cpu_reg_byte_242_p2[3], S, driverinvsel_1_out, cpu_reg_byte_1_p5, driverinvsel_2_out, Reset
  // CPU_REG_BYTE cpu_reg_byte_199: pin names not known; wires that end beside it: cpu_reg_byte_1_p1[5], cpu_reg_byte_242_p2[3], S, driverinvsel_1_out, cpu_reg_byte_1_p5, driverinvsel_2_out, Reset
  // CPU_REG_BYTE cpu_reg_byte_200: pin names not known; wires that end beside it: cpu_reg_byte_1_p1[6], cpu_reg_byte_242_p2[3], S, driverinvsel_1_out, cpu_reg_byte_1_p5, driverinvsel_2_out, Reset
  // CPU_REG_BYTE cpu_reg_byte_201: pin names not known; wires that end beside it: cpu_reg_byte_1_p1[7], cpu_reg_byte_242_p2[3], S, driverinvsel_1_out, cpu_reg_byte_1_p5, driverinvsel_2_out, Reset
  // CPU_REG_BYTE cpu_reg_byte_202: pin names not known; wires that end beside it: cpu_reg_byte_1_p1[8], cpu_reg_byte_242_p2[3], S, driverinvsel_1_out, cpu_reg_byte_1_p5, driverinvsel_2_out, Reset
  // CPU_REG_BYTE cpu_reg_byte_203: pin names not known; wires that end beside it: cpu_reg_byte_1_p1[9], cpu_reg_byte_242_p2[3], S, driverinvsel_1_out, cpu_reg_byte_1_p5, driverinvsel_2_out, Reset
  // CPU_REG_BYTE cpu_reg_byte_204: pin names not known; wires that end beside it: cpu_reg_byte_1_p1[10], cpu_reg_byte_242_p2[3], S, driverinvsel_1_out, cpu_reg_byte_1_p5, driverinvsel_2_out, Reset
  // CPU_REG_BYTE cpu_reg_byte_205: pin names not known; wires that end beside it: cpu_reg_byte_1_p1[11], cpu_reg_byte_242_p2[3], S, driverinvsel_1_out, cpu_reg_byte_1_p5, driverinvsel_2_out, Reset
  // CPU_REG_BYTE cpu_reg_byte_206: pin names not known; wires that end beside it: cpu_reg_byte_1_p1[12], cpu_reg_byte_242_p2[3], S, driverinvsel_1_out, cpu_reg_byte_1_p5, driverinvsel_2_out, Reset
  // CPU_REG_BYTE cpu_reg_byte_207: pin names not known; wires that end beside it: cpu_reg_byte_1_p1[13], cpu_reg_byte_242_p2[3], S, driverinvsel_1_out, cpu_reg_byte_1_p5, driverinvsel_2_out, Reset
  // CPU_REG_BYTE cpu_reg_byte_208: pin names not known; wires that end beside it: cpu_reg_byte_1_p1[14], cpu_reg_byte_242_p2[3], S, driverinvsel_1_out, cpu_reg_byte_1_p5, driverinvsel_2_out, Reset
  // CPU_REG_BYTE cpu_reg_byte_209: pin names not known; wires that end beside it: cpu_reg_byte_1_p1[15], cpu_reg_byte_242_p2[3], S, driverinvsel_1_out, cpu_reg_byte_1_p5, driverinvsel_2_out, Reset
  // CPU_REG_BYTE cpu_reg_byte_210: pin names not known; wires that end beside it: cpu_reg_byte_1_p1[0], cpu_reg_byte_242_p2[2], S, driverinvsel_1_out, cpu_reg_byte_1_p5, driverinvsel_2_out, Reset
  // CPU_REG_BYTE cpu_reg_byte_211: pin names not known; wires that end beside it: cpu_reg_byte_1_p1[1], cpu_reg_byte_242_p2[2], S, driverinvsel_1_out, cpu_reg_byte_1_p5, driverinvsel_2_out, Reset
  // CPU_REG_BYTE cpu_reg_byte_212: pin names not known; wires that end beside it: cpu_reg_byte_1_p1[2], cpu_reg_byte_242_p2[2], S, driverinvsel_1_out, cpu_reg_byte_1_p5, driverinvsel_2_out, Reset
  // CPU_REG_BYTE cpu_reg_byte_213: pin names not known; wires that end beside it: cpu_reg_byte_1_p1[3], cpu_reg_byte_242_p2[2], S, driverinvsel_1_out, cpu_reg_byte_1_p5, driverinvsel_2_out, Reset
  // CPU_REG_BYTE cpu_reg_byte_214: pin names not known; wires that end beside it: cpu_reg_byte_1_p1[4], cpu_reg_byte_242_p2[2], S, driverinvsel_1_out, cpu_reg_byte_1_p5, driverinvsel_2_out, Reset
  // CPU_REG_BYTE cpu_reg_byte_215: pin names not known; wires that end beside it: cpu_reg_byte_1_p1[5], cpu_reg_byte_242_p2[2], S, driverinvsel_1_out, cpu_reg_byte_1_p5, driverinvsel_2_out, Reset
  // CPU_REG_BYTE cpu_reg_byte_216: pin names not known; wires that end beside it: cpu_reg_byte_1_p1[6], cpu_reg_byte_242_p2[2], S, driverinvsel_1_out, cpu_reg_byte_1_p5, driverinvsel_2_out, Reset
  // CPU_REG_BYTE cpu_reg_byte_217: pin names not known; wires that end beside it: cpu_reg_byte_1_p1[7], cpu_reg_byte_242_p2[2], S, driverinvsel_1_out, cpu_reg_byte_1_p5, driverinvsel_2_out, Reset
  // CPU_REG_BYTE cpu_reg_byte_218: pin names not known; wires that end beside it: cpu_reg_byte_1_p1[8], cpu_reg_byte_242_p2[2], S, driverinvsel_1_out, cpu_reg_byte_1_p5, driverinvsel_2_out, Reset
  // CPU_REG_BYTE cpu_reg_byte_219: pin names not known; wires that end beside it: cpu_reg_byte_1_p1[9], cpu_reg_byte_242_p2[2], S, driverinvsel_1_out, cpu_reg_byte_1_p5, driverinvsel_2_out, Reset
  // CPU_REG_BYTE cpu_reg_byte_220: pin names not known; wires that end beside it: cpu_reg_byte_1_p1[10], cpu_reg_byte_242_p2[2], S, driverinvsel_1_out, cpu_reg_byte_1_p5, driverinvsel_2_out, Reset
  // CPU_REG_BYTE cpu_reg_byte_221: pin names not known; wires that end beside it: cpu_reg_byte_1_p1[11], cpu_reg_byte_242_p2[2], S, driverinvsel_1_out, cpu_reg_byte_1_p5, driverinvsel_2_out, Reset
  // CPU_REG_BYTE cpu_reg_byte_222: pin names not known; wires that end beside it: cpu_reg_byte_1_p1[12], cpu_reg_byte_242_p2[2], S, driverinvsel_1_out, cpu_reg_byte_1_p5, driverinvsel_2_out, Reset
  // CPU_REG_BYTE cpu_reg_byte_223: pin names not known; wires that end beside it: cpu_reg_byte_1_p1[13], cpu_reg_byte_242_p2[2], S, driverinvsel_1_out, cpu_reg_byte_1_p5, driverinvsel_2_out, Reset
  // CPU_REG_BYTE cpu_reg_byte_224: pin names not known; wires that end beside it: cpu_reg_byte_1_p1[14], cpu_reg_byte_242_p2[2], S, driverinvsel_1_out, cpu_reg_byte_1_p5, driverinvsel_2_out, Reset
  // CPU_REG_BYTE cpu_reg_byte_225: pin names not known; wires that end beside it: cpu_reg_byte_1_p1[15], cpu_reg_byte_242_p2[2], S, driverinvsel_1_out, cpu_reg_byte_1_p5, driverinvsel_2_out, Reset
  // CPU_REG_BYTE cpu_reg_byte_226: pin names not known; wires that end beside it: cpu_reg_byte_1_p1[0], cpu_reg_byte_242_p2[1], S, driverinvsel_1_out, cpu_reg_byte_1_p5, driverinvsel_2_out, Reset
  // CPU_REG_BYTE cpu_reg_byte_227: pin names not known; wires that end beside it: cpu_reg_byte_1_p1[1], cpu_reg_byte_242_p2[1], S, driverinvsel_1_out, cpu_reg_byte_1_p5, driverinvsel_2_out, Reset
  // CPU_REG_BYTE cpu_reg_byte_228: pin names not known; wires that end beside it: cpu_reg_byte_1_p1[2], cpu_reg_byte_242_p2[1], S, driverinvsel_1_out, cpu_reg_byte_1_p5, driverinvsel_2_out, Reset
  // CPU_REG_BYTE cpu_reg_byte_229: pin names not known; wires that end beside it: cpu_reg_byte_1_p1[3], cpu_reg_byte_242_p2[1], S, driverinvsel_1_out, cpu_reg_byte_1_p5, driverinvsel_2_out, Reset
  // CPU_REG_BYTE cpu_reg_byte_230: pin names not known; wires that end beside it: cpu_reg_byte_1_p1[4], cpu_reg_byte_242_p2[1], S, driverinvsel_1_out, cpu_reg_byte_1_p5, driverinvsel_2_out, Reset
  // CPU_REG_BYTE cpu_reg_byte_231: pin names not known; wires that end beside it: cpu_reg_byte_1_p1[5], cpu_reg_byte_242_p2[1], S, driverinvsel_1_out, cpu_reg_byte_1_p5, driverinvsel_2_out, Reset
  // CPU_REG_BYTE cpu_reg_byte_232: pin names not known; wires that end beside it: cpu_reg_byte_1_p1[6], cpu_reg_byte_242_p2[1], S, driverinvsel_1_out, cpu_reg_byte_1_p5, driverinvsel_2_out, Reset
  // CPU_REG_BYTE cpu_reg_byte_233: pin names not known; wires that end beside it: cpu_reg_byte_1_p1[7], cpu_reg_byte_242_p2[1], S, driverinvsel_1_out, cpu_reg_byte_1_p5, driverinvsel_2_out, Reset
  // CPU_REG_BYTE cpu_reg_byte_234: pin names not known; wires that end beside it: cpu_reg_byte_1_p1[8], cpu_reg_byte_242_p2[1], S, driverinvsel_1_out, cpu_reg_byte_1_p5, driverinvsel_2_out, Reset
  // CPU_REG_BYTE cpu_reg_byte_235: pin names not known; wires that end beside it: cpu_reg_byte_1_p1[9], cpu_reg_byte_242_p2[1], S, driverinvsel_1_out, cpu_reg_byte_1_p5, driverinvsel_2_out, Reset
  // CPU_REG_BYTE cpu_reg_byte_236: pin names not known; wires that end beside it: cpu_reg_byte_1_p1[10], cpu_reg_byte_242_p2[1], S, driverinvsel_1_out, cpu_reg_byte_1_p5, driverinvsel_2_out, Reset
  // CPU_REG_BYTE cpu_reg_byte_237: pin names not known; wires that end beside it: cpu_reg_byte_1_p1[11], cpu_reg_byte_242_p2[1], S, driverinvsel_1_out, cpu_reg_byte_1_p5, driverinvsel_2_out, Reset
  // CPU_REG_BYTE cpu_reg_byte_238: pin names not known; wires that end beside it: cpu_reg_byte_1_p1[12], cpu_reg_byte_242_p2[1], S, driverinvsel_1_out, cpu_reg_byte_1_p5, driverinvsel_2_out, Reset
  // CPU_REG_BYTE cpu_reg_byte_239: pin names not known; wires that end beside it: cpu_reg_byte_1_p1[13], cpu_reg_byte_242_p2[1], S, driverinvsel_1_out, cpu_reg_byte_1_p5, driverinvsel_2_out, Reset
  // CPU_REG_BYTE cpu_reg_byte_240: pin names not known; wires that end beside it: cpu_reg_byte_1_p1[14], cpu_reg_byte_242_p2[1], S, driverinvsel_1_out, cpu_reg_byte_1_p5, driverinvsel_2_out, Reset
  // CPU_REG_BYTE cpu_reg_byte_241: pin names not known; wires that end beside it: cpu_reg_byte_1_p1[15], cpu_reg_byte_242_p2[1], S, driverinvsel_1_out, cpu_reg_byte_1_p5, driverinvsel_2_out, Reset
  // CPU_REG_BYTE cpu_reg_byte_242: pin names not known; wires that end beside it: cpu_reg_byte_1_p1[0], cpu_reg_byte_242_p2[0], S, driverinvsel_1_out, cpu_reg_byte_1_p5, driverinvsel_2_out, Reset
  // CPU_REG_BYTE cpu_reg_byte_243: pin names not known; wires that end beside it: cpu_reg_byte_1_p1[1], cpu_reg_byte_242_p2[0], S, driverinvsel_1_out, cpu_reg_byte_1_p5, driverinvsel_2_out, Reset
  // CPU_REG_BYTE cpu_reg_byte_244: pin names not known; wires that end beside it: cpu_reg_byte_1_p1[2], cpu_reg_byte_242_p2[0], S, driverinvsel_1_out, cpu_reg_byte_1_p5, driverinvsel_2_out, Reset
  // CPU_REG_BYTE cpu_reg_byte_245: pin names not known; wires that end beside it: cpu_reg_byte_1_p1[3], cpu_reg_byte_242_p2[0], S, driverinvsel_1_out, cpu_reg_byte_1_p5, driverinvsel_2_out, Reset
  // CPU_REG_BYTE cpu_reg_byte_246: pin names not known; wires that end beside it: cpu_reg_byte_1_p1[4], cpu_reg_byte_242_p2[0], S, driverinvsel_1_out, cpu_reg_byte_1_p5, driverinvsel_2_out, Reset
  // CPU_REG_BYTE cpu_reg_byte_247: pin names not known; wires that end beside it: cpu_reg_byte_1_p1[5], cpu_reg_byte_242_p2[0], S, driverinvsel_1_out, cpu_reg_byte_1_p5, driverinvsel_2_out, Reset
  // CPU_REG_BYTE cpu_reg_byte_248: pin names not known; wires that end beside it: cpu_reg_byte_1_p1[6], cpu_reg_byte_242_p2[0], S, driverinvsel_1_out, cpu_reg_byte_1_p5, driverinvsel_2_out, Reset
  // CPU_REG_BYTE cpu_reg_byte_249: pin names not known; wires that end beside it: cpu_reg_byte_1_p1[7], cpu_reg_byte_242_p2[0], S, driverinvsel_1_out, cpu_reg_byte_1_p5, driverinvsel_2_out, Reset
  // CPU_REG_BYTE cpu_reg_byte_250: pin names not known; wires that end beside it: cpu_reg_byte_1_p1[8], cpu_reg_byte_242_p2[0], S, driverinvsel_1_out, cpu_reg_byte_1_p5, driverinvsel_2_out, Reset
  // CPU_REG_BYTE cpu_reg_byte_251: pin names not known; wires that end beside it: cpu_reg_byte_1_p1[9], cpu_reg_byte_242_p2[0], S, driverinvsel_1_out, cpu_reg_byte_1_p5, driverinvsel_2_out, Reset
  // CPU_REG_BYTE cpu_reg_byte_252: pin names not known; wires that end beside it: cpu_reg_byte_1_p1[10], cpu_reg_byte_242_p2[0], S, driverinvsel_1_out, cpu_reg_byte_1_p5, driverinvsel_2_out, Reset
  // CPU_REG_BYTE cpu_reg_byte_253: pin names not known; wires that end beside it: cpu_reg_byte_1_p1[11], cpu_reg_byte_242_p2[0], S, driverinvsel_1_out, cpu_reg_byte_1_p5, driverinvsel_2_out, Reset
  // CPU_REG_BYTE cpu_reg_byte_254: pin names not known; wires that end beside it: cpu_reg_byte_1_p1[12], cpu_reg_byte_242_p2[0], S, driverinvsel_1_out, cpu_reg_byte_1_p5, driverinvsel_2_out, Reset
  // CPU_REG_BYTE cpu_reg_byte_255: pin names not known; wires that end beside it: cpu_reg_byte_1_p1[13], cpu_reg_byte_242_p2[0], S, driverinvsel_1_out, cpu_reg_byte_1_p5, driverinvsel_2_out, Reset
  // CPU_REG_BYTE cpu_reg_byte_256: pin names not known; wires that end beside it: cpu_reg_byte_1_p1[14], cpu_reg_byte_242_p2[0], S, driverinvsel_1_out, cpu_reg_byte_1_p5, driverinvsel_2_out, Reset
  // CPU_REG_BYTE cpu_reg_byte_257: pin names not known; wires that end beside it: cpu_reg_byte_1_p1[15], cpu_reg_byte_242_p2[0], S, driverinvsel_1_out, cpu_reg_byte_1_p5, driverinvsel_2_out, Reset
endmodule
