// Digital circuit CPU_ENABLE.dig as structural Verilog
module CPU_ENABLE (
  input  [7:0] I,
  input  E,
  output [7:0] O
);

  and and_1 (O[0], I[0], E);
  and and_2 (O[1], I[1], E);
  and and_3 (O[2], I[2], E);
  and and_4 (O[3], I[3], E);
  and and_5 (O[4], I[4], E);
  and and_6 (O[5], I[5], E);
  and and_7 (O[6], I[6], E);
  and and_8 (O[7], I[7], E);
endmodule
